// Digital circuit 4116.dig as structural Verilog
// 16k x 1 Dynamic RAM
module _4116 (
  input  A0,
  input  A1,
  input  A2,
  input  A3,
  input  A4,
  input  A5,
  input  A6,
  input  nWE,
  input  nRAS,
  input  nCAS,
  input  DI,
  output DO
);

  wire and_1_out, and_2_out, d_ff_as_1_q, nor_1_out, not_1_out, ramasync_1_q, rs_ff_as_1_q;
  wire [6:0] d_ff_1_q, d_ff_2_q;

  D_FF #(.Bits(7)) d_ff_1 (.D({A6, A5, A4, A3, A2, A1, A0}), .C(~nRAS), .Q(d_ff_1_q));  // open: nQ
  D_FF #(.Bits(7)) d_ff_2 (.D({A6, A5, A4, A3, A2, A1, A0}), .C(~nCAS), .Q(d_ff_2_q));  // open: nQ
  nor nor_1 (nor_1_out, nWE, nRAS, nCAS);
  not not_1 (not_1_out, nCAS);
  RAMAsync #(.AddrBits(14)) ramasync_1 (.A({d_ff_2_q, d_ff_1_q}), .D(DI), .we(nor_1_out), .Q(ramasync_1_q));
  and and_1 (and_1_out, nWE, not_1_out);
  RS_FF_AS rs_ff_as_1 (.S(and_1_out), .R(d_ff_as_1_q), .Q(rs_ff_as_1_q));  // open: nQ
  D_FF_AS d_ff_as_1 (.Set(1'b0), .D(1'b1), .C(~nRAS), .Clr(not_1_out), .Q(d_ff_as_1_q));  // open: nQ
  and and_2 (and_2_out, nWE, rs_ff_as_1_q);
  assign DO = and_2_out ? ramasync_1_q : 1'bz;  // Driver driver_1

  // Notes on the sheet:
  //   nWE: default 1
  //   nRAS: default 1
  //   nCAS: default 1
  //   Latch output until next ~RAS
endmodule
