// Digital circuit 6114.dig as structural Verilog
// 1kx4 Static RAM (Initialized to Random Values)
module _6114 (
  input  R_nW,
  input  nCE,
  input  A0,
  input  A1,
  input  A2,
  input  A3,
  input  A4,
  input  A5,
  input  A6,
  input  A7,
  input  A8,
  input  A9,
  output D0,
  output D1,
  output D2,
  output D3
);

  wire [3:0] ramsingleportselrnd_1_p5;

  // RAMSinglePortSelRnd #(.AddrBits(10), .Bits(4)) ramsingleportselrnd_1: pin names not known; wires that end beside it: nCE, R_nW, {A9, A8, A7, A6, A5, A4, A3, A2, A1, A0}, R_nW, ramsingleportselrnd_1_p5
  BusSplitter #(.Bits(4)) bussplitter_1 (.D(ramsingleportselrnd_1_p5), .OE(R_nW), .D0(D0), .D1(D1), .D2(D2), .D3(D3));
endmodule
