// Digital circuit 6502-DIAG-Clip.dig as structural Verilog
// 6502 with the PET2001 Diagnostic Clip installed
module _6502_DIAG_Clip (
  input  \Φ0 ,
  input  nRESET,
  input  nNMI,
  input  nIRQ,
  input  RDY,
  input  S_O,
  output AB0,
  output AB1,
  output AB2,
  output AB3,
  output AB4,
  output AB5,
  output AB6,
  output AB7,
  output AB8,
  output AB9,
  output AB10,
  output AB11,
  output AB12,
  output AB13,
  output AB14,
  output AB15,
  output \Φ2 ,
  output \Φ1 ,
  output R_W,
  output SYNC,
  output DA0,
  output DA1,
  output DA2,
  output DA3,
  output DA4,
  output DA5,
  output DA6,
  output DA7,
  output N_C
);

  wire and_1_out, d_out, DIAG_SEL, mos6502_1_p8, nr_w;
  wire [7:0] relay_2_p3, rom_1_d;

  and and_1 (and_1_out, AB12, AB15);
  PullUp pullup_1 (.out(S_O));
  and and_2 (DIAG_SEL, ~S_O, and_1_out, R_W);  // And
  // MOS6502 mos6502_1: pin names not known; wires that end beside it: RDY, nRESET, nNMI, nIRQ, \Φ0 , d_out, {AB15, AB14, AB13, AB12, AB11, AB10, AB9, AB8, AB7, AB6, AB5, AB4, AB3, AB2, AB1, AB0}, mos6502_1_p8, SYNC, \Φ1 , \Φ2 
  ROM #(.AddrBits(12), .Bits(8)) rom_1 (
    .A({AB11, AB10, AB9, AB8, AB7, AB6, AB5, AB4, AB3, AB2, AB1, AB0}), .sel(DIAG_SEL), .D(rom_1_d));
  Delay delay_1 (.in(mos6502_1_p8), .out(R_W));
  not not_1 (nr_w, mos6502_1_p8);
  // Relay #(.Bits(8)) relay_1: pin names not known; wires that end beside it: DIAG_SEL, rom_1_d, 1'b0, d_out
  // Relay #(.Bits(8)) relay_2: pin names not known; wires that end beside it: d_out, DIAG_SEL, relay_2_p3, 1'b1
  BusSplitter #(.Bits(8)) bussplitter_1 (
    .D(relay_2_p3), .OE(nr_w), .D0(DA0), .D1(DA1), .D2(DA2), .D3(DA3), .D4(DA4), .D5(DA5), .D6(DA6), .D7(DA7));

  assign N_C = S_O;

  // Other names for the same wires on the sheet: a_out[15:0] = {AB15, AB14, AB13, AB12, AB11, AB10, AB9, AB8, AB7, AB6, AB5, AB4, AB3, AB2, AB1, AB0}

  // Notes on the sheet:
  //   Φ0: Hz: 2147483647
  //   nNMI: default 1
  //   nIRQ: default 1
  //   RDY: default 1
  //   S_O: When set low DIAG ROM active
  //   Set Overflow Flag used to switch
  //   DIAG clip On/Off
  //   S.O. high = normal ops
  //   S.O. low = DIAG ROM active
  //   contents of rom_1 (hex, n*v repeats v):
  //   2048*aa,78,a2,80,9a,d8,a2,0,8a,9d,0,80,a9,20,9d,0,81,9d,0,82,9d
  //   ,0,83,e8,d0,ee,a2,12,bd,84,99,9d,8f,81,ca,d0,f7,ca,8a,5d,0,80
  //   ,f0,4c,a9,ff,9d,0,80,5d,0,80,d0,22,9d,0,80,5d,0,80,d0,1a,a0,a
  //   ,b9,bb,99,99,df,81,88,d0,f7,e8,8a,ce,e1,81,a,90,fa,fe,0,80,e8
  //   ,4c,50,98,a0,b8,29,f,d0,1,88,8c,e0,81,a0,86,8c,e1,81,a0,8,b9,aa
  //   ,99,99,e1,81,88,d0,f7,fe,0,80,4c,71,98,8a,d0,aa,a2,9,bd,a0,99
  //   ,9d,df,81,ca,d0,f7,a9,0,9d,0,1,e8,d0,fa,8a,95,0,e8,d0,fa,ca,8a
  //   ,55,0,f0,47,a9,ff,95,0,55,0,d0,1f,95,0,55,0,d0,19,a0,a,b9,bb,99,99
  //   ,2f,82,88,d0,f7,e8,8a,ce,31,82,a,90,fa,f6,0,e8,4c,ba,98,9a,a2
  //   ,b1,e8,a,90,fc,8e,30,82,a2,9,bd,a9,99,9d,30,82,ca,d0,f7,ba,95
  //   ,0,9d,0,1,91,2,4c,d6,98,8a,d0,b0,a2,9,bd,b2,99,9d,2f,82,ca,d0
  //   ,f7,a0,1,bd,0,1,f0,17,a0,a,b9,bb,99,99,7f,82,88,d0,f7,85,0,8d
  //   ,ff,1,85,aa,8d,55,1,f0,f4,98,9d,0,1,c8,e8,d0,dc,98,5d,0,1,d0,a6
  //   ,c8,e8,d0,f6,a0,8,b9,c5,99,99,7f,82,88,d0,f7,84,2,84,0,a9,1,85
  //   ,3,a9,99,85,1,a2,7,b1,0,91,2,c8,d0,f9,e6,1,e6,3,ca,d0,f2,a2,7
  //   ,c6,1,c6,3,b1,2,d1,0,f0,20,a9,ff,91,2,51,2,d0,bf,91,2,51,2,d0
  //   ,b9,a2,a,bd,96,99,9d,cf,82,ca,d0,f7,85,7f,8d,80,3f,f0,f9,c8,d0
  //   ,d7,ca,d0,d0,a2,a,bd,ce,99,9d,d0,82,ca,10,f7,4c,d9,1,4,9,1,7,e
  //   ,f,13,14,9,3,20,33,32,30,33,35,30,7,81,b8,ad,81,b1,b1,a0,82,81
  //   ,84,14,16,20,12,1,d,20,f,b,89,ad,92,81,8d,a0,82,81,84,1a,2d,10
  //   ,1,7,5,20,f,b,81,b8,ad,81,84,92,a0,82,81,84,13,14,1,3,b,20,f,b
  //   ,12,5,d,f,16,5,20,3,c,9,10,a9,6,85,7,20,63,5,a2,b,bd,cf,82,49
  //   ,80,9d,cf,82,ca,d0,f5,ad,fd,ff,c9,98,f0,e5,c6,7,10,e5,a2,b,a9
  //   ,20,9d,cf,82,ca,d0,fa,84,0,a9,10,85,1,98,91,0,c8,d0,fa,98,d1,0
  //   ,d0,8,c8,d0,f8,e8,6,1,10,ed,a5,1,85,b,c9,40,90,2,46,b,38,e9,8
  //   ,85,a,bd,6c,7,85,10,a9,f,8d,10,e8,a,8d,40,e8,8d,42,e8,a2,ff,8e
  //   ,22,e8,8e,45,e8,a9,3c,8d,13,e8,8d,21,e8,8d,23,e8,8d,11,e8,8e,22
  //   ,e8,a9,c,8d,4c,e8,84,11,84,12,20,9f,6,20,3b,6,f0,12,10,3,4c,86
  //   ,5,a2,9,20,5,6,20,9f,6,20,63,5,f0,f3,a2,9,20,2a,6,20,3b,6,f0,e9
  //   ,a2,9,20,18,6,a2,1a,20,2a,6,a8,85,e,2c,4f,e8,10,5,88,d0,f8,f0
  //   ,1b,a0,0,2c,4f,e8,30,5,88,d0,f8,f0,f,a0,a,2c,4f,e8,30,fb,88,d0
  //   ,fd,2c,4f,e8,30,6,20,5,6,4c,1d,7,ee,ff,ff,2c,4f,e8,30,f2,20,18
  //   ,6,a5,10,20,ff,6,a2,21,20,2a,6,a0,ff,84,6,c8,a6,a,84,0,a9,8,85
  //   ,1,98,18,65,1,45,6,91,0,a5,0,d0,24,c8,d0,f1,e6,1,ca,d0,ec,a6,a
  //   ,c6,1,98,18,65,1,45,6,51,0,f0,5c,a9,ff,91,0,51,0,d0,33,91,0,51
  //   ,0,d0,2d,a2,37,e6,1,a5,1,e8,4a,90,fc,a9,41,20,21,6,8a,c9,3a,90
  //   ,a,38,e9,a,48,a9,31,20,21,6,68,20,21,6,a2,26,20,5,6,85,7f,8d,80
  //   ,3f,30,f9,a2,31,e8,a,90,fc,a9,49,a4,1,c4,b,90,2,a9,4a,20,a8,6
  //   ,a2,22,20,5,6,a9,aa,91,0,4a,91,0,90,f7,c8,d0,97,ca,d0,92,e6,6
  //   ,d0,3,4c,d3,2,a5,10,20,ff,6,a2,21,20,18,6,a2,1e,20,2a,6,84,5,84
  //   ,4,a2,10,a5,5,c9,f0,d0,6,a9,e8,85,5,a2,8,a9,0,18,c6,5,71,4,c8
  //   ,d0,fb,ca,d0,f6,69,0,48,a2,1e,20,e,6,a9,20,20,b0,6,a5,5,4*4a,18
  //   ,69,ca,a2,3d,20,15,7,68,a2,d,20,15,7,a5,5,c9,a0,b0,be,e6,e,20
  //   ,c8,6,20,5a,5,a2,2a,20,2a,6,a9,fd,a0,9,8c,10,e8,cd,12,e8,f0,d
  //   ,20,5,6,a0,a,8c,10,e8,88,10,fa,30,f6,4a,90,2,9,80,88,10,e3,8c
  //   ,10,e8,cc,12,e8,d0,e3,20,18,6,ad,fe,ff,85,0,ad,ff,ff,85,1,a9,0
  //   ,85,9,a4,9,b1,0,c9,6c,d0,15,c8,b1,0,85,2,c8,b1,0,85,3,a0,0,a9
  //   ,68,91,2,c8,a9,6,91,2,e6,9,d0,df,a2,e,20,2a,6,20,3b,6,58,20,d7
  //   ,5,84,f,58,20,7d,5,a2,30,20,2a,6,20,d7,5,98,84,f,8d,44,e8,8d,45
  //   ,e8,20,6f,5,a2,43,20,2a,6,20,d7,5,98,84,f,8d,48,e8,8d,49,e8,20
  //   ,6f,5,a2,4d,20,c4,5,a2,52,20,c4,5,a2,57,20,2a,6,a0,0,98,8d,22
  //   ,e8,4d,20,e8,f0,18,48,20,a,6,68,a2,30,e8,4a,90,fc,8a,20,21,6,20
  //   ,8,6,ee,22,e8,4c,89,4,c8,d0,dc,20,18,6,a2,5f,20,2a,6,78,a2,68
  //   ,2c,20,e8,a0,4,20,fa,5,2c,21,e8,30,8,20,5,6,20,fa,5,d0,fb,a2,6e
  //   ,a0,2,2c,40,e8,50,ef,20,fd,5,2c,40,e8,70,e7,20,fd,5,a2,6b,a0,3c
  //   ,8c,23,e8,2c,40,e8,10,2c,a9,34,8d,23,e8,2c,40,e8,30,22,a2,76,8c
  //   ,11,e8,2c,10,e8,50,1b,8d,11,e8,2c,10,e8,70,13,8c,11,e8,a2,72,8c
  //   ,21,e8,4e,40,e8,b0,15,a0,21,2c,a0,23,2c,a0,11,20,5,6,a9,8,59,0
  //   ,e8,99,0,e8,d0,f6,8d,21,e8,4e,40,e8,b0,e3,a2,79,2c,22,e8,ee,43
  //   ,e8,ce,43,e8,2c,23,e8,30,c,20,5,6,ee,43,e8,ce,43,e8,4c,2b,5,a2
  //   ,5f,20,18,6,a2,5,fe,f3,7,bd,f3,7,c9,3a,90,a,a9,30,9d,f3,7,ca,10
  //   ,ee,30,ea,a2,7c,20,a,6,20,5a,5,4c,2f,2,a2,a,20,63,5,ca,d0,fa,60
  //   ,a9,0,a8,18,69,1,d0,fc,c8,d0,f9,60,86,7,a4,e,b9,4f,7,aa,bd,0,e8
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endmodule
