// Digital circuit 6502-layout-2.dig as structural Verilog
// MOS6502
// VHDL code for 6502 from:
// https://github.com/Steve-Teal/mx65
module _6502_layout_2 (
  input  \Φ0 ,
  input  nRESET,
  input  nNMI,
  input  nIRQ,
  input  RDY,
  output \Φ2 ,
  output \Φ1 ,
  output R_W,
  output SYNC,
  output D0,
  output D1,
  output D2,
  output D3,
  output D4,
  output D5,
  output D6,
  output D7,
  output A15,
  output A14,
  output A13,
  output A12,
  output A11,
  output A10,
  output A9,
  output A8,
  output A7,
  output A6,
  output A5,
  output A4,
  output A3,
  output A2,
  output A1,
  output A0
);

  wire mos6502_1_p8, nr_w;
  wire [7:0] d_out;

  // MOS6502 mos6502_1: pin names not known; wires that end beside it: RDY, nRESET, nNMI, nIRQ, \Φ0 , d_out, {A15, A14, A13, A12, A11, A10, A9, A8, A7, A6, A5, A4, A3, A2, A1, A0}, mos6502_1_p8, SYNC, \Φ1 , \Φ2 
  Delay delay_1 (.in(mos6502_1_p8), .out(R_W));
  not not_1 (nr_w, mos6502_1_p8);
  BusSplitter #(.Bits(8)) bussplitter_1 (
    .D(d_out), .OE(nr_w), .D0(D0), .D1(D1), .D2(D2), .D3(D3), .D4(D4), .D5(D5), .D6(D6), .D7(D7));

  // Other names for the same wires on the sheet: a_out[15:0] = {A15, A14, A13, A12, A11, A10, A9, A8, A7, A6, A5, A4, A3, A2, A1, A0}

  // Notes on the sheet:
  //   Φ0: Hz: 2
  //   nNMI: default 1
  //   nIRQ: default 1
  //   RDY: default 1
endmodule
