// Digital circuit 6522.dig as structural Verilog
// https://github.com/MiSTer-devel/VIC20_MiSTer/blob/master/rtl/via6522.vhd
module _6522 (
  input  D0,
  input  D1,
  input  D2,
  input  D3,
  input  D4,
  input  D5,
  input  D6,
  input  D7,
  input  CS1,
  input  nCS2,
  input  RS0,
  input  RS1,
  input  RS2,
  input  RS3,
  input  R_W,
  input  nRESET,
  input  CA1,
  input  \Φ2 ,
  input  CB1,
  output nIRQ,
  output CA2,
  output CB2,
  output PA0,
  output PA1,
  output PA2,
  output PA3,
  output PA4,
  output PA5,
  output PA6,
  output PA7,
  output PB0,
  output PB1,
  output PB2,
  output PB3,
  output PB4,
  output PB5,
  output PB6,
  output PB7
);

  wire and_1_out, and_2_out, mos6522_1_p12;
  wire [7:0] bussplitter_1_d, porta_dir, porta_out, portb_dir, portb_out;

  BusSplitter #(.Bits(8)) bussplitter_1 (
    .D(bussplitter_1_d), .OE(and_2_out), .D0(D0), .D1(D1), .D2(D2), .D3(D3), .D4(D4), .D5(D5), .D6(D6),
    .D7(D7));
  and and_1 (and_1_out, CS1, ~nCS2);  // And
  and and_2 (and_2_out, R_W, and_1_out);
  // MOS6522 mos6522_1: pin names not known; wires that end beside it: CS1, nCS2, {RS3, RS2, RS1, RS0}, R_W, nRESET, \Φ2 , CA1, CB1, {PA7, PA6, PA5, PA4, PA3, PA2, PA1, PA0}, {PB7, PB6, PB5, PB4, PB3, PB2, PB1, PB0}, bussplitter_1_d, mos6522_1_p12, CA2, porta_out, porta_dir, portb_out, portb_dir, CB2
  assign nIRQ = ~mos6522_1_p12 ? 1'b0 : 1'bz;  // DriverInvSel driverinvsel_1
  assign PA6 = porta_dir[6] ? porta_out[6] : 1'bz;  // Driver driver_1
  assign PA7 = porta_dir[7] ? porta_out[7] : 1'bz;  // Driver driver_2
  assign PB6 = portb_dir[6] ? portb_out[6] : 1'bz;  // Driver driver_3
  assign PB7 = portb_dir[7] ? portb_out[7] : 1'bz;  // Driver driver_4
  assign PA2 = porta_dir[2] ? porta_out[2] : 1'bz;  // Driver driver_5
  assign PA3 = porta_dir[3] ? porta_out[3] : 1'bz;  // Driver driver_6
  assign PA4 = porta_dir[4] ? porta_out[4] : 1'bz;  // Driver driver_7
  assign PA5 = porta_dir[5] ? porta_out[5] : 1'bz;  // Driver driver_8
  assign PB2 = portb_dir[2] ? portb_out[2] : 1'bz;  // Driver driver_9
  assign PB3 = portb_dir[3] ? portb_out[3] : 1'bz;  // Driver driver_10
  assign PB4 = portb_dir[4] ? portb_out[4] : 1'bz;  // Driver driver_11
  assign PB5 = portb_dir[5] ? portb_out[5] : 1'bz;  // Driver driver_12
  PullUp pullup_1 (.out(CA1));
  PullUp pullup_2 (.out(CA2));
  assign PA0 = porta_dir[0] ? porta_out[0] : 1'bz;  // Driver driver_13
  assign PA1 = porta_dir[1] ? porta_out[1] : 1'bz;  // Driver driver_14
  assign PB0 = portb_dir[0] ? portb_out[0] : 1'bz;  // Driver driver_15
  assign PB1 = portb_dir[1] ? portb_out[1] : 1'bz;  // Driver driver_16
  PullUp pullup_3 (.out(CB1));
  PullUp pullup_4 (.out(CB2));
  PullUp #(.Bits(8)) pullup_5 (.out({PA7, PA6, PA5, PA4, PA3, PA2, PA1, PA0}));
  PullUp #(.Bits(8)) pullup_6 (.out({PB7, PB6, PB5, PB4, PB3, PB2, PB1, PB0}));

  // Other names for the same wires on the sheet: porta_in[7:0] = {PA7, PA6, PA5, PA4, PA3, PA2, PA1, PA0};
  //   portb_in[7:0] = {PB7, PB6, PB5, PB4, PB3, PB2, PB1, PB0}; addr[3:0] = {RS3, RS2, RS1, RS0}; rw = R_W

  // Notes on the sheet:
  //   R_W: default 1
  //   PA0: Bidirectional Port
  //   PA1: Bidirectional Port
  //   PA2: Bidirectional Port
  //   PA3: Bidirectional Port
  //   PA4: Bidirectional Port
  //   PA5: Bidirectional Port
  //   PA6: Bidirectional Port
  //   PA7: Bidirectional Port
  //   PB0: Bidirectional Port
  //   PB1: Bidirectional Port
  //   PB2: Bidirectional Port
  //   PB3: Bidirectional Port
  //   PB4: Bidirectional Port
  //   PB5: Bidirectional Port
  //   PB6: Bidirectional Port
  //   PB7: Bidirectional Port
endmodule
