// Digital circuit 6540 Character ROM.dig as structural Verilog
// 2k ROM loaded with the PET Character set
module _6540_Character_ROM (
  input  A0,
  input  A1,
  input  A2,
  input  CS1,
  input  CS2,
  input  nCS3,
  input  nCS4,
  input  nCS5,
  input  \Φ2 ,
  input  A3,
  input  A4,
  input  A5,
  input  A6,
  input  A7,
  input  A8,
  input  A9,
  input  A10,
  output D0,
  output D1,
  output D2,
  output D3,
  output D4,
  output D5,
  output D6,
  output D7
);

  wire and_1_out, nor_1_out;
  wire [10:0] d_ff_1_q;

  D_FF #(.Bits(11)) d_ff_1 (.D({A10, A9, A8, A7, A6, A5, A4, A3, A2, A1, A0}), .C(\Φ2 ), .Q(d_ff_1_q));  // open: nQ
  and and_1 (and_1_out, CS1, CS2, nor_1_out, \Φ2 );
  ROM #(.AddrBits(11), .Bits(8)) Character_ROM (.A(d_ff_1_q), .sel(and_1_out), .D({D7, D6, D5, D4, D3, D2, D1, D0}));
  nor nor_1 (nor_1_out, nCS3, nCS4, nCS5);

  // Notes on the sheet:
  //   contents of Character_ROM (hex, n*v repeats v):
  //   1c,22,4a,56,4c,20,1e,0,18,24,42,7e,42,42,42,0,7c,22,22,3c,22,22
  //   ,7c,0,1c,22,40,40,40,22,1c,0,78,24,22,22,22,24,78,0,7e,40,40,78
  //   ,40,40,7e,0,7e,40,40,78,40,40,40,0,1c,22,40,4e,42,22,1c,0,42,42,42
  //   ,7e,42,42,42,0,1c,5*8,1c,0,e,4*4,44,38,0,42,44,48,70,48,44,42
  //   ,0,6*40,7e,0,42,66,5a,5a,42,42,42,0,42,62,52,4a,46,42,42,0,18
  //   ,24,42,42,42,24,18,0,7c,42,42,7c,40,40,40,0,18,24,42,42,4a,24
  //   ,1a,0,7c,42,42,7c,48,44,42,0,3c,42,40,3c,2,42,3c,0,3e,6*8,0,6*42
  //   ,3c,0,42,42,42,24,24,18,18,0,42,42,42,5a,5a,66,42,0,42,42,24,18
  //   ,24,42,42,0,22,22,22,1c,8,8,8,0,7e,2,4,18,20,40,7e,0,3c,5*20,3c
  //   ,0,0,40,20,10,8,4,2,0,3c,5*4,3c,0,0,8,1c,2a,4*8,0,0,10,20,7f,20
  //   ,10,9*0,4*8,0,0,8,0,24,24,24,5*0,24,24,7e,24,7e,24,24,0,8,1e,28
  //   ,1c,a,3c,8,0,0,62,64,8,10,26,46,0,30,48,48,30,4a,44,3a,0,4,8,10
  //   ,5*0,4,8,10,10,10,8,4,0,20,10,8,8,8,10,20,0,8,2a,1c,3e,1c,2a,8
  //   ,0,0,8,8,3e,8,8,7*0,8,8,10,0,0,0,7e,9*0,18,18,0,0,2,4,8,10,20
  //   ,40,0,3c,42,46,5a,62,42,3c,0,8,18,28,8,8,8,3e,0,3c,42,2,c,30,40
  //   ,7e,0,3c,42,2,1c,2,42,3c,0,4,c,14,24,7e,4,4,0,7e,40,78,4,2,44
  //   ,38,0,1c,20,40,7c,42,42,3c,0,7e,42,4,8,10,10,10,0,3c,42,42,3c
  //   ,42,42,3c,0,3c,42,42,3e,2,4,38,0,0,0,8,0,0,8,4*0,8,0,0,8,8,10
  //   ,e,18,30,60,30,18,e,0,0,0,7e,0,7e,0,0,0,70,18,c,6,c,18,70,0,3c
  //   ,42,2,c,10,0,10,5*0,ff,0,0,0,8,1c,3e,7f,7f,1c,3e,0,8*10,0,0,0
  //   ,ff,6*0,ff,6*0,ff,11*0,ff,0,0,8*20,8*4,4*0,e0,10,5*8,4,3,0,0,0
  //   ,8,8,8,10,e0,0,0,0,7*80,ff,80,40,20,10,8,4,2,1,1,2,4,8,10,20,40
  //   ,80,ff,7*80,ff,7*1,0,3c,4*7e,3c,7*0,ff,0,36,7f,7f,7f,3e,1c,8,0
  //   ,8*40,4*0,3,4,8,8,81,42,24,18,18,24,42,81,0,3c,4*42,3c,0,8,1c
  //   ,2a,77,2a,8,8,0,8*2,8,1c,3e,7f,3e,1c,8,0,4*8,ff,8,8,8,a0,50,a0
  //   ,50,a0,50,a0,50,8*8,0,0,1,3e,54,14,14,0,ff,7f,3f,1f,f,7,3,1,8*0
  //   ,8*f0,4*0,5*ff,14*0,ff,8*80,aa,55,aa,55,aa,55,aa,55,8*1,4*0,aa
  //   ,55,aa,55,ff,fe,fc,f8,f0,e0,c0,80,8*3,4*8,f,8,8,8,4*0,4*f,4*8
  //   ,f,7*0,f8,8,8,8,6*0,ff,ff,4*0,f,7*8,ff,7*0,ff,7*8,f8,8,8,8,8*c0
  //   ,8*e0,8*7,ff,ff,6*0,ff,ff,ff,10*0,ff,ff,ff,7*1,ff,4*0,4*f0,4*f
  //   ,4*0,4*8,f8,0,0,0,4*f0,4*0,4*f0,4*f,1c,22,4a,56,4c,20,1e,0,0,0
  //   ,38,4,3c,44,3a,0,40,40,5c,62,42,62,5c,0,0,0,3c,42,40,42,3c,0,2,2
  //   ,3a,46,42,46,3a,0,0,0,3c,42,7e,40,3c,0,c,12,10,7c,10,10,10,0,0,0
  //   ,3a,46,46,3a,2,3c,40,40,5c,62,42,42,42,0,8,0,18,8,8,8,1c,0,4,0
  //   ,c,4,4,4,44,38,40,40,44,48,50,68,44,0,18,5*8,1c,0,0,0,76,4*49
  //   ,0,0,0,5c,62,42,42,42,0,0,0,3c,42,42,42,3c,0,0,0,5c,62,62,5c,40,40
  //   ,0,0,3a,46,46,3a,2,2,0,0,5c,62,40,40,40,0,0,0,3e,40,3c,2,7c,0
  //   ,10,10,7c,10,10,12,c,0,0,0,42,42,42,46,3a,0,0,0,42,42,42,24,18
  //   ,0,0,0,41,49,49,49,36,0,0,0,42,24,18,24,42,0,0,0,42,42,46,3a,2
  //   ,3c,0,0,7e,4,18,20,7e,0,3c,5*20,3c,0,0,40,20,10,8,4,2,0,3c,5*4
  //   ,3c,0,0,8,1c,2a,4*8,0,0,10,20,7f,20,10,9*0,4*8,0,0,8,0,24,24,24
  //   ,5*0,24,24,7e,24,7e,24,24,0,8,1e,28,1c,a,3c,8,0,0,62,64,8,10,26
  //   ,46,0,30,48,48,30,4a,44,3a,0,4,8,10,5*0,4,8,10,10,10,8,4,0,20
  //   ,10,8,8,8,10,20,0,8,2a,1c,3e,1c,2a,8,0,0,8,8,3e,8,8,7*0,8,8,10
  //   ,0,0,0,7e,9*0,18,18,0,0,2,4,8,10,20,40,0,3c,42,46,5a,62,42,3c
  //   ,0,8,18,28,8,8,8,3e,0,3c,42,2,c,30,40,7e,0,3c,42,2,1c,2,42,3c
  //   ,0,4,c,14,24,7e,4,4,0,7e,40,78,4,2,44,38,0,1c,20,40,7c,42,42,3c
  //   ,0,7e,42,4,8,10,10,10,0,3c,42,42,3c,42,42,3c,0,3c,42,42,3e,2,4
  //   ,38,0,0,0,8,0,0,8,4*0,8,0,0,8,8,10,e,18,30,60,30,18,e,0,0,0,7e
  //   ,0,7e,0,0,0,70,18,c,6,c,18,70,0,3c,42,2,c,10,0,10,5*0,ff,0,0,0
  //   ,18,24,42,7e,42,42,42,0,7c,22,22,3c,22,22,7c,0,1c,22,40,40,40
  //   ,22,1c,0,78,24,22,22,22,24,78,0,7e,40,40,78,40,40,7e,0,7e,40,40
  //   ,78,40,40,40,0,1c,22,40,4e,42,22,1c,0,42,42,42,7e,42,42,42,0,1c
  //   ,5*8,1c,0,e,4*4,44,38,0,42,44,48,70,48,44,42,0,6*40,7e,0,42,66
  //   ,5a,5a,42,42,42,0,42,62,52,4a,46,42,42,0,18,24,42,42,42,24,18
  //   ,0,7c,42,42,7c,40,40,40,0,18,24,42,42,4a,24,1a,0,7c,42,42,7c,48
  //   ,44,42,0,3c,42,40,3c,2,42,3c,0,3e,6*8,0,6*42,3c,0,42,42,42,24,24
  //   ,18,18,0,42,42,42,5a,5a,66,42,0,42,42,24,18,24,42,42,0,22,22,22
  //   ,1c,8,8,8,0,7e,2,4,18,20,40,7e,0,4*8,ff,8,8,8,a0,50,a0,50,a0,50
  //   ,a0,50,8*8,cc,cc,33,33,cc,cc,33,33,cc,66,33,99,cc,66,33,99,8*0
  //   ,8*f0,4*0,5*ff,14*0,ff,8*80,aa,55,aa,55,aa,55,aa,55,8*1,4*0,aa
  //   ,55,aa,55,99,33,66,cc,99,33,66,cc,8*3,4*8,f,8,8,8,4*0,4*f,4*8
  //   ,f,7*0,f8,8,8,8,6*0,ff,ff,4*0,f,7*8,ff,7*0,ff,7*8,f8,8,8,8,8*c0
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endmodule
