// Digital circuit 6550-layout-3.dig as structural Verilog
// 1kx4 Static RAM (Initialized to Random Values)
module _6550_layout_3 (
  input  R_nW,
  input  CS1,
  input  CS2,
  input  nCS3,
  input  nCS4,
  input  \Φ2 ,
  input  [9:0] A0_A9,
  output D0,
  output D1,
  output D2,
  output D3
);

  wire _1Kx4_RAM_p2, nor_1_out;
  wire [3:0] bussplitter_1_d;
  wire [9:0] _1Kx4_RAM_p1;

  BusSplitter #(.Bits(4)) bussplitter_1 (.D(bussplitter_1_d), .OE(R_nW), .D0(D0), .D1(D1), .D2(D2), .D3(D3));
  // RAMSinglePortSelRnd #(.AddrBits(10), .Bits(4)) _1Kx4_RAM: pin names not known; wires that end beside it: _1Kx4_RAM_p1, _1Kx4_RAM_p2, bussplitter_1_d, R_nW, R_nW
  D_FF #(.Bits(10)) d_ff_1 (.D(A0_A9), .C(\Φ2 ), .Q(_1Kx4_RAM_p1));  // open: nQ
  and and_1 (_1Kx4_RAM_p2, \Φ2 , nor_1_out, CS2, CS1);
  nor nor_1 (nor_1_out, nCS4, nCS3);
endmodule
