// Digital circuit 74100.dig as structural Verilog
// 8-Bit Bistable Latches
module _74100 (
  input  _1,
  input  C1,
  input  C2,
  input  _2,
  input  _3,
  input  _4,
  input  _5,
  input  _6,
  input  _7,
  input  _8,
  output Q1,
  output Q2,
  output Q3,
  output Q4,
  output Q5,
  output Q6,
  output Q7,
  output Q8
);

  wire and_1_out, and_2_out, and_3_out, and_4_out, and_5_out, and_6_out, and_7_out, and_8_out, and_9_out,
       and_10_out, and_11_out, and_12_out, and_13_out, and_14_out, and_15_out, and_16_out, nor_1_out,
       nor_2_out, nor_3_out, nor_4_out, nor_5_out, nor_6_out, nor_7_out, nor_8_out, not_1_out, not_2_out,
       not_3_out, not_4_out, not_5_out, not_6_out, not_7_out, not_8_out;

  nor nor_1 (nor_1_out, Q1, and_1_out);
  nor nor_2 (nor_2_out, Q2, and_2_out);
  nor nor_3 (nor_3_out, Q3, and_3_out);
  nor nor_4 (nor_4_out, Q4, and_4_out);
  nor nor_5 (nor_5_out, Q5, and_5_out);
  nor nor_6 (nor_6_out, Q6, and_6_out);
  nor nor_7 (nor_7_out, Q7, and_7_out);
  nor nor_8 (nor_8_out, Q8, and_8_out);
  and and_1 (and_1_out, C1, _1);
  and and_2 (and_2_out, C1, _2);
  and and_3 (and_3_out, C1, _3);
  and and_4 (and_4_out, C1, _4);
  and and_5 (and_5_out, C2, _5);
  and and_6 (and_6_out, C2, _6);
  and and_7 (and_7_out, C2, _7);
  and and_8 (and_8_out, C2, _8);
  not not_1 (not_1_out, _1);
  not not_2 (not_2_out, _2);
  not not_3 (not_3_out, _3);
  not not_4 (not_4_out, _4);
  not not_5 (not_5_out, _5);
  not not_6 (not_6_out, _6);
  not not_7 (not_7_out, _7);
  not not_8 (not_8_out, _8);
  and and_9 (and_9_out, not_1_out, C1);
  and and_10 (and_10_out, not_2_out, C1);
  and and_11 (and_11_out, not_3_out, C1);
  and and_12 (and_12_out, not_4_out, C1);
  and and_13 (and_13_out, not_5_out, C2);
  and and_14 (and_14_out, not_6_out, C2);
  and and_15 (and_15_out, not_7_out, C2);
  and and_16 (and_16_out, not_8_out, C2);
  nor nor_9 (Q1, and_9_out, nor_1_out);
  nor nor_10 (Q2, and_10_out, nor_2_out);
  nor nor_11 (Q3, and_11_out, nor_3_out);
  nor nor_12 (Q4, and_12_out, nor_4_out);
  nor nor_13 (Q5, and_13_out, nor_5_out);
  nor nor_14 (Q6, and_14_out, nor_6_out);
  nor nor_15 (Q7, and_15_out, nor_7_out);
  nor nor_16 (Q8, and_16_out, nor_8_out);
endmodule
