// Digital circuit 74177-layout-2.dig as structural Verilog
// 4-bit synchronous counter, async clear
module _74177_layout_2 (
  input  CLK2,
  input  CLK1,
  input  nLD,
  input  nCLR,
  input  A,
  input  B,
  input  C,
  input  D,
  output QA,
  output QB,
  output QC,
  output QD
);

  wire delay_1_out, delay_2_out, delay_3_out, delay_4_out, nand_1_out, nand_2_out, nand_3_out, nand_4_out,
       nand_5_out, nand_6_out, nand_7_out, nand_8_out, or_1_out;

  or or_1 (or_1_out, ~nLD, ~nCLR);  // Or
  Delay delay_1 (.in(nCLR), .out(delay_1_out));
  Delay delay_2 (.in(nCLR), .out(delay_2_out));
  Delay delay_3 (.in(nCLR), .out(delay_3_out));
  Delay delay_4 (.in(nCLR), .out(delay_4_out));
  nand nand_1 (nand_1_out, A, or_1_out, delay_1_out);
  nand nand_2 (nand_2_out, B, or_1_out, delay_2_out);
  nand nand_3 (nand_3_out, C, or_1_out, delay_3_out);
  nand nand_4 (nand_4_out, D, or_1_out, delay_4_out);
  nand nand_5 (nand_5_out, nand_1_out, or_1_out);
  nand nand_6 (nand_6_out, nand_2_out, or_1_out);
  nand nand_7 (nand_7_out, nand_3_out, or_1_out);
  nand nand_8 (nand_8_out, nand_4_out, or_1_out);
  JK_FF_AS jk_ff_as_1 (.Set(~nand_1_out), .J(1'b1), .C(~CLK1), .K(1'b1), .Clr(~nand_5_out), .Q(QA));  // open: nQ
  JK_FF_AS jk_ff_as_2 (.Set(~nand_2_out), .J(1'b1), .C(~CLK2), .K(1'b1), .Clr(~nand_6_out), .Q(QB));  // open: nQ
  JK_FF_AS jk_ff_as_3 (.Set(~nand_3_out), .J(1'b1), .C(~QB), .K(1'b1), .Clr(~nand_7_out), .Q(QC));  // open: nQ
  JK_FF_AS jk_ff_as_4 (.Set(~nand_4_out), .J(1'b1), .C(~QC), .K(1'b1), .Clr(~nand_8_out), .Q(QD));  // open: nQ
endmodule
