// Digital circuit 74191simplified.dig as structural Verilog
// 4 Bit Counter.
// Simplified to remove LOAD function (not needed in the PET2001 Circuit)
module _74191simplified (
  input  nENG,
  input  DN_UP,
  input  CLK,
  output QA,
  output QB,
  output QC,
  output QD,
  output MAX_MIN,
  output nRCO
);

  wire not_1_out, not_2_out;

  not not_1 (not_1_out, nENG);
  CounterPreset #(.maxValue(16), .Bits(4)) counterpreset_1 (
    .en(not_1_out), .C(CLK), .dir(DN_UP), .in(4'b0000), .ld(1'b0), .clr(1'b0), .out({QD, QC, QB, QA}),
    .ovf(MAX_MIN));
  not not_2 (not_2_out, CLK);
  nand nand_1 (nRCO, MAX_MIN, not_1_out, not_2_out);

  // Notes on the sheet:
  //   This Circuit is simplified from the original in
  //   that the LOAD is synchronous, i.e. it 
  //   requires one clock cycle to take effect.
  //   The original is asynchronous, i.e. LOAD takes effect
  //   immediatley.
  //   The load is often not used and this circuit is 3x 
  //   faster than the original.
endmodule
