// Digital circuit 74LS107-CLR-TOP.dig as structural Verilog
module _74LS107_CLR_TOP (
  input  J,
  input  nCLK,
  input  K,
  input  nCLR,
  output Q,
  output nQ
);

  JK_FF_AS jk_ff_as_1 (.Set(1'b0), .J(J), .C(~nCLK), .K(K), .Clr(~nCLR), .Q(Q), .nQ(nQ));

  // Notes on the sheet:
  //   J: default 1
  //   K: default 1
endmodule
