// Digital circuit 74LS145.dig as structural Verilog
// BCD to Decimal Decoder
module _74LS145 (
  input  A,
  input  B,
  input  C,
  input  D,
  output _0,
  output _1,
  output _2,
  output _3,
  output _4,
  output _5,
  output _6,
  output _7,
  output _8,
  output _9
);

  LookUpTable #(.Bits(10)) lookuptable_1 (
    .in0(A), .in1(B), .in2(C), .in3(D), .out({_9, _8, _7, _6, _5, _4, _3, _2, _1, _0}));

  // Notes on the sheet:
  //   contents of lookuptable_1 (hex, n*v repeats v):
  //   1,2,4,8,10,20,40,80,100,200
endmodule
