// Digital circuit 74LS157.dig as structural Verilog
// quad 2-line to 1-line data selectors/multiplexers
module _74LS157 (
  input  _1A,
  input  _1B,
  input  _2A,
  input  _2B,
  input  _3A,
  input  _3B,
  input  _4A,
  input  _4B,
  input  S,
  input  G,
  output Y1,
  output Y2,
  output Y3,
  output Y4
);

  wire [3:0] multiplexer_1_out;

  Multiplexer #(.Bits(4)) multiplexer_1 (
    .sel(S), .in_0({_4A, _3A, _2A, _1A}), .in_1({_4B, _3B, _2B, _1B}), .out(multiplexer_1_out));
  Multiplexer #(.Bits(4)) multiplexer_2 (.sel(G), .in_0(multiplexer_1_out), .in_1(4'b0000), .out({Y4, Y3, Y2, Y1}));

  // Notes on the sheet:
  //   S: select
  //   G: strobe
endmodule
