// Digital circuit 74LS164.dig as structural Verilog
// 8-bit parallel-out serial shift register, asynchronous clear
module _74LS164 (
  input  CK,
  input  A,
  input  B,
  input  nCL,
  output QA,
  output QB,
  output QC,
  output QD,
  output QE,
  output QF,
  output QG,
  output QH
);

  wire and_1_out, not_1_out;

  and and_1 (and_1_out, A, B);
  not not_1 (not_1_out, nCL);
  D_FF_AS d_ff_as_1 (.Set(1'b0), .D(and_1_out), .C(CK), .Clr(not_1_out), .Q(QA));  // open: nQ
  D_FF_AS d_ff_as_2 (.Set(1'b0), .D(QA), .C(CK), .Clr(not_1_out), .Q(QB));  // open: nQ
  D_FF_AS d_ff_as_3 (.Set(1'b0), .D(QB), .C(CK), .Clr(not_1_out), .Q(QC));  // open: nQ
  D_FF_AS d_ff_as_4 (.Set(1'b0), .D(QC), .C(CK), .Clr(not_1_out), .Q(QD));  // open: nQ
  D_FF_AS d_ff_as_5 (.Set(1'b0), .D(QD), .C(CK), .Clr(not_1_out), .Q(QE));  // open: nQ
  D_FF_AS d_ff_as_6 (.Set(1'b0), .D(QE), .C(CK), .Clr(not_1_out), .Q(QF));  // open: nQ
  D_FF_AS d_ff_as_7 (.Set(1'b0), .D(QF), .C(CK), .Clr(not_1_out), .Q(QG));  // open: nQ
  D_FF_AS d_ff_as_8 (.Set(1'b0), .D(QG), .C(CK), .Clr(not_1_out), .Q(QH));  // open: nQ

  // Notes on the sheet:
  //   CK: pin 8
  //   A: pin 1
  //   B: pin 2
  //   nCL: pin 9
  //   QA: pin 3
  //   QB: pin 4
  //   QC: pin 5
  //   QD: pin 6
  //   QE: pin 10
  //   QF: pin 11
  //   QG: pin 12
  //   QH: pin 13
endmodule
