// Digital circuit 74LS165-layout-2.dig as structural Verilog
// parallel-load 8-bit shift register
module _74LS165_layout_2 (
  input  SH_nLD,
  input  CLK,
  input  CLKINH,
  input  SER,
  input  A,
  input  B,
  input  C,
  input  D,
  input  E,
  input  F,
  input  G,
  input  H,
  output QH,
  output nQH
);

  wire and_1_out, and_2_out, and_3_out, and_4_out, and_5_out, and_6_out, and_7_out, and_8_out, d_ff_as_1_q,
       d_ff_as_2_q, d_ff_as_3_q, d_ff_as_4_q, d_ff_as_5_q, d_ff_as_6_q, d_ff_as_7_q, nand_1_out, nand_2_out,
       nand_3_out, nand_4_out, nand_5_out, nand_6_out, nand_7_out, nand_8_out, nor_1_out, not_1_out;

  nor nor_1 (nor_1_out, CLKINH, CLK);
  not not_1 (not_1_out, SH_nLD);
  nand nand_1 (nand_1_out, not_1_out, A);
  D_FF_AS d_ff_as_1 (.Set(~nand_1_out), .D(SER), .C(nor_1_out), .Clr(and_1_out), .Q(d_ff_as_1_q));  // open: nQ
  and and_1 (and_1_out, nand_1_out, not_1_out);
  nand nand_2 (nand_2_out, not_1_out, B);
  D_FF_AS d_ff_as_2 (.Set(~nand_2_out), .D(d_ff_as_1_q), .C(nor_1_out), .Clr(and_2_out), .Q(d_ff_as_2_q));  // open: nQ
  and and_2 (and_2_out, nand_2_out, not_1_out);
  nand nand_3 (nand_3_out, not_1_out, C);
  D_FF_AS d_ff_as_3 (.Set(~nand_3_out), .D(d_ff_as_2_q), .C(nor_1_out), .Clr(and_3_out), .Q(d_ff_as_3_q));  // open: nQ
  and and_3 (and_3_out, nand_3_out, not_1_out);
  nand nand_4 (nand_4_out, not_1_out, D);
  D_FF_AS d_ff_as_4 (.Set(~nand_4_out), .D(d_ff_as_3_q), .C(nor_1_out), .Clr(and_4_out), .Q(d_ff_as_4_q));  // open: nQ
  and and_4 (and_4_out, nand_4_out, not_1_out);
  nand nand_5 (nand_5_out, not_1_out, E);
  D_FF_AS d_ff_as_5 (.Set(~nand_5_out), .D(d_ff_as_4_q), .C(nor_1_out), .Clr(and_5_out), .Q(d_ff_as_5_q));  // open: nQ
  and and_5 (and_5_out, nand_5_out, not_1_out);
  nand nand_6 (nand_6_out, not_1_out, F);
  D_FF_AS d_ff_as_6 (.Set(~nand_6_out), .D(d_ff_as_5_q), .C(nor_1_out), .Clr(and_6_out), .Q(d_ff_as_6_q));  // open: nQ
  and and_6 (and_6_out, nand_6_out, not_1_out);
  nand nand_7 (nand_7_out, not_1_out, G);
  D_FF_AS d_ff_as_7 (.Set(~nand_7_out), .D(d_ff_as_6_q), .C(nor_1_out), .Clr(and_7_out), .Q(d_ff_as_7_q));  // open: nQ
  and and_7 (and_7_out, nand_7_out, not_1_out);
  nand nand_8 (nand_8_out, not_1_out, H);
  D_FF_AS d_ff_as_8 (.Set(~nand_8_out), .D(d_ff_as_7_q), .C(nor_1_out), .Clr(and_8_out), .Q(QH), .nQ(nQH));
  and and_8 (and_8_out, nand_8_out, not_1_out);

  // Notes on the sheet:
  //   SH_nLD: pin 1
  //   CLK: pin 2
  //   CLKINH: pin 15
  //   SER: pin 10
  //   QH: pin 9
  //   nQH: pin 7
  //   A: pin 11
  //   B: pin 12
  //   C: pin 13
  //   D: pin 14
  //   E: pin 3
  //   F: pin 4
  //   G: pin 5
  //   H: pin 6
endmodule
