// Digital circuit 74LS191.dig as structural Verilog
module _74LS191 (
  input  nENG,
  input  DN_UP,
  input  A,
  input  B,
  input  C,
  input  D,
  input  nLOAD,
  input  CLK,
  output QA,
  output QB,
  output QC,
  output QD,
  output MAX_MIN,
  output nRCO
);

  wire not_1_out, not_2_out;

  not not_1 (not_1_out, nENG);
  not not_2 (not_2_out, nLOAD);
  CounterPreset #(.Bits(4), .maxValue(16)) counterpreset_1 (
    .en(not_1_out), .C(CLK), .dir(DN_UP), .in({D, C, B, A}), .ld(not_2_out), .clr(1'b0),
    .out({QD, QC, QB, QA}), .ovf(MAX_MIN));
  nand nand_1 (nRCO, MAX_MIN, not_1_out, CLK);
endmodule
