// Digital circuit 74LS244.dig as structural Verilog
module _74LS244 (
  input  _1A1,
  input  _1A2,
  input  _1A3,
  input  _1A4,
  input  _2A1,
  input  _2A2,
  input  _2A3,
  input  _2A4,
  input  _2nG,
  input  _1nG,
  output _1Y1,
  output _1Y2,
  output _1Y3,
  output _1Y4,
  output _2Y1,
  output _2Y2,
  output _2Y3,
  output _2Y4
);

  assign _2Y1 = ~_2nG ? _2A1 : 1'bz;  // DriverInvSel driverinvsel_1
  assign _2Y2 = ~_2nG ? _2A2 : 1'bz;  // DriverInvSel driverinvsel_2
  assign _2Y3 = ~_2nG ? _2A3 : 1'bz;  // DriverInvSel driverinvsel_3
  assign _2Y4 = ~_2nG ? _2A4 : 1'bz;  // DriverInvSel driverinvsel_4
  PullUp pullup_1 (.out(_2nG));
  PullUp pullup_2 (.out(_1nG));
  assign _1Y1 = ~_1nG ? _1A1 : 1'bz;  // DriverInvSel driverinvsel_5
  assign _1Y2 = ~_1nG ? _1A2 : 1'bz;  // DriverInvSel driverinvsel_6
  assign _1Y3 = ~_1nG ? _1A3 : 1'bz;  // DriverInvSel driverinvsel_7
  assign _1Y4 = ~_1nG ? _1A4 : 1'bz;  // DriverInvSel driverinvsel_8

  // Notes on the sheet:
  //   _2nG: default 1
  //   _1nG: default 1
endmodule
