// Digital circuit 74LS244fake2.dig as structural Verilog
module _74LS244fake2 (
  input  _1A1,
  input  _1A2,
  input  _1A3,
  input  _1A4,
  input  _2A1,
  input  _2A2,
  input  _2A3,
  input  _2A4,
  input  _2nG,
  input  _1nG,
  output _1Y1,
  output _1Y2,
  output _1Y3,
  output _1Y4,
  output _2Y1,
  output _2Y2,
  output _2Y3,
  output _2Y4
);

  wire not_1_out, not_2_out;
  wire [3:0] bussplitter_1_d, bussplitter_2_d, bussplitter_3_d, driver_1_out;

  BusSplitter #(.Bits(4)) bussplitter_1 (.D(bussplitter_1_d), .OE(_1nG), .D0(_1A1), .D1(_1A2), .D2(_1A3), .D3(_1A4));
  not not_1 (not_1_out, _2nG);
  BusSplitter #(.Bits(4)) bussplitter_2 (
    .D(bussplitter_2_d), .OE(not_1_out), .D0(_2Y1), .D1(_2Y2), .D2(_2Y3), .D3(_2Y4));
  assign driver_1_out = not_2_out ? bussplitter_1_d : 4'bz;  // Driver driver_1
  assign bussplitter_2_d = not_1_out ? bussplitter_3_d : 4'bz;  // Driver driver_2
  BusSplitter #(.Bits(4)) bussplitter_3 (.D(bussplitter_3_d), .OE(_2nG), .D0(_2A1), .D1(_2A2), .D2(_2A3), .D3(_2A4));
  not not_2 (not_2_out, _1nG);
  BusSplitter #(.Bits(4)) bussplitter_4 (.D(driver_1_out), .OE(not_2_out), .D0(_1Y1), .D1(_1Y2), .D2(_1Y3), .D3(_1Y4));
endmodule
