// Digital circuit 74LS93.dig as structural Verilog
// 4-bit Binary Counter.
// Connect QA to CKB and clock on CKA for full 4-bit counter.  Connect QB to R1 and QD to R2 for a BCD counter.
module _74LS93 (
  input  CKA,
  input  CKB,
  input  R1,
  input  R2,
  output QA,
  output QB,
  output QC,
  output QD
);

  wire nand_1_out;

  nand nand_1 (nand_1_out, R1, R2);
  JK_FF_AS jk_ff_as_1 (.Set(1'b0), .J(1'b1), .C(~CKA), .K(1'b1), .Clr(~nand_1_out), .Q(QA));  // open: nQ
  JK_FF_AS jk_ff_as_2 (.Set(1'b0), .J(1'b1), .C(~CKB), .K(1'b1), .Clr(~nand_1_out), .Q(QB));  // open: nQ
  JK_FF_AS jk_ff_as_3 (.Set(1'b0), .J(1'b1), .C(~QB), .K(1'b1), .Clr(~nand_1_out), .Q(QC));  // open: nQ
  JK_FF_AS jk_ff_as_4 (.Set(1'b0), .J(1'b1), .C(~QC), .K(1'b1), .Clr(~nand_1_out), .Q(QD));  // open: nQ

  // Notes on the sheet:
  //   CKA: Clock A input, pin 14
  //   CKB: Clock B input, pin 1
  //   R1: First reset input, pin 2
  //   QA: Bit 0 (LSB) of 4-bit counter, pin 12
  //   QB: Bit 1 of 4-bit counter, pin 9
  //   QC: Bit 2 of 4-bit counter, pin 8
  //   QD: Bit 3 (MSB) of 4-bit counter, pin 11
  //   R2: First reset input, pin 3
endmodule
