// Digital circuit 74S74.dig as structural Verilog
// 1/2 74LS74 D-flip-flop
module _74S74 (
  input  nP,
  input  D,
  input  CK,
  input  nCL,
  output Q,
  output nQ
);

  wire and_1_out, d_ff_as_1_nq;

  D_FF_AS d_ff_as_1 (.Set(~nP), .D(D), .C(CK), .Clr(~nCL), .Q(Q), .nQ(d_ff_as_1_nq));
  and and_1 (and_1_out, ~nP, ~nCL);  // And
  or or_1 (nQ, d_ff_as_1_nq, and_1_out);
endmodule
