// Digital circuit CRT-white.dig as structural Verilog
module CRT_white (
  input  VIDEO,
  input  CLK8,
  input  HOR_DRIVE_IN,
  input  VER_DRIVE_IN
);

  wire d_ff_1_q, monoflop_1_q;
  wire [7:0] ROW_out;
  wire [8:0] COLUMN_out;

  Monoflop #(.timerDelay(100)) monoflop_1 (.C(HOR_DRIVE_IN), .R(~HOR_DRIVE_IN), .Q(monoflop_1_q));  // open: nQ
  D_FF d_ff_1 (.D(~VER_DRIVE_IN), .C(CLK8), .Q(d_ff_1_q));  // open: nQ
  Counter #(.Bits(9)) COLUMN (.en(1'b1), .C(CLK8), .clr(monoflop_1_q), .out(COLUMN_out));  // open: ovf
  Counter #(.Bits(8)) ROW (.en(1'b1), .C(monoflop_1_q), .clr(d_ff_1_q), .out(ROW_out));  // open: ovf
  // Probe on {1'b0, ROW_out, COLUMN_out}
  GraphicCard #(.graphicHeight(256), .graphicWidth(512)) graphiccard_1 (
    .A({1'b0, ROW_out, COLUMN_out}), .str(1'b1), .C(CLK8), .ld(1'b0), .B(1'b0), .D(VIDEO));

  // Notes on the sheet:
  //   VIDEO: Video Signal (1=Black, 0=White)
  //   CLK8: Hz: 10
  //   HOR_DRIVE_IN: Horizontal sync (active high)
  //   VER_DRIVE_IN: Vertical Sync (active low)
  //   Always write to Bank 0
endmodule
