// Digital circuit DIAG-Keyboard-Dongle.dig as structural Verilog
module DIAG_Keyboard_Dongle (
  input  _2,
  input  _3,
  input  _4,
  input  _5,
  input  _6,
  input  _7,
  input  _8,
  input  _9,
  input  _10,
  input  _1,
  input  CLK,
  output A,
  output B,
  output C,
  output D,
  output E,
  output F,
  output H,
  output J
);

  wire or_1_out, or_2_out;

  not not_1 (A, or_1_out);
  not not_2 (B, or_2_out);
  not not_3 (C, _3);
  not not_4 (D, _4);
  not not_5 (E, _5);
  not not_6 (F, _6);
  not not_7 (H, _7);
  not not_8 (J, _8);
  or or_1 (or_1_out, _1, _9);
  or or_2 (or_2_out, _2, _10);

  // Notes on the sheet:
  //   The real dongle does not have 
  //   these OR-Gates.
  //   Source:
  //   https://www.c64-wiki.com/wiki/PET_2001#Diagnostic_plugs
endmodule
