// Digital circuit DIAG-Userport-Dongle.dig as structural Verilog
// Dignostic Mode Dongle
// Source: https://www.c64-wiki.com/wiki/PET_2001#Diagnostic_plugs
module DIAG_Userport_Dongle (
  input  VIDEO__2,
  input  CASS_WRITE__7,
  input  VERT_DRIVE__9,
  input  HORZ_DRIVE__10,
  input  GND__11,
  input  PA2__E,
  input  PA3__F,
  input  PA4__H,
  input  PA5__J,
  input  PA0__C,
  input  PA1__D,
  output CA1__B,
  output PA6__K,
  output PA7__L,
  output nSRQ_IN__3,
  output nEOI_IN__4,
  output DIAG__5,
  output _2_CASS_READ__6,
  output _1_CASS_READ__8
);

  or or_1 (DIAG__5, GND__11, PA2__E);
  PullDown pulldown_1 (.out(PA2__E));

  assign _1_CASS_READ__8 = CASS_WRITE__7;
  assign _2_CASS_READ__6 = CASS_WRITE__7;
  assign CA1__B = VIDEO__2;
  assign nEOI_IN__4 = PA1__D;
  assign nSRQ_IN__3 = PA0__C;
  assign PA6__K = VERT_DRIVE__9;
  assign PA7__L = HORZ_DRIVE__10;
endmodule
