// Digital circuit MB-3032-Debugging_and_Tests.dig as structural Verilog
module MB_3032_Debugging_and_Tests (
  input  _16MHz,
  output [15:0] BA,
  output [7:0] D,
  output \BΦ2 ,
  output [31:0] cycle,
  output r_w,
  output nIRQ,
  output SYNC
);

  wire _1_CASS_MOTOR, _1_CASS_READ, _1_CASS_SWITCH, _2_CASS_MOTOR, _2_CASS_READ, _2_CASS_SWITCH,
       _74ls93_2_qc, _74ls107_2_nq, _74ls107_5_nq, _74ls107_5_q, _74ls107_6_nq, _74ls107_6_q, _74ls107_7_q,
       _74LS145__0, _74LS145__1, _74LS145__2, _74LS145__3, _74LS145__4, _74LS145__5, _74LS145__6,
       _74LS145__7, _74LS145__8, _74LS145__9, _74ls157_1_y1, _74ls157_1_y4, _74ls164_1_qa, _74ls164_1_qb,
       _74ls164_1_qc, _74ls164_1_qd, _74ls164_1_qf, _74ls164_1_qg, _74ls165_1_nqh, _74ls165_1_qh,
       _74ls244_6__2y1, _74ls373_1_q0, _74ls373_1_q1, _74ls373_1_q2, _74ls373_1_q3, _74ls373_1_q4,
       _74ls373_1_q5, _74ls373_1_q6, _74ls373_1_q7, _74ls373_2_q7, _74s74_2_nq, _74s74_3_nq, _74s74_5_nq,
       _74s74_5_q, _4116_1_do, _4116_2_do, _4116_3_do, _4116_4_do, _4116_5_do, _4116_6_do, _4116_7_do,
       _4116_8_do, _4116_9_do, _4116_10_do, _4116_11_do, _4116_12_do, _4116_13_do, _4116_14_do, _4116_15_do,
       _6316_rom_1_d0, _6316_rom_1_d1, _6316_rom_1_d2, _6316_rom_1_d3, _6316_rom_1_d4, _6316_rom_1_d5,
       _6316_rom_1_d6, _6316_rom_1_d7, _6502_diag_clip_1_ab0, _6502_diag_clip_1_ab1, _6502_diag_clip_1_ab2,
       _6502_diag_clip_1_ab3, _6502_diag_clip_1_ab4, _6502_diag_clip_1_ab5, _6502_diag_clip_1_ab6,
       _6502_diag_clip_1_ab7, _6502_diag_clip_1_ab8, _6502_diag_clip_1_ab9, _6502_diag_clip_1_ab10,
       _6502_diag_clip_1_ab11, _6502_diag_clip_1_ab12, _6502_diag_clip_1_ab13, _6502_diag_clip_1_ab14,
       _6502_diag_clip_1_ab15, \_6502_diag_clip_1_φ1 , _6520_1_ca2, _6520_1_cb2, _6520_1_pa0, _6520_1_pa1,
       _6520_1_pa2, _6520_1_pa3, _6520_1_pa4, _6520_1_pa5, _6520_1_pa6, _6520_1_pa7, _6520_1_pb0,
       _6520_1_pb1, _6520_1_pb2, _6520_1_pb3, _6520_1_pb4, _6520_1_pb5, _6520_1_pb6, _6520_1_pb7,
       _6520_2_cb2, _6520_2_pa0, _6520_2_pa1, _6520_2_pa2, _6520_2_pa3, _6520_2_pb0, _6520_2_pb1,
       _6520_2_pb2, _6520_2_pb3, _6520_2_pb4, _6520_2_pb5, _6520_2_pb6, _6520_2_pb7, _6522_1_cb2,
       _6522_1_pb0, _6522_1_pb1, _6522_1_pb2, _6522_1_pb4, _6522_1_pb6, _6522_1_pb7, _74177_1_qa,
       _74177_1_qb, _74177_1_qc, _74177_1_qd, _74177_2_qa, _74177_2_qb, _74177_2_qc, _74177_2_qd, and_2_out,
       and_3_out, and_4_out, and_5_out, and_11_out, and_12_out, and_13_out, B_R_W, BANK_SEL, BD0, BD1, BD2,
       BD3, BD4, BD5, BD6, BD7, \BΦ2H , CA1, CASS_WRITE, CLK1, CLK8, comparator_1_eq, CS1, DIAG, DIAG_CLIP,
       fuse_1_b, fuse_5_b, fuse_7_b, fuse_10_b, fuse_11_b, fuse_14_b, GRAPHIC, HORZ_DISP_OFF, HORZ_DISP_ON,
       HORZ_DRIVE, LOAD_SR, MUX_A, nand_1_out, nand_2_out, nand_3_out, nand_4_out, nand_8_out, nand_9_out,
       nand_10_out, nand_11_out, nand_12_out, nand_14_out, nand_15_out, nand_17_out, nand_18_out, nB_R_W,
       nBA11, nCAS0, nCAS1, nEOI, nEOI_OUT, NEXT, nI_O, nINIT, nLOAD_SR, nNEXT, nNMI, not_2_out, not_4_out,
       not_5_out, not_6_out, not_7_out, not_8_out, not_9_out, not_10_out, not_12_out, not_13_out, not_14_out,
       not_15_out, not_17_out, not_18_out, not_19_out, not_20_out, notconnected_1_out, notconnected_2_out,
       notconnected_3_out, notconnected_4_out, notconnected_5_out, notconnected_6_out, notconnected_7_out,
       nRA1, nRAS0, nRELOAD, nRES, nSEL_8, nSEL_9, nSEL_A, nSEL_B, nSEL_C, nSEL_D, nSEL_E, nSEL_F, nSRQ_IN,
       nTV_READ, or_1_out, PA0, PA1, PA2, PA3, PA4, PA5, PA6, PA7, pullup_5_out, pullup_6_out, pullup_7_out,
       pullup_8_out, pullup_9_out, pullup_10_out, pullup_11_out, RA1, RA2, RA3, RA4, RA5, RA6, RA7, RA9,
       RAM_R_W, RDY, reset_1_out, RESET_Delay_ovf, SD0, SD1, SD2, SD3, SD4, SD5, SD6, SD7, SEL_8, TV_RAM_R_W,
       VERT_DRIVE, VIDEO, VIDEO_LATCH, VIDEO_ON, X8XX;
  wire [6:0] _74ls373_2_q0, _74153simplified_4__1y;
  wire [7:0] F000_d;
  wire [9:0] SA;

  not not_1 (nBA11, BA[11]);
  PullUp pullup_1 (.out(nIRQ));
  Reset reset_1 (.out(reset_1_out));
  Reset RESET_2 (.out(nINIT));
  _74191simplified _74191simplified_1 (
    .nENG(1'b0), .DN_UP(1'b0), .CLK(_16MHz), .QA(CLK8), .QD(CLK1));  // open: QB, QC, MAX_MIN, nRCO
  _74LS107 _74ls107_1 (.J(nINIT), .nCLK(not_15_out), .K(nINIT), .Q(RA1), .nQ(nRA1), .nCLR(nINIT));
  not not_2 (not_2_out, nINIT);
  _74LS107 _74ls107_2 (.J(nINIT), .nCLK(RA5), .K(nINIT), .Q(RA6), .nQ(_74ls107_2_nq), .nCLR(nINIT));
  Fuse #(.Blown("true")) fuse_1 (.A(BA[14]), .B(fuse_1_b));
  Fuse fuse_2 (.A(nSEL_8), .B(fuse_1_b));
  not not_3 (SEL_8, nSEL_8);
  and and_1 (X8XX, ~BA[8], ~BA[9], ~BA[10], ~nBA11);  // And
  Counter #(.Bits(2)) RESET_Delay (.en(reset_1_out), .C(CLK1), .clr(nRES), .ovf(RESET_Delay_ovf));  // open: out
  PullUp pullup_2 (.out(nNMI));
  not not_4 (not_4_out, nSEL_F);
  not not_5 (not_5_out, nSEL_E);
  not not_6 (not_6_out, nSEL_D);
  not not_7 (not_7_out, nSEL_C);
  not not_8 (not_8_out, nSEL_B);
  not not_9 (not_9_out, nSEL_A);
  not not_10 (not_10_out, nSEL_9);
  nand nand_1 (nand_1_out, BA[15], fuse_1_b);
  nand nand_2 (nand_2_out, SEL_8, X8XX);
  PullUp pullup_3 (.out(RDY));
  RS_FF_AS rs_ff_as_1 (.S(RESET_Delay_ovf), .R(1'b0), .Q(nRES));  // open: nQ
  _74LS93 _74ls93_1 (.CKA(RA1), .CKB(RA2), .R1(not_2_out), .R2(not_2_out), .QA(RA2), .QB(RA3), .QC(RA4), .QD(RA5));
  PullUp pullup_4 (.out(DIAG_CLIP));
  or or_1 (or_1_out, ~nand_1_out, ~nand_2_out, ~B_R_W);  // Or
  _6502_DIAG_Clip _6502_diag_clip_1 (
    .AB0(_6502_diag_clip_1_ab0), .AB1(_6502_diag_clip_1_ab1), .AB2(_6502_diag_clip_1_ab2),
    .AB3(_6502_diag_clip_1_ab3), .AB4(_6502_diag_clip_1_ab4), .AB5(_6502_diag_clip_1_ab5),
    .AB6(_6502_diag_clip_1_ab6), .AB7(_6502_diag_clip_1_ab7), .AB8(_6502_diag_clip_1_ab8),
    .AB9(_6502_diag_clip_1_ab9), .AB10(_6502_diag_clip_1_ab10), .AB11(_6502_diag_clip_1_ab11),
    .AB12(_6502_diag_clip_1_ab12), .AB13(_6502_diag_clip_1_ab13), .AB14(_6502_diag_clip_1_ab14),
    .AB15(_6502_diag_clip_1_ab15), .\Φ0 (CLK1), .nRESET(nRES), .nNMI(nNMI), .nIRQ(nIRQ), .RDY(RDY),
    .\Φ2 (\BΦ2 ), .\Φ1 (\_6502_diag_clip_1_φ1 ), .R_W(r_w), .SYNC(SYNC), .DA0(D[0]), .DA1(D[1]), .DA2(D[2]),
    .DA3(D[3]), .DA4(D[4]), .DA5(D[5]), .DA6(D[6]), .DA7(D[7]), .S_O(DIAG_CLIP));  // open: N_C
  ROM #(.AddrBits(12), .isProgramMemory("true"), .Bits(8)) F000 (.A(BA[11:0]), .sel(not_4_out), .D(F000_d));
  ROM #(.AddrBits(12), .isProgramMemory("true"), .Bits(8)) E000 (.A(BA[11:0]), .sel(and_2_out), .D(F000_d));
  and and_2 (and_2_out, ~BA[11], not_5_out);  // And
  and and_3 (and_3_out, RA1, RA3);
  and and_4 (and_4_out, RA4, RA6);
  and and_5 (and_5_out, RA5, _74ls107_2_nq);
  ROM #(.AddrBits(12), .isProgramMemory("true"), .Bits(8)) D000 (.A(BA[11:0]), .sel(not_6_out), .D(F000_d));
  _74S74 _74s74_1 (.Q(LOAD_SR), .nQ(nLOAD_SR), .nP(pullup_5_out), .D(nINIT), .CK(not_15_out), .nCL(_74ls164_1_qb));
  _74LS107 _74ls107_3 (
    .J(and_4_out), .nCLK(nLOAD_SR), .K(and_5_out), .Q(HORZ_DISP_ON), .nQ(HORZ_DISP_OFF), .nCLR(nINIT));
  ROM #(.AddrBits(12), .isProgramMemory("true"), .Bits(8)) C000 (.A(BA[11:0]), .sel(not_7_out), .D(F000_d));
  _74LS164 _74ls164_1 (
    .A(CLK1), .B(1'b1), .CK(_16MHz), .nCL(nINIT), .QA(_74ls164_1_qa), .QB(_74ls164_1_qb), .QC(_74ls164_1_qc),
    .QD(_74ls164_1_qd), .QF(_74ls164_1_qf), .QG(_74ls164_1_qg), .QH(\BΦ2H ));  // open: QE
  PullUp pullup_5 (.out(pullup_5_out));
  nand nand_3 (nand_3_out, BANK_SEL, \BΦ2 );
  _74LS244 _74ls244_1 (
    ._1Y1(BD0), ._2A1(BD0), ._1Y2(BD1), ._2A2(BD1), ._1Y3(BD2), ._2A3(BD2), ._1Y4(BD3), ._2A4(BD3),
    ._1nG(nand_4_out), ._1A1(D[0]), ._2Y1(D[0]), ._1A2(D[1]), ._2Y2(D[1]), ._1A3(D[2]), ._2Y3(D[2]),
    ._1A4(D[3]), ._2Y4(D[3]), ._2nG(or_1_out));
  _74LS244 _74ls244_2 (
    ._1Y1(BD4), ._2A1(BD4), ._1Y2(BD5), ._2A2(BD5), ._1Y3(BD6), ._2A3(BD6), ._1Y4(BD7), ._2A4(BD7),
    ._1nG(nand_4_out), ._1A1(D[4]), ._2Y1(D[4]), ._1A2(D[5]), ._2Y2(D[5]), ._1A3(D[6]), ._2Y3(D[6]),
    ._1A4(D[7]), ._2Y4(D[7]), ._2nG(or_1_out));
  _74LS244 _74ls244_3 (
    ._1A1(_6502_diag_clip_1_ab0), ._1A2(_6502_diag_clip_1_ab1), ._1A3(_6502_diag_clip_1_ab2),
    ._1A4(_6502_diag_clip_1_ab3), ._2A1(_6502_diag_clip_1_ab4), ._2A2(_6502_diag_clip_1_ab5),
    ._2A3(_6502_diag_clip_1_ab6), ._2A4(_6502_diag_clip_1_ab7), ._2nG(1'b0), ._1nG(1'b0), ._1Y1(BA[0]),
    ._1Y2(BA[1]), ._1Y3(BA[2]), ._1Y4(BA[3]), ._2Y1(BA[4]), ._2Y2(BA[5]), ._2Y3(BA[6]), ._2Y4(BA[7]));
  _74LS244 _74ls244_4 (
    ._1A1(_6502_diag_clip_1_ab8), ._1A2(_6502_diag_clip_1_ab9), ._1A3(_6502_diag_clip_1_ab10),
    ._1A4(_6502_diag_clip_1_ab11), ._2A1(_6502_diag_clip_1_ab12), ._2A2(_6502_diag_clip_1_ab13),
    ._2A3(_6502_diag_clip_1_ab14), ._2A4(_6502_diag_clip_1_ab15), ._2nG(1'b0), ._1nG(1'b0), ._1Y1(BA[8]),
    ._1Y2(BA[9]), ._1Y3(BA[10]), ._1Y4(BA[11]), ._2Y1(BA[12]), ._2Y2(BA[13]), ._2Y3(BA[14]), ._2Y4(BA[15]));
  Delay delay_1 (.in(r_w), .out(B_R_W));
  ROM #(.AddrBits(12), .Bits(8)) B000 (.A(BA[11:0]), .sel(not_8_out), .D(F000_d));
  nand nand_4 (nand_4_out, 1'b1, or_1_out);
  not not_11 (nB_R_W, B_R_W);
  ROM #(.AddrBits(12), .Bits(8)) A000 (.A(BA[11:0]), .sel(not_9_out), .D(F000_d));
  _74LS107 _74ls107_4 (
    .J(HORZ_DISP_ON), .nCLK(and_3_out), .K(HORZ_DISP_OFF), .nQ(HORZ_DRIVE), .nCLR(nINIT));  // open: Q
  ROM #(.AddrBits(12), .Bits(8)) _9000 (.A(BA[11:0]), .sel(not_10_out), .D(F000_d));
  not not_12 (not_12_out, _74ls164_1_qb);
  not not_13 (not_13_out, _74ls164_1_qf);
  not not_14 (not_14_out, _74ls164_1_qg);
  not not_15 (not_15_out, _74ls164_1_qa);
  _74154simplified _74154simplified_1 (
    .G1(1'b0), .G2(1'b0), .A(BA[12]), .B(BA[13]), .C(BA[14]), .D(BA[15]), .Y8(nSEL_8), .Y9(nSEL_9),
    .Y10(nSEL_A), .Y11(nSEL_B), .Y12(nSEL_C), .Y13(nSEL_D), .Y14(nSEL_E), .Y15(nSEL_F));  // open: Y0, Y1, Y2, Y3, Y4, Y5, Y6, Y7
  not not_16 (RAM_R_W, nB_R_W);
  // Relay #(.Bits(8)) relay_1: pin names not known; wires that end beside it: r_w, F000_d, 1'b0, D
  _74LS157 _74ls157_1 (
    ._1A(_74ls164_1_qb), ._1B(_74ls164_1_qa), ._2A(notconnected_1_out), ._2B(notconnected_2_out),
    ._3A(_74ls164_1_qc), ._3B(_74ls164_1_qb), ._4A(_74ls164_1_qd), ._4B(_74ls164_1_qc), .S(B_R_W),
    .G(nand_3_out), .Y1(_74ls157_1_y1), .Y3(MUX_A), .Y4(_74ls157_1_y4));  // open: Y2
  // NotConnected on notconnected_1_out
  // NotConnected on notconnected_2_out
  and and_6 (VIDEO_LATCH, not_13_out, \BΦ2H );
  _74LS107 _74ls107_5 (
    .J(_74ls107_6_nq), .nCLK(NEXT), .K(_74ls107_6_q), .Q(_74ls107_5_q), .nQ(_74ls107_5_nq), .nCLR(nINIT));
  Fuse fuse_3 (.A(nSEL_E), .B(nI_O));
  Fuse #(.Blown("true")) fuse_4 (.A(nSEL_8), .B(nI_O));
  Fuse #(.Blown("true")) fuse_5 (.A(BA[13]), .B(fuse_5_b));
  Fuse fuse_6 (.A(BA[14]), .B(fuse_5_b));
  _74S74 _74s74_2 (.nQ(_74s74_2_nq), .nP(nINIT), .D(nINIT), .CK(_74ls157_1_y1), .nCL(not_14_out));  // open: Q
  _74S74 _74s74_3 (.nQ(_74s74_3_nq), .nP(1'b1), .D(nINIT), .CK(not_12_out), .nCL(_74ls164_1_qf));  // open: Q
  not not_17 (not_17_out, fuse_5_b);
  _74LS107 _74ls107_6 (
    .J(_74ls107_5_q), .nCLK(NEXT), .K(_74ls107_5_nq), .Q(_74ls107_6_q), .nQ(_74ls107_6_nq), .nCLR(nINIT));
  and and_7 (nRAS0, _74s74_2_nq, _74s74_3_nq);
  nand nand_5 (nCAS1, _74ls157_1_y4, _74ls157_1_y4, fuse_5_b);
  nand nand_6 (nCAS0, _74ls157_1_y4, _74ls157_1_y4, not_17_out);
  nand nand_7 (VERT_DRIVE, _74ls107_6_nq, _74ls107_5_nq);
  and and_8 (VIDEO_ON, _74ls107_5_q, _74ls107_6_q);
  Fuse fuse_7 (.A(BA[13]), .B(fuse_7_b));
  Fuse #(.Blown("true")) fuse_8 (.A(1'b1), .B(fuse_7_b));
  Fuse #(.Blown("true")) fuse_9 (.A(1'b0), .B(fuse_7_b));
  // NotConnected on notconnected_3_out
  // NotConnected on notconnected_4_out
  // NotConnected on notconnected_5_out
  // NotConnected on notconnected_6_out
  nand nand_8 (nand_8_out, nRELOAD, nNEXT);
  _74153simplified _74153simplified_1 (
    .n1G(1'b0), ._1C0(RA7), ._1C1(RA7), ._1C2(BA[0]), ._1C3(fuse_7_b), .A(MUX_A), .B(CLK1), ._2C0(RA1),
    ._2C1(RA1), ._2C2(BA[1]), ._2C3(BA[7]), .n2G(1'b0), ._1Y(_74153simplified_4__1y[0]),
    ._2Y(_74153simplified_4__1y[1]));
  _74153simplified _74153simplified_2 (
    .n1G(1'b0), ._1C0(RA2), ._1C1(RA2), ._1C2(BA[2]), ._1C3(BA[8]), .A(MUX_A), .B(CLK1), ._2C0(RA3),
    ._2C1(RA3), ._2C2(BA[3]), ._2C3(BA[9]), .n2G(1'b0), ._1Y(_74153simplified_4__1y[2]),
    ._2Y(_74153simplified_4__1y[3]));
  _74153simplified _74153simplified_3 (
    .n1G(1'b0), ._1C0(RA4), ._1C1(RA4), ._1C2(BA[4]), ._1C3(BA[10]), .A(MUX_A), .B(CLK1), ._2C0(RA5),
    ._2C1(RA5), ._2C2(BA[5]), ._2C3(BA[11]), .n2G(1'b0), ._1Y(_74153simplified_4__1y[4]),
    ._2Y(_74153simplified_4__1y[5]));
  _74153simplified _74153simplified_4 (
    .n1G(1'b0), ._1C0(RA6), ._1C1(RA6), ._1C2(BA[6]), ._1C3(BA[12]), .A(MUX_A), .B(CLK1),
    ._2C0(notconnected_3_out), ._2C1(notconnected_4_out), ._2C2(notconnected_5_out),
    ._2C3(notconnected_6_out), .n2G(1'b0), ._1Y(_74153simplified_4__1y[6]));  // open: _2Y
  not not_18 (not_18_out, VIDEO_ON);
  PullUp pullup_6 (.out(pullup_6_out));
  and and_9 (CS1, X8XX, BA[6]);
  _74LS373 _74ls373_1 (
    .D0(_74177_1_qa), .D1(_74177_1_qb), .D2(_74177_1_qc), .D3(_74177_1_qd), .D4(_74177_2_qa),
    .D5(_74177_2_qb), .D6(_74177_2_qc), .D7(_74177_2_qd), .G(nand_8_out), .nOC(1'b0), .Q0(_74ls373_1_q0),
    .Q1(_74ls373_1_q1), .Q2(_74ls373_1_q2), .Q3(_74ls373_1_q3), .Q4(_74ls373_1_q4), .Q5(_74ls373_1_q5),
    .Q6(_74ls373_1_q6), .Q7(_74ls373_1_q7));
  _6520 _6520_1 (
    .D0(D[0]), .D1(D[1]), .D2(D[2]), .D3(D[3]), .D4(D[4]), .D5(D[5]), .D6(D[6]), .D7(D[7]), .CS1(BA[5]),
    .nCS2(nI_O), .CS0(X8XX), .RS0(BA[0]), .RS1(BA[1]), .R_W(r_w), .\Φ2 (\BΦ2 ), .nRESET(nRES), .nIRQA(nIRQ),
    .CA1(1'b1), .CA2(_6520_1_ca2), .PA0(_6520_1_pa0), .PA1(_6520_1_pa1), .PA2(_6520_1_pa2),
    .PA3(_6520_1_pa3), .PA4(_6520_1_pa4), .PA5(_6520_1_pa5), .PA6(_6520_1_pa6), .PA7(_6520_1_pa7),
    .PB0(_6520_1_pb0), .PB1(_6520_1_pb1), .PB2(_6520_1_pb2), .PB3(_6520_1_pb3), .PB4(_6520_1_pb4),
    .PB5(_6520_1_pb5), .PB6(_6520_1_pb6), .PB7(_6520_1_pb7), .CB1(nSRQ_IN), .CB2(_6520_1_cb2), .nIRQB(nIRQ));
  Fuse #(.Blown("true")) fuse_10 (.A(BA[13]), .B(fuse_10_b));
  Fuse fuse_11 (.A(BA[14]), .B(fuse_11_b));
  Fuse #(.Blown("true")) fuse_12 (.A(1'b0), .B(fuse_11_b));
  Fuse fuse_13 (.A(1'b0), .B(fuse_10_b));
  Fuse fuse_14 (.A(1'b0), .B(fuse_14_b));
  nand nand_9 (nand_9_out, _74177_2_qa, pullup_6_out, not_18_out, RA9);
  _4116 _4116_1 (
    .A0(_74153simplified_4__1y[0]), .A1(_74153simplified_4__1y[1]), .A2(_74153simplified_4__1y[2]),
    .A3(_74153simplified_4__1y[3]), .A4(_74153simplified_4__1y[4]), .A5(_74153simplified_4__1y[5]),
    .A6(_74153simplified_4__1y[6]), .nWE(RAM_R_W), .nRAS(nRAS0), .nCAS(nCAS1), .DI(_4116_2_do),
    .DO(_4116_1_do));
  _4116 _4116_2 (
    .A0(_74153simplified_4__1y[0]), .A1(_74153simplified_4__1y[1]), .A2(_74153simplified_4__1y[2]),
    .A3(_74153simplified_4__1y[3]), .A4(_74153simplified_4__1y[4]), .A5(_74153simplified_4__1y[5]),
    .A6(_74153simplified_4__1y[6]), .nWE(RAM_R_W), .nRAS(nRAS0), .nCAS(nCAS0), .DI(_4116_2_do),
    .DO(_4116_2_do));
  and and_10 (BANK_SEL, ~fuse_11_b, ~fuse_10_b, ~fuse_14_b, ~BA[15]);  // And
  and and_11 (and_11_out, nBA11, SEL_8);
  PullUp pullup_7 (.out(pullup_7_out));
  nand nand_10 (nand_10_out, _74ls373_1_q4, _74ls373_1_q5, _74ls373_1_q6, _74ls373_1_q7);
  _74LS107 _74ls107_7 (.J(nINIT), .nCLK(nRA1), .K(nINIT), .Q(_74ls107_7_q), .nCLR(HORZ_DISP_ON));  // open: nQ
  _4116 _4116_3 (
    .A0(_74153simplified_4__1y[0]), .A1(_74153simplified_4__1y[1]), .A2(_74153simplified_4__1y[2]),
    .A3(_74153simplified_4__1y[3]), .A4(_74153simplified_4__1y[4]), .A5(_74153simplified_4__1y[5]),
    .A6(_74153simplified_4__1y[6]), .nWE(RAM_R_W), .nRAS(nRAS0), .nCAS(nCAS1), .DI(_4116_4_do),
    .DO(_4116_3_do));
  _4116 _4116_4 (
    .A0(_74153simplified_4__1y[0]), .A1(_74153simplified_4__1y[1]), .A2(_74153simplified_4__1y[2]),
    .A3(_74153simplified_4__1y[3]), .A4(_74153simplified_4__1y[4]), .A5(_74153simplified_4__1y[5]),
    .A6(_74153simplified_4__1y[6]), .nWE(RAM_R_W), .nRAS(nRAS0), .nCAS(nCAS0), .DI(_4116_4_do),
    .DO(_4116_4_do));
  _74177 _74177_1 (
    .CLK2(_74177_1_qa), .CLK1(_74ls107_7_q), .nLD(HORZ_DISP_ON), .nCLR(nNEXT), .A(_74ls373_1_q0),
    .B(_74ls373_1_q1), .C(_74ls373_1_q2), .D(_74ls373_1_q3), .QA(_74177_1_qa), .QB(_74177_1_qb),
    .QC(_74177_1_qc), .QD(_74177_1_qd));
  _74177 _74177_2 (
    .CLK2(_74177_2_qa), .CLK1(_74177_1_qd), .nLD(HORZ_DISP_ON), .nCLR(nNEXT), .A(_74ls373_1_q4),
    .B(_74ls373_1_q5), .C(_74ls373_1_q6), .D(_74ls373_1_q7), .QA(_74177_2_qa), .QB(_74177_2_qb),
    .QC(_74177_2_qc), .QD(_74177_2_qd));
  not not_19 (not_19_out, nand_10_out);
  nand nand_11 (nand_11_out, pullup_7_out, BANK_SEL, B_R_W);
  nand nand_12 (nand_12_out, _74ls373_1_q1, not_19_out);
  _4116 _4116_5 (
    .A0(_74153simplified_4__1y[0]), .A1(_74153simplified_4__1y[1]), .A2(_74153simplified_4__1y[2]),
    .A3(_74153simplified_4__1y[3]), .A4(_74153simplified_4__1y[4]), .A5(_74153simplified_4__1y[5]),
    .A6(_74153simplified_4__1y[6]), .nWE(RAM_R_W), .nRAS(nRAS0), .nCAS(nCAS1), .DI(_4116_6_do),
    .DO(_4116_5_do));
  _4116 _4116_6 (
    .A0(_74153simplified_4__1y[0]), .A1(_74153simplified_4__1y[1]), .A2(_74153simplified_4__1y[2]),
    .A3(_74153simplified_4__1y[3]), .A4(_74153simplified_4__1y[4]), .A5(_74153simplified_4__1y[5]),
    .A6(_74153simplified_4__1y[6]), .nWE(RAM_R_W), .nRAS(nRAS0), .nCAS(nCAS0), .DI(_4116_6_do),
    .DO(_4116_6_do));
  PullUp pullup_8 (.out(pullup_8_out));
  nand nand_13 (nTV_READ, pullup_8_out, B_R_W, and_11_out);
  nand nand_14 (nand_14_out, and_11_out, nB_R_W, \BΦ2 );
  assign nEOI = ~nEOI_OUT ? 1'b0 : 1'bz;  // DriverInvSel driverinvsel_1
  nand nand_15 (nand_15_out, nand_12_out, nand_9_out);
  _4116 _4116_7 (
    .A0(_74153simplified_4__1y[0]), .A1(_74153simplified_4__1y[1]), .A2(_74153simplified_4__1y[2]),
    .A3(_74153simplified_4__1y[3]), .A4(_74153simplified_4__1y[4]), .A5(_74153simplified_4__1y[5]),
    .A6(_74153simplified_4__1y[6]), .nWE(RAM_R_W), .nRAS(nRAS0), .nCAS(nCAS1), .DI(_4116_8_do),
    .DO(_4116_7_do));
  _4116 _4116_8 (
    .A0(_74153simplified_4__1y[0]), .A1(_74153simplified_4__1y[1]), .A2(_74153simplified_4__1y[2]),
    .A3(_74153simplified_4__1y[3]), .A4(_74153simplified_4__1y[4]), .A5(_74153simplified_4__1y[5]),
    .A6(_74153simplified_4__1y[6]), .nWE(RAM_R_W), .nRAS(nRAS0), .nCAS(nCAS0), .DI(_4116_8_do),
    .DO(_4116_8_do));
  _74LS244 _74ls244_5 (
    ._1Y1(BD4), ._2A1(BD4), ._1Y2(BD5), ._2A2(BD5), ._1Y3(BD6), ._2A3(BD6), ._1Y4(BD7), ._2A4(BD7),
    ._1nG(nand_11_out), ._1A1(_4116_8_do), ._2Y1(_4116_8_do), ._1A2(_4116_6_do), ._2Y2(_4116_6_do),
    ._1A3(_4116_4_do), ._2Y3(_4116_4_do), ._1A4(_4116_2_do), ._2Y4(_4116_2_do), ._2nG(B_R_W));
  and and_12 (and_12_out, nand_15_out, HORZ_DISP_OFF);
  _4116 _4116_9 (
    .A0(_74153simplified_4__1y[0]), .A1(_74153simplified_4__1y[1]), .A2(_74153simplified_4__1y[2]),
    .A3(_74153simplified_4__1y[3]), .A4(_74153simplified_4__1y[4]), .A5(_74153simplified_4__1y[5]),
    .A6(_74153simplified_4__1y[6]), .nWE(RAM_R_W), .nRAS(nRAS0), .nCAS(nCAS1), .DI(_4116_10_do),
    .DO(_4116_9_do));
  _4116 _4116_10 (
    .A0(_74153simplified_4__1y[0]), .A1(_74153simplified_4__1y[1]), .A2(_74153simplified_4__1y[2]),
    .A3(_74153simplified_4__1y[3]), .A4(_74153simplified_4__1y[4]), .A5(_74153simplified_4__1y[5]),
    .A6(_74153simplified_4__1y[6]), .nWE(RAM_R_W), .nRAS(nRAS0), .nCAS(nCAS0), .DI(_4116_10_do),
    .DO(_4116_10_do));
  PullUp pullup_9 (.out(pullup_9_out));
  _74LS157 _74ls157_2 (
    ._1A(pullup_9_out), ._1B(pullup_9_out), ._2A(pullup_9_out), ._2B(nand_14_out), ._3A(nRA1), ._3B(BA[0]),
    ._4A(_74ls107_7_q), ._4B(BA[1]), .S(CLK1), .G(1'b0), .Y2(TV_RAM_R_W), .Y3(SA[0]), .Y4(SA[1]));  // open: Y1
  _74LS157 _74ls157_3 (
    ._1A(_74177_1_qa), ._1B(BA[2]), ._2A(_74177_1_qb), ._2B(BA[3]), ._3A(_74177_1_qc), ._3B(BA[4]),
    ._4A(_74177_1_qd), ._4B(BA[5]), .S(CLK1), .G(1'b0), .Y1(SA[2]), .Y2(SA[3]), .Y3(SA[4]), .Y4(SA[5]));
  _74LS157 _74ls157_4 (
    ._1A(_74177_2_qa), ._1B(BA[6]), ._2A(_74177_2_qb), ._2B(BA[7]), ._3A(_74177_2_qc), ._3B(BA[8]),
    ._4A(_74177_2_qd), ._4B(BA[9]), .S(CLK1), .G(1'b0), .Y1(SA[6]), .Y2(SA[7]), .Y3(SA[8]), .Y4(SA[9]));
  PullUp pullup_10 (.out(pullup_10_out));
  _74S74 _74s74_4 (.Q(NEXT), .nQ(nNEXT), .nP(pullup_10_out), .D(and_12_out), .CK(VIDEO_LATCH), .nCL(\BΦ2H ));
  _4116 _4116_11 (
    .A0(_74153simplified_4__1y[0]), .A1(_74153simplified_4__1y[1]), .A2(_74153simplified_4__1y[2]),
    .A3(_74153simplified_4__1y[3]), .A4(_74153simplified_4__1y[4]), .A5(_74153simplified_4__1y[5]),
    .A6(_74153simplified_4__1y[6]), .nWE(RAM_R_W), .nRAS(nRAS0), .nCAS(nCAS1), .DI(_4116_12_do),
    .DO(_4116_11_do));
  _4116 _4116_12 (
    .A0(_74153simplified_4__1y[0]), .A1(_74153simplified_4__1y[1]), .A2(_74153simplified_4__1y[2]),
    .A3(_74153simplified_4__1y[3]), .A4(_74153simplified_4__1y[4]), .A5(_74153simplified_4__1y[5]),
    .A6(_74153simplified_4__1y[6]), .nWE(RAM_R_W), .nRAS(nRAS0), .nCAS(nCAS0), .DI(_4116_12_do),
    .DO(_4116_12_do));
  _4116 _4116_13 (
    .A0(_74153simplified_4__1y[0]), .A1(_74153simplified_4__1y[1]), .A2(_74153simplified_4__1y[2]),
    .A3(_74153simplified_4__1y[3]), .A4(_74153simplified_4__1y[4]), .A5(_74153simplified_4__1y[5]),
    .A6(_74153simplified_4__1y[6]), .nWE(RAM_R_W), .nRAS(nRAS0), .nCAS(nCAS1), .DI(_4116_14_do),
    .DO(_4116_13_do));
  _4116 _4116_14 (
    .A0(_74153simplified_4__1y[0]), .A1(_74153simplified_4__1y[1]), .A2(_74153simplified_4__1y[2]),
    .A3(_74153simplified_4__1y[3]), .A4(_74153simplified_4__1y[4]), .A5(_74153simplified_4__1y[5]),
    .A6(_74153simplified_4__1y[6]), .nWE(RAM_R_W), .nRAS(nRAS0), .nCAS(nCAS0), .DI(_4116_14_do),
    .DO(_4116_14_do));
  _74LS244 _74ls244_6 (
    ._1Y1(BD0), ._2A1(BD0), ._1Y2(BD1), ._2A2(BD1), ._1Y3(BD2), ._2A3(BD2), ._1Y4(BD3), ._2A4(BD3),
    ._1nG(nand_11_out), ._1A1(_74ls244_6__2y1), ._2Y1(_74ls244_6__2y1), ._1A2(_4116_14_do),
    ._2Y2(_4116_14_do), ._1A3(_4116_12_do), ._2Y3(_4116_12_do), ._1A4(_4116_10_do), ._2Y4(_4116_10_do),
    ._2nG(B_R_W));
  _4116 _4116_15 (
    .A0(_74153simplified_4__1y[0]), .A1(_74153simplified_4__1y[1]), .A2(_74153simplified_4__1y[2]),
    .A3(_74153simplified_4__1y[3]), .A4(_74153simplified_4__1y[4]), .A5(_74153simplified_4__1y[5]),
    .A6(_74153simplified_4__1y[6]), .nWE(RAM_R_W), .nRAS(nRAS0), .nCAS(nCAS1), .DI(_74ls244_6__2y1),
    .DO(_4116_15_do));
  _4116 _4116_16 (
    .A0(_74153simplified_4__1y[0]), .A1(_74153simplified_4__1y[1]), .A2(_74153simplified_4__1y[2]),
    .A3(_74153simplified_4__1y[3]), .A4(_74153simplified_4__1y[4]), .A5(_74153simplified_4__1y[5]),
    .A6(_74153simplified_4__1y[6]), .nWE(RAM_R_W), .nRAS(nRAS0), .nCAS(nCAS0), .DI(_74ls244_6__2y1),
    .DO(_74ls244_6__2y1));
  Button #(.activeLow("true")) button_1 (.out(RDY));
  Comparator #(.Bits(16)) comparator_1 (.a(BA), .b(16'he813), .eq(comparator_1_eq));  // open: gt, lt
  // NotConnected on notconnected_7_out
  _74LS93 _74ls93_2 (
    .CKA(notconnected_7_out), .CKB(HORZ_DISP_ON), .R1(NEXT), .R2(NEXT), .QB(RA7), .QC(_74ls93_2_qc), .QD(RA9));  // open: QA
  not not_20 (not_20_out, nIRQ);
  Break #(.Cycles(90000000)) break_1 (.brk(comparator_1_eq));
  _6522 _6522_1 (
    .D0(D[0]), .D1(D[1]), .D2(D[2]), .D3(D[3]), .D4(D[4]), .D5(D[5]), .D6(D[6]), .D7(D[7]), .CS1(CS1),
    .nCS2(nI_O), .RS0(BA[0]), .RS1(BA[1]), .RS2(BA[2]), .RS3(BA[3]), .R_W(r_w), .\Φ2 (\BΦ2 ), .nRESET(nRES),
    .nIRQ(nIRQ), .CA1(CA1), .CA2(GRAPHIC), .PA0(PA0), .PA1(PA1), .PA2(PA2), .PA3(PA3), .PA4(PA4), .PA5(PA5),
    .PA6(PA6), .PA7(PA7), .PB0(_6522_1_pb0), .PB1(_6522_1_pb1), .PB2(_6522_1_pb2), .PB3(CASS_WRITE),
    .PB4(_6522_1_pb4), .PB5(VIDEO_ON), .PB6(_6522_1_pb6), .PB7(_6522_1_pb7), .CB1(_2_CASS_READ),
    .CB2(_6522_1_cb2));
  _6520 _6520_2 (
    .D0(D[0]), .D1(D[1]), .D2(D[2]), .D3(D[3]), .D4(D[4]), .D5(D[5]), .D6(D[6]), .D7(D[7]), .CS1(BA[4]),
    .nCS2(nI_O), .CS0(X8XX), .RS0(BA[0]), .RS1(BA[1]), .R_W(r_w), .\Φ2 (\BΦ2 ), .nRESET(nRES), .nIRQA(nIRQ),
    .CA1(_1_CASS_READ), .CA2(nEOI_OUT), .PA0(_6520_2_pa0), .PA1(_6520_2_pa1), .PA2(_6520_2_pa2),
    .PA3(_6520_2_pa3), .PA4(_1_CASS_SWITCH), .PA5(_2_CASS_SWITCH), .PA6(nEOI), .PA7(DIAG), .PB0(_6520_2_pb0),
    .PB1(_6520_2_pb1), .PB2(_6520_2_pb2), .PB3(_6520_2_pb3), .PB4(_6520_2_pb4), .PB5(_6520_2_pb5),
    .PB6(_6520_2_pb6), .PB7(_6520_2_pb7), .CB1(VIDEO_ON), .CB2(_6520_2_cb2), .nIRQB(nIRQ));
  DipSwitch dipswitch_1 (.out(DIAG_CLIP));
  Break #(.Cycles(90000000)) break_2 (.brk(not_20_out));
  nand nand_16 (nRELOAD, HORZ_DISP_ON, RA7, _74ls93_2_qc, RA9);
  Counter #(.Bits(32)) counter_1 (.en(1'b1), .C(\BΦ2 ), .clr(1'b0), .out(cycle));  // open: ovf
  _6316_ROM _6316_rom_1 (
    .A0(RA7), .A1(_74ls93_2_qc), .A2(RA9), .A3(_74ls373_2_q0[0]), .A4(_74ls373_2_q0[1]),
    .A5(_74ls373_2_q0[2]), .A6(_74ls373_2_q0[3]), .A7(_74ls373_2_q0[4]), .A8(_74ls373_2_q0[5]),
    .A9(_74ls373_2_q0[6]), .A10(GRAPHIC), .nCS1(1'b0), .nCS2(1'b0), .CS3(nINIT), .D0(_6316_rom_1_d0),
    .D1(_6316_rom_1_d1), .D2(_6316_rom_1_d2), .D3(_6316_rom_1_d3), .D4(_6316_rom_1_d4), .D5(_6316_rom_1_d5),
    .D6(_6316_rom_1_d6), .D7(_6316_rom_1_d7));
  _74LS373 _74ls373_2 (
    .D0(SD0), .D1(SD1), .D2(SD2), .D3(SD3), .D4(SD4), .D5(SD5), .D6(SD6), .D7(SD7), .G(VIDEO_LATCH),
    .nOC(1'b0), .Q0(_74ls373_2_q0[0]), .Q1(_74ls373_2_q0[1]), .Q2(_74ls373_2_q0[2]), .Q3(_74ls373_2_q0[3]),
    .Q4(_74ls373_2_q0[4]), .Q5(_74ls373_2_q0[5]), .Q6(_74ls373_2_q0[6]), .Q7(_74ls373_2_q7));
  _6114 _6114_1 (
    .R_nW(TV_RAM_R_W), .nCE(1'b0), .A0(SA[0]), .A1(SA[1]), .A2(SA[2]), .A3(SA[3]), .A4(SA[4]), .A5(SA[5]),
    .A6(SA[6]), .A7(SA[7]), .A8(SA[8]), .A9(SA[9]), .D0(SD0), .D1(SD1), .D2(SD2), .D3(SD3));
  _74LS145 _74LS145 (
    .A(_6520_2_pa0), .B(_6520_2_pa1), .C(_6520_2_pa2), .D(_6520_2_pa3), ._0(_74LS145__0), ._1(_74LS145__1),
    ._2(_74LS145__2), ._3(_74LS145__3), ._4(_74LS145__4), ._5(_74LS145__5), ._6(_74LS145__6),
    ._7(_74LS145__7), ._8(_74LS145__8), ._9(_74LS145__9));
  _74S74 _74s74_5 (.Q(_74s74_5_q), .nQ(_74s74_5_nq), .nP(pullup_11_out), .D(_74ls373_2_q7), .CK(LOAD_SR), .nCL(nINIT));
  not not_21 (_2_CASS_MOTOR, _6522_1_pb4);
  not not_22 (_1_CASS_MOTOR, _6520_2_cb2);
  PullUp pullup_11 (.out(pullup_11_out));
  _74LS165 _74ls165_1 (
    .SH_nLD(nLOAD_SR), .CLK(CLK8), .CLKINH(1'b0), .SER(_6316_rom_1_d7), .A(_6316_rom_1_d0),
    .B(_6316_rom_1_d1), .C(_6316_rom_1_d2), .D(_6316_rom_1_d3), .E(_6316_rom_1_d4), .F(_6316_rom_1_d5),
    .G(_6316_rom_1_d6), .H(_6316_rom_1_d7), .QH(_74ls165_1_qh), .nQH(_74ls165_1_nqh));
  _6114 _6114_2 (
    .R_nW(TV_RAM_R_W), .nCE(1'b0), .A0(SA[0]), .A1(SA[1]), .A2(SA[2]), .A3(SA[3]), .A4(SA[4]), .A5(SA[5]),
    .A6(SA[6]), .A7(SA[7]), .A8(SA[8]), .A9(SA[9]), .D0(SD4), .D1(SD5), .D2(SD6), .D3(SD7));
  nand nand_17 (nand_17_out, _74s74_5_q, _74ls165_1_qh);
  nand nand_18 (nand_18_out, _74s74_5_nq, _74ls165_1_nqh);
  DIAG_Keyboard_Dongle diag_keyboard_dongle_1 (
    ._1(_74LS145__0), ._2(_74LS145__1), ._3(_74LS145__2), ._4(_74LS145__3), ._5(_74LS145__4),
    ._6(_74LS145__5), ._7(_74LS145__6), ._8(_74LS145__7), ._9(_74LS145__8), ._10(_74LS145__9),
    .A(_6520_2_pb0), .B(_6520_2_pb1), .C(_6520_2_pb2), .D(_6520_2_pb3), .E(_6520_2_pb4), .F(_6520_2_pb5),
    .H(_6520_2_pb6), .J(_6520_2_pb7), .CLK(VIDEO_ON));
  DIAG_Userport_Dongle diag_userport_dongle_1 (
    .CA1__B(CA1), .PA0__C(PA0), .PA1__D(PA1), .PA2__E(PA2), .PA3__F(PA3), .PA4__H(PA4), .PA5__J(PA5),
    .PA6__K(PA6), .PA7__L(PA7), .VIDEO__2(VIDEO), .nSRQ_IN__3(nSRQ_IN), .nEOI_IN__4(nEOI), .DIAG__5(DIAG),
    ._2_CASS_READ__6(_2_CASS_READ), .CASS_WRITE__7(CASS_WRITE), ._1_CASS_READ__8(_1_CASS_READ),
    .VERT_DRIVE__9(VERT_DRIVE), .HORZ_DRIVE__10(HORZ_DRIVE), .GND__11(1'b0));
  and and_13 (and_13_out, nand_17_out, nand_18_out);
  _74LS244 _74ls244_7 (
    ._1Y1(BD0), ._2A1(BD0), ._1Y2(BD1), ._2A2(BD1), ._1Y3(BD2), ._2A3(BD2), ._1Y4(BD3), ._2A4(BD3),
    ._1nG(nTV_READ), ._1A1(SD0), ._2Y1(SD0), ._1A2(SD1), ._2Y2(SD1), ._1A3(SD2), ._2Y3(SD2), ._1A4(SD3),
    ._2Y4(SD3), ._2nG(TV_RAM_R_W));
  _74LS244 _74ls244_8 (
    ._1Y1(BD4), ._2A1(BD4), ._1Y2(BD5), ._2A2(BD5), ._1Y3(BD6), ._2A3(BD6), ._1Y4(BD7), ._2A4(BD7),
    ._1nG(nTV_READ), ._1A1(SD4), ._2Y1(SD4), ._1A2(SD5), ._2Y2(SD5), ._1A3(SD6), ._2Y3(SD6), ._1A4(SD7),
    ._2Y4(SD7), ._2nG(TV_RAM_R_W));
  nand nand_19 (VIDEO, and_13_out, 1'b1, VIDEO_ON, HORZ_DISP_ON);
  DipSwitch #(.dipDefault("true")) dipswitch_2 (.out(_2_CASS_SWITCH));
  DipSwitch #(.dipDefault("true")) dipswitch_3 (.out(_1_CASS_SWITCH));
  CRT_green crt_green_1 (.VIDEO(VIDEO), .CLK8(CLK8), .HOR_DRIVE_IN(HORZ_DRIVE), .VER_DRIVE_IN(VERT_DRIVE));

  // Other names for the same wires on the sheet: nEOI_IN = nEOI

  // Notes on the sheet:
  //   _16MHz: Hz: 2147483647
  //   1 - CPU
  //   4 - ROMS
  //   6 - MASTER CLOCK
  //   N
  //   P
  //   contents of F000 (hex, n*v repeats v):
  //   54,4f,4f,20,4d,41,4e,59,20,46,49,4c,45,d3,46,49,4c,45,20,4f,50
  //   ,45,ce,46,49,4c,45,20,4e,4f,54,20,4f,50,45,ce,46,49,4c,45,20,4e
  //   ,4f,54,20,46,4f,55,4e,c4,d,53,45,41,52,43,48,49,4e,47,a0,46,4f
  //   ,52,a0,d,50,52,45,53,53,20,50,4c,41,59,a0,26,20,52,45,43,4f,52
  //   ,44,a0,4f,4e,20,54,41,50,45,20,a3,d,4c,4f,41,c4,d,57,52,49,54
  //   ,49,4e,47,a0,d,56,45,52,49,46,d9,44,45,56,49,43,45,20,4e,4f,54
  //   ,20,50,52,45,53,45,4e,d4,4e,4f,54,20,49,4e,50,55,54,20,46,49,4c
  //   ,c5,4e,4f,54,20,4f,55,54,50,55,54,20,46,49,4c,c5,d,46,4f,55,4e
  //   ,44,a0,d,4f,4b,8d,d,52,45,41,44,59,2e,8d,a9,40,d0,2,a9,20,48,ad
  //   ,40,e8,9,2,8d,40,e8,a9,3c,8d,21,e8,24,a0,f0,11,a9,34,8d,11,e8
  //   ,20,ee,f0,a9,0,85,a0,a9,3c,8d,11,e8,68,5,d4,85,a5,ad,40,e8,10
  //   ,fb,29,fb,8d,40,e8,a9,3c,8d,23,e8,ad,40,e8,29,41,c9,41,f0,41,a5,a5
  //   ,49,ff,8d,22,e8,2c,40,e8,50,fb,a9,34,8d,23,e8,a9,ff,8d,45,e8,ad
  //   ,40,e8,2c,4d,e8,70,1c,4a,90,f5,a9,3c,8d,23,e8,a9,ff,8d,22,e8,60
  //   ,85,a5,20,ee,f0,ad,40,e8,9,4,8d,40,e8,60,a9,1,20,7f,fb,d0,e0,a9
  //   ,80,30,f7,a9,2,20,7f,fb,ad,40,e8,29,fd,8d,40,e8,a9,34,8d,21,e8
  //   ,a9,d,60,b9,0,f0,8,29,7f,20,d8,e3,c8,28,10,f3,60,85,a5,20,ee,f0
  //   ,20,46,f1,4c,2d,f1,24,a0,30,4,c6,a0,d0,5,48,20,ee,f0,68,85,a5
  //   ,60,a9,5f,d0,2,a9,3f,ea,ea,20,bc,f0,d0,a1,a9,34,8d,21,e8,ad,40
  //   ,e8,9,2,8d,40,e8,a9,ff,8d,45,e8,2c,4d,e8,70,9e,2c,40,e8,30,f6
  //   ,ad,40,e8,29,fd,8d,40,e8,2c,10,e8,70,5,a9,40,20,7f,fb,ad,20,e8
  //   ,49,ff,48,a9,3c,8d,21,e8,2c,40,e8,10,fb,a9,34,8d,21,e8,68,60,a9
  //   ,0,85,96,a5,af,d0,17,a5,9e,f0,51,78,4c,85,e2,a5,af,d0,b,a5,c6
  //   ,85,a4,a5,d8,85,a3,4c,f4,e2,c9,3,d0,9,85,ac,a5,d5,85,a1,4c,f4
  //   ,e2,b0,29,86,ad,20,15,f2,48,20,15,f2,d0,5,a9,40,20,7f,fb,d6,ba
  //   ,a6,ad,68,60,20,6,f8,d0,b,20,55,f8,a6,d4,a9,0,95,ba,f0,f0,b1,d6
  //   ,60,a5,96,f0,3,a9,d,60,4c,8c,f1,48,a5,b0,c9,3,d0,4,68,4c,d8,e3
  //   ,30,4,68,4c,6f,f1,68,85,b4,c9,a,f0,e4,48,8a,48,98,48,20,6,f8,d0
  //   ,10,20,86,f8,a6,d4,a9,1,95,ba,a0,0,a9,2,91,d6,c8,a5,b4,91,d6,68
  //   ,a8,68,aa,68,60,a9,0,85,ae,a5,b0,c9,4,90,3,20,83,f1,a5,af,c9,4
  //   ,90,3,20,7f,f1,a9,3,85,b0,a9,0,85,af,60,a6,ae,ca,30,16,dd,51,2
  //   ,f0,11,d0,f6,bd,51,2,85,d2,bd,5b,2,85,d4,bd,65,2,85,d3,60,20,ce
  //   ,f4,a5,d2,20,8d,f2,d0,4d,20,99,f2,8a,48,a5,d4,f0,28,c9,3,f0,24
  //   ,b0,1f,a5,d3,29,f,f0,1c,20,56,f6,a9,0,20,44,f2,20,86,f8,a5,d3
  //   ,c9,62,d0,b,a9,5,20,da,f5,4c,e4,f2,20,f0,f6,68,aa,c6,ae,e4,ae
  //   ,f0,14,a4,ae,b9,51,2,9d,51,2,b9,5b,2,9d,5b,2,b9,65,2,9d,65,2,60
  //   ,a5,9b,c9,ef,d0,7,8,20,72,f2,85,9e,28,60,20,1,f3,4c,3f,c7,20,1d
  //   ,f3,d0,f4,4c,56,f1,a5,78,c9,2,60,a5,d4,d0,3,4c,3,ce,c9,3,f0,f9
  //   ,90,66,a9,60,85,d3,a4,d1,d0,3,4c,3,ce,20,a,f4,20,66,f4,20,b6,f0
  //   ,a5,d3,20,28,f1,20,8c,f1,85,fb,20,8c,f1,85,fc,20,2e,f4,a9,fd,25
  //   ,96,85,96,20,f,f3,20,8c,f1,aa,a5,96,4a,4a,b0,ed,8a,a4,9d,f0,b
  //   ,88,d1,fb,f0,8,a2,10,86,96,d0,2,91,fb,e6,fb,d0,2,e6,fc,24,96,50
  //   ,d1,ea,ea,ea,a5,fb,85,c9,a5,fc,85,ca,20,7f,f1,4c,f0,f6,20,56,f6
  //   ,20,12,f8,20,a,f4,a5,d1,f0,8,20,94,f4,d0,8,4c,6e,f5,20,a6,f5,f0
  //   ,f8,e0,1,d0,eb,a5,96,29,10,d0,74,20,3c,f6,20,2e,f4,4c,5e,f8,a9
  //   ,0,85,9d,20,3e,f4,20,8d,f6,a9,ff,c5,9b,d0,fc,c5,9b,d0,f8,20,22
  //   ,f3,a5,9d,d0,50,20,e6,f8,a5,96,29,10,f0,9,a0,0,84,9e,a0,60,4c
  //   ,70,f5,a0,ae,20,15,f3,20,1d,f3,d0,b,a5,ca,85,2b,a5,c9,85,2a,4c
  //   ,39,c4,20,a7,c5,4c,90,c5,20,1d,f3,d0,1e,a0,32,20,56,f1,a5,d1,f0
  //   ,15,a0,3d,20,56,f1,a4,d1,f0,c,a0,0,b1,da,20,d2,ff,c8,c4,d1,d0
  //   ,f6,60,a0,5f,a5,9d,f0,2,a0,6d,20,15,f3,a0,39,4c,15,f3,a2,0,86
  //   ,96,86,d1,86,d3,e8,86,d4,20,e,f5,20,fd,f4,20,e,f5,20,60,f4,86
  //   ,d4,20,e,f5,20,60,f4,86,d3,60,20,16,f5,4c,78,d6,a5,d3,30,f5,a4
  //   ,d1,f0,f1,20,ba,f0,a5,d3,9,f0,20,28,f1,a5,96,10,5,a0,74,4c,70
  //   ,f5,a5,d1,f0,c,a0,0,b1,da,20,6f,f1,c8,c4,d1,d0,f6,4c,83,f1,20
  //   ,a6,f5,f0,1d,a0,5,84,b5,a0,0,84,b4,c4,d1,f0,10,b1,da,a4,b5,d1
  //   ,d6,d0,e7,e6,b4,e6,b5,a4,b4,d0,ec,98,60,a9,1,85,9d,20,c6,f3,a5
  //   ,96,29,10,f0,5,a0,6e,4c,70,f5,a0,aa,4c,56,f1,a2,0,86,d3,86,96
  //   ,86,d1,e8,86,d4,20,19,f5,20,78,d6,86,d2,20,e,f5,20,60,f4,86,d4
  //   ,e0,3,90,2,c6,d3,20,e,f5,20,60,f4,86,d3,20,e,f5,20,16,f5,20,9f
  //   ,cc,20,7d,d5,85,d1,a5,1f,85,da,a5,20,85,db,60,20,76,0,d0,2,68,68
  //   ,60,20,f8,cd,20,76,0,d0,f7,4c,3,ce,20,ce,f4,a5,d2,f0,f6,a0,e,20
  //   ,8d,f2,f0,41,a6,ae,a0,0,84,96,e0,a,f0,37,e6,ae,a5,d2,9d,51,2,a5
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  //   contents of E000 (hex, n*v repeats v):
  //   63,48,10,d,20,2c,d7,a5,63,30,9,a5,c,49,ff,85,c,20,a1,de,a9,5e
  //   ,a0,e0,20,73,d7,68,10,3,20,a1,de,a9,63,a0,e0,4c,2d,df,20,d6,da
  //   ,a9,0,85,c,20,df,df,a2,4b,a0,0,20,d5,df,a9,54,a0,0,20,ae,da,a9
  //   ,0,85,63,a5,c,20,50,e0,a9,4b,a0,0,4c,1b,da,48,4c,11,e0,81,49,f
  //   ,da,a2,83,49,f,da,a2,7f,4*0,5,84,e6,1a,2d,1b,86,28,7,fb,f8,87
  //   ,99,68,89,1,87,23,35,df,e1,86,a5,5d,e7,28,83,49,f,da,a2,a1,54
  //   ,46,8f,13,8f,52,43,89,cd,a5,63,48,10,3,20,a1,de,a5,5e,48,c9,81
  //   ,90,7,a9,c8,a0,d8,20,1b,da,a9,bc,a0,e0,20,2d,df,68,c9,81,90,7
  //   ,a9,54,a0,e0,20,33,d7,68,10,3,4c,a1,de,60,b,76,b3,83,bd,d3,79
  //   ,1e,f4,a6,f5,7b,83,fc,b0,10,7c,c,1f,67,ca,7c,de,53,cb,c1,7d,14
  //   ,64,70,4c,7d,b7,ea,51,7a,7d,63,30,88,7e,7e,92,44,99,3a,7e,4c,cc
  //   ,91,c7,7f,aa,aa,aa,13,81,4*0,e6,77,d0,2,e6,78,ad,60,ea,c9,3a,b0
  //   ,a,c9,20,f0,ef,38,e9,30,38,e9,d0,60,80,4f,c7,52,58,a2,fb,9a,a9
  //   ,4c,85,51,85,0,a9,23,a0,d1,85,1,84,2,a9,28,85,f,a9,1e,85,10,a2
  //   ,1c,bd,f8,e0,95,6f,ca,d0,f8,a9,3,85,50,8a,85,65,85,e,85,15,48
  //   ,85,d,e8,8e,fd,1,8e,fc,1,a2,16,86,13,a0,4,85,28,84,29,85,11,84
  //   ,12,a8,e6,11,d0,4,e6,12,30,f,a9,55,91,11,d1,11,d0,7,a,91,11,d1
  //   ,11,f0,e9,a5,11,a4,12,85,34,84,35,85,30,84,31,a2,0,a0,4,86,28
  //   ,84,29,a0,0,98,91,28,e6,28,a5,28,a4,29,20,28,c3,a9,c4,a0,e1,20
  //   ,1c,ca,a5,34,38,e5,28,aa,a5,35,e5,29,20,d9,dc,a9,b7,a0,e1,20,1c
  //   ,ca,20,5d,c5,4c,89,c3,20,42,59,54,45,53,20,46,52,45,45,d,0,23,23,23
  //   ,20,43,4f,4d,4d,4f,44,4f,52,45,20,42,41,53,49,43,20,23,23,23,d,d
  //   ,0,a9,7f,8d,4e,e8,a2,6d,a9,0,95,8d,ca,10,fb,a9,2e,85,90,a9,e6
  //   ,85,91,a9,3,85,b0,a9,f,8d,10,e8,a,8d,40,e8,8d,42,e8,8e,22,e8,8e
  //   ,45,e8,a9,3d,8d,13,e8,2c,12,e8,a9,3c,8d,21,e8,8d,23,e8,8d,11,e8
  //   ,8e,22,e8,a9,c,8d,4c,e8,85,a8,85,a7,a0,83,a2,18,94,e0,e0,14,f0
  //   ,8,e0,d,f0,4,e0,7,d0,1,88,ca,10,ee,84,c5,e8,86,9f,86,c4,a9,20
  //   ,9d,0,80,9d,0,81,9d,0,82,9d,0,83,ca,d0,f1,a0,0,84,c6,84,d8,a6
  //   ,d8,b5,e0,9,80,85,c5,bd,48,e7,85,c4,a9,27,85,d5,e0,18,f0,8,b5
  //   ,e1,30,4,a9,4f,85,d5,a5,c6,c9,28,90,4,e9,28,85,c6,60,ac,6f,2,a2
  //   ,0,bd,70,2,9d,6f,2,e8,e4,9e,d0,f5,c6,9e,98,58,60,20,d8,e3,a5,9e
  //   ,85,a7,f0,fa,78,a5,aa,f0,9,a5,a9,a0,0,84,aa,20,ea,e6,20,85,e2
  //   ,c9,83,d0,10,78,a2,9,86,9e,bd,60,e7,9d,6e,2,ca,d0,f7,f0,d5,c9
  //   ,d,d0,ce,a4,d5,84,ac,b1,c4,c9,20,d0,3,88,d0,f7,c8,84,a1,a0,0,84
  //   ,c6,84,cd,a5,a3,30,16,c5,d8,d0,12,a5,a4,85,c6,c5,a1,90,a,b0,2b
  //   ,98,48,8a,48,a5,ac,f0,a1,a4,c6,b1,c4,85,d9,29,3f,6,d9,24,d9,10
  //   ,2,9,80,90,4,a6,cd,d0,4,70,2,9,40,e6,c6,20,3f,e3,c4,a1,d0,11,a9
  //   ,0,85,ac,a9,d,a6,b0,e0,3,f0,3,20,d8,e3,a9,d,85,d9,68,aa,68,a8
  //   ,a5,d9,c9,de,d0,2,a9,ff,60,c9,22,d0,8,a5,cd,49,1,85,cd,a9,22,60
  //   ,9,40,a6,9f,f0,2,9,80,a6,dc,f0,2,c6,dc,20,ea,e6,e6,c6,a4,d5,c4
  //   ,c6,b0,19,a6,d8,c0,4f,d0,c,20,8b,e3,20,19,e5,a9,0,85,c6,f0,7,e0
  //   ,18,d0,1b,20,9c,e3,68,a8,a5,dc,f0,2,46,cd,68,aa,68,58,60,e0,17
  //   ,b0,6,b5,e2,9,80,95,e2,60,20,a3,e3,4c,7e,e3,20,3f,e5,c6,d8,a6
  //   ,d8,16,e1,56,e1,20,8b,e3,a5,c6,48,20,5d,e2,68,85,c6,60,a0,27,a6
  //   ,d8,d0,6,86,c6,68,68,d0,be,b5,df,30,5,ca,b5,df,a0,4f,ca,86,d8
  //   ,85,c5,bd,48,e7,85,c4,84,c6,84,d5,60,48,85,d9,8a,48,98,48,a9,0
  //   ,85,ac,a4,c6,a5,d9,10,3,4c,7a,e4,c9,d,d0,3,4c,2f,e5,c9,20,90,8
  //   ,29,3f,20,3f,e3,4c,4e,e3,a6,dc,f0,3,4c,52,e3,c9,14,d0,1c,88,84
  //   ,c6,10,6,20,b4,e3,4c,20,e4,c8,b1,c4,88,91,c4,c8,c4,d5,d0,f5,a9
  //   ,20,91,c4,d0,3c,a6,cd,f0,3,4c,52,e3,c9,12,d0,2,85,9f,c9,13,d0
  //   ,3,20,57,e2,c9,1d,d0,12,c8,84,c6,88,c4,d5,90,7,20,19,e5,a0,0,84
  //   ,c6,4c,7e,e3,c9,11,d0,e,18,98,69,28,a8,c5,d5,90,ee,f0,ec,20,19
  //   ,e5,4c,7e,e3,e8,85,d8,98,e9,28,85,c6,e6,d8,ad,48,e7,85,c4,a5,e0
  //   ,85,c5,d0,e8,29,7f,c9,7f,d0,2,a9,5e,c9,20,90,3,4c,4c,e3,c9,d,d0
  //   ,3,4c,2f,e5,a6,cd,d0,30,c9,14,d0,28,a4,d5,b1,c4,c9,20,d0,4,c4
  //   ,c6,d0,7,c0,4f,f0,ba,20,ba,e5,a4,d5,88,b1,c4,c8,91,c4,88,c4,c6
  //   ,d0,f5,a9,20,91,c4,e6,dc,d0,56,a6,dc,f0,5,9,40,4c,52,e3,c9,11
  //   ,d0,2b,a5,c6,c9,28,90,6,e9,28,85,c6,b0,3d,a6,d8,f0,39,b5,df,10
  //   ,7,c6,d8,20,5d,e2,90,2e,ca,ca,86,d8,20,5d,e2,a5,c6,18,69,28,85
  //   ,c6,d0,1e,c9,12,d0,4,a9,0,85,9f,c9,1d,d0,b,88,84,c6,10,d,20,b4
  //   ,e3,4c,7e,e3,c9,13,d0,3,20,29,e2,4c,7e,e3,38,46,a3,a6,d8,e8,e0
  //   ,19,d0,3,20,3f,e5,b5,e0,10,f4,86,d8,4c,5d,e2,a9,0,85,dc,85,9f
  //   ,85,cd,85,c6,20,19,e5,4c,7e,e3,78,a0,0,84,c4,a9,80,85,c8,85,c5
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  //   contents of D000 (hex, n*v repeats v):
  //   60,68,48,c9,11,d0,5,a9,1f,a0,de,60,a5,42,a4,43,c9,54,d0,b,c0,c9
  //   ,f0,ef,c0,49,d0,3,4c,3,ce,c9,53,d0,4,c0,54,f0,f5,a5,2c,a4,2d,85
  //   ,5c,84,5d,a5,2e,a4,2f,85,57,84,58,18,69,7,90,1,c8,85,55,84,56
  //   ,20,d8,c2,a5,55,a4,56,c8,85,2c,84,2d,a0,0,a5,42,91,5c,c8,a5,43
  //   ,91,5c,a9,0,c8,91,5c,c8,91,5c,c8,91,5c,c8,91,5c,c8,91,5c,a5,5c
  //   ,18,69,2,a4,5d,90,1,c8,85,44,84,45,60,a5,5,a,69,5,65,5c,a4,5d
  //   ,90,1,c8,85,55,84,56,60,90,80,0,0,20,70,0,20,9f,cc,20,8e,cc,a5
  //   ,63,30,d,a5,5e,c9,90,90,9,a9,89,a0,d0,20,67,db,d0,7a,4c,a7,db
  //   ,a5,6,5,8,48,a5,7,48,a0,0,98,48,a5,43,48,a5,42,48,20,8d,d0,68
  //   ,85,42,68,85,43,68,a8,ba,bd,2,1,48,bd,1,1,48,a5,61,9d,2,1,a5,62
  //   ,9d,1,1,c8,20,76,0,c9,2c,f0,d2,84,5,20,f2,cd,68,85,7,68,85,8,29
  //   ,7f,85,6,a6,2c,a5,2d,86,5c,85,5d,c5,2f,d0,4,e4,2e,f0,39,a0,0,b1
  //   ,5c,c8,c5,42,d0,6,a5,43,d1,5c,f0,16,c8,b1,5c,18,65,5c,aa,c8,b1
  //   ,5c,65,5d,90,d7,a2,6b,2c,a2,35,4c,57,c3,a2,78,a5,6,d0,f7,20,78
  //   ,d0,a5,5,a0,4,d1,5c,d0,e7,4c,c6,d1,20,78,d0,20,28,c3,a9,0,a8,85
  //   ,6f,a2,5,a5,42,91,5c,10,1,ca,c8,a5,43,91,5c,10,2,ca,ca,86,6e,a5
  //   ,5,c8,c8,c8,91,5c,a2,b,a9,0,24,6,50,8,68,18,69,1,aa,68,69,0,c8
  //   ,91,5c,c8,8a,91,5c,20,28,d2,86,6e,85,6f,a4,1f,c6,5,d0,dc,65,56
  //   ,b0,5d,85,56,a8,8a,65,55,90,3,c8,f0,52,20,28,c3,85,2e,84,2f,a9
  //   ,0,e6,6f,a4,6e,f0,5,88,91,55,d0,fb,c6,56,c6,6f,d0,f5,e6,56,38
  //   ,a5,2e,e5,5c,a0,2,91,5c,a5,2f,c8,e5,5d,91,5c,a5,6,d0,62,c8,b1
  //   ,5c,85,5,a9,0,85,6e,85,6f,c8,68,aa,85,61,68,85,62,d1,5c,90,e,d0
  //   ,6,c8,8a,d1,5c,90,7,4c,20,d1,4c,55,c3,c8,a5,6f,5,6e,18,f0,a,20
  //   ,28,d2,8a,65,61,aa,98,a4,1f,65,62,86,6e,c6,5,d0,ca,85,6f,a2,5
  //   ,a5,42,10,1,ca,a5,43,10,2,ca,ca,86,25,a9,0,20,31,d2,8a,65,55,85
  //   ,44,98,65,56,85,45,a8,a5,44,60,84,1f,b1,5c,85,25,88,b1,5c,85,26
  //   ,a9,10,85,5a,a2,0,a0,0,8a,a,aa,98,2a,a8,b0,a4,6,6e,26,6f,90,b
  //   ,18,8a,65,25,aa,98,65,26,a8,b0,93,c6,5a,d0,e3,60,a5,7,f0,3,20
  //   ,80,d5,20,0,d4,38,a5,30,e5,2e,a8,a5,31,e5,2f,a2,0,86,7,85,5f,84
  //   ,60,a2,90,4c,50,db,a4,c6,a9,0,f0,ed,a6,37,e8,d0,a2,a2,95,2c,a2
  //   ,e9,4c,57,c3,20,bb,d2,20,80,d2,20,f5,cd,a9,80,85,a,20,6d,cf,20
  //   ,8e,cc,20,f2,cd,a9,b2,20,fa,cd,48,a5,45,48,a5,44,48,a5,78,48,a5
  //   ,77,48,20,0,c8,4c,29,d3,a9,a5,20,fa,cd,9,80,85,a,20,74,cf,85,4b
  //   ,84,4c,4c,8e,cc,20,bb,d2,a5,4c,48,a5,4b,48,20,ec,cd,20,8e,cc,68
  //   ,85,4b,68,85,4c,a0,2,b1,4b,85,44,aa,c8,b1,4b,f0,99,85,45,c8,b1
  //   ,44,48,88,10,fa,a4,45,20,e0,da,a5,78,48,a5,77,48,b1,4b,85,77,c8
  //   ,b1,4b,85,78,a5,45,48,a5,44,48,20,8b,cc,68,85,4b,68,85,4c,20,76
  //   ,0,f0,3,4c,3,ce,68,85,77,68,85,78,a0,0,68,91,4b,68,c8,91,4b,68
  //   ,c8,91,4b,68,c8,91,4b,68,c8,91,4b,60,20,8e,cc,a0,0,20,eb,dc,68,68
  //   ,a9,ff,a0,0,f0,12,a6,61,a4,62,86,4d,84,4e,20,ce,d3,86,5f,84,60
  //   ,85,5e,60,a2,22,86,3,86,4,85,6c,84,6d,85,5f,84,60,a0,ff,c8,b1
  //   ,6c,f0,c,c5,3,f0,4,c5,4,d0,f3,c9,22,f0,1,18,84,5e,98,65,6c,85
  //   ,6e,a6,6d,90,1,e8,86,6f,a5,6d,f0,4,c9,2,d0,b,98,20,4f,d3,a6,6c
  //   ,a4,6d,20,62,d5,a6,13,e0,1f,d0,5,a2,c8,4c,57,c3,a5,5e,95,0,a5
  //   ,5f,95,1,a5,60,95,2,a0,0,86,61,84,62,84,6d,88,84,7,86,14,e8,e8,e8
  //   ,86,13,60,46,9,48,49,ff,38,65,30,a4,31,b0,1,88,c4,2f,90,11,d0
  //   ,4,c5,2e,90,b,85,30,84,31,85,32,84,33,aa,68,60,a2,4d,a5,9,30,b6
  //   ,20,0,d4,a9,80,85,9,68,d0,d0,a6,34,a5,35,86,30,85,31,a0,0,84,4c
  //   ,84,4b,a5,2e,a6,2f,85,5c,86,5d,a9,16,a2,0,85,1f,86,20,c5,13,f0
  //   ,5,20,a1,d4,f0,f7,a9,7,85,50,a5,2a,a6,2b,85,1f,86,20,e4,2d,d0
  //   ,4,c5,2c,f0,5,20,97,d4,f0,f3,85,55,86,56,a9,3,85,50,a5,55,a6,56
  //   ,e4,2f,d0,7,c5,2e,d0,3,4c,e0,d4,85,1f,86,20,a0,0,b1,1f,aa,c8,b1
  //   ,1f,8,c8,b1,1f,65,55,85,55,c8,b1,1f,65,56,85,56,28,10,d3,8a,30
  //   ,d0,c8,b1,1f,a0,0,a,69,5,65,1f,85,1f,90,2,e6,20,a6,20,e4,56,d0
  //   ,4,c5,55,f0,ba,20,a1,d4,f0,f3,b1,1f,30,35,c8,b1,1f,10,30,c8,b1
  //   ,1f,f0,2b,c8,b1,1f,aa,c8,b1,1f,c5,31,90,6,d0,1e,e4,30,b0,1a,c5
  //   ,5d,90,16,d0,4,e4,5c,90,10,86,5c,85,5d,a5,1f,a6,20,85,4b,86,4c
  //   ,a5,50,85,52,a5,50,18,65,1f,85,1f,90,2,e6,20,a6,20,a0,0,60,a5
  //   ,4c,5,4b,f0,f5,a5,52,29,4,4a,a8,85,52,b1,4b,65,5c,85,57,a5,5d
  //   ,69,0,85,58,a5,30,a6,31,85,55,86,56,20,df,c2,a4,52,c8,a5,55,91
  //   ,4b,aa,e6,56,a5,56,c8,91,4b,4c,4,d4,a5,62,48,a5,61,48,20,84,cd
  //   ,20,90,cc,68,85,6c,68,85,6d,a0,0,b1,6c,18,71,61,90,5,a2,b0,4c
  //   ,57,c3,20,4f,d3,20,54,d5,a5,4d,a4,4e,20,84,d5,20,66,d5,a5,6c,a4
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  //   contents of C000 (hex, n*v repeats v):
  //   40,c7,57,c6,1f,cc,ff,c7,a6,ca,c0,ca,62,cf,6,cb,ac,c8,ac,c7,84
  //   ,c7,2f,c8,2f,c7,8f,c7,d9,c7,42,c8,3e,c7,52,c8,f,d7,d4,ff,d7,ff
  //   ,da,ff,8c,d2,6,d7,8a,c9,aa,c9,6a,c7,b4,c5,76,c5,90,c9,dd,ff,bf
  //   ,ff,c2,ff,7c,ca,5a,c5,45,db,d8,db,64,db,0,0,59,d2,7a,d2,5e,de
  //   ,7f,df,f6,d8,da,de,d8,df,df,df,28,e0,8c,e0,e8,d6,56,d6,3f,d3,87
  //   ,d6,65,d6,c6,d5,da,d5,6,d6,11,d6,79,75,d7,79,35,d7,7b,36,d9,7b
  //   ,1d,da,7f,67,de,50,ca,ce,46,c7,ce,7d,a0,de,5a,ce,cd,64,f7,ce,45
  //   ,4e,c4,46,4f,d2,4e,45,58,d4,44,41,54,c1,49,4e,50,55,54,a3,49,4e
  //   ,50,55,d4,44,49,cd,52,45,41,c4,4c,45,d4,47,4f,54,cf,52,55,ce,49
  //   ,c6,52,45,53,54,4f,52,c5,47,4f,53,55,c2,52,45,54,55,52,ce,52,45
  //   ,cd,53,54,4f,d0,4f,ce,57,41,49,d4,4c,4f,41,c4,53,41,56,c5,56,45
  //   ,52,49,46,d9,44,45,c6,50,4f,4b,c5,50,52,49,4e,54,a3,50,52,49,4e
  //   ,d4,43,4f,4e,d4,4c,49,53,d4,43,4c,d2,43,4d,c4,53,59,d3,4f,50,45
  //   ,ce,43,4c,4f,53,c5,47,45,d4,4e,45,d7,54,41,42,a8,54,cf,46,ce,53
  //   ,50,43,a8,54,48,45,ce,4e,4f,d4,53,54,45,d0,ab,ad,aa,af,de,41,4e
  //   ,c4,4f,d2,be,bd,bc,53,47,ce,49,4e,d4,41,42,d3,55,53,d2,46,52,c5
  //   ,50,4f,d3,53,51,d2,52,4e,c4,4c,4f,c7,45,58,d0,43,4f,d3,53,49,ce
  //   ,54,41,ce,41,54,ce,50,45,45,cb,4c,45,ce,53,54,52,a4,56,41,cc,41
  //   ,53,c3,43,48,52,a4,4c,45,46,54,a4,52,49,47,48,54,a4,4d,49,44,a4
  //   ,47,cf,0,4e,45,58,54,20,57,49,54,48,4f,55,54,20,46,4f,d2,53,59
  //   ,4e,54,41,d8,52,45,54,55,52,4e,20,57,49,54,48,4f,55,54,20,47,4f
  //   ,53,55,c2,4f,55,54,20,4f,46,20,44,41,54,c1,49,4c,4c,45,47,41,4c
  //   ,20,51,55,41,4e,54,49,54,d9,4f,56,45,52,46,4c,4f,d7,4f,55,54,20
  //   ,4f,46,20,4d,45,4d,4f,52,d9,55,4e,44,45,46,27,44,20,53,54,41,54
  //   ,45,4d,45,4e,d4,42,41,44,20,53,55,42,53,43,52,49,50,d4,52,45,44
  //   ,49,4d,27,44,20,41,52,52,41,d9,44,49,56,49,53,49,4f,4e,20,42,59
  //   ,20,5a,45,52,cf,49,4c,4c,45,47,41,4c,20,44,49,52,45,43,d4,54,59
  //   ,50,45,20,4d,49,53,4d,41,54,43,c8,53,54,52,49,4e,47,20,54,4f,4f
  //   ,20,4c,4f,4e,c7,46,49,4c,45,20,44,41,54,c1,46,4f,52,4d,55,4c,41
  //   ,20,54,4f,4f,20,43,4f,4d,50,4c,45,d8,43,41,4e,27,54,20,43,4f,4e
  //   ,54,49,4e,55,c5,55,4e,44,45,46,27,44,20,46,55,4e,43,54,49,4f,ce
  //   ,20,45,52,52,4f,52,0,20,49,4e,20,0,d,a,52,45,41,44,59,2e,d,a,0
  //   ,d,a,42,52,45,41,4b,0,ba,4*e8,bd,1,1,c9,81,d0,21,a5,47,d0,a,bd
  //   ,2,1,85,46,bd,3,1,85,47,dd,3,1,d0,7,a5,46,dd,2,1,f0,7,8a,18,69
  //   ,12,aa,d0,d8,60,20,28,c3,85,2e,84,2f,38,a5,57,e5,5c,85,1f,a8,a5
  //   ,58,e5,5d,aa,e8,98,f0,23,a5,57,38,e5,1f,85,57,b0,3,c6,58,38,a5
  //   ,55,e5,1f,85,55,b0,8,c6,56,90,4,b1,57,91,55,88,d0,f9,b1,57,91
  //   ,55,c6,58,c6,56,ca,d0,f2,60,a,69,3e,b0,35,85,1f,ba,e4,1f,90,2e
  //   ,60,c4,31,90,28,d0,4,c5,30,90,22,48,a2,9,98,48,b5,54,ca,10,fa
  //   ,20,0,d4,a2,f7,68,95,5e,e8,30,fa,68,a8,68,c4,31,90,6,d0,5,c5,30
  //   ,b0,1,60,a2,4d,46,d,a5,e,f0,7,20,cc,ff,a9,0,85,e,20,e2,c9,20,43
  //   ,ca,bd,92,c1,48,29,7f,20,45,ca,e8,68,10,f3,20,93,c5,a9,8b,a0,c2
  //   ,20,1c,ca,a4,37,c8,f0,3,20,ce,dc,46,d,a9,97,a0,c2,20,1c,ca,20
  //   ,6f,c4,86,77,84,78,20,70,0,aa,f0,f3,a2,ff,86,37,90,6,20,95,c4
  //   ,4c,f7,c6,20,73,c8,20,95,c4,84,5,20,2c,c5,90,44,a0,1,b1,5c,85
  //   ,20,a5,2a,85,1f,a5,5d,85,22,a5,5c,88,f1,5c,18,65,2a,85,2a,85,21
  //   ,a5,2b,69,ff,85,2b,e5,5d,aa,38,a5,5c,e5,2a,a8,b0,3,e8,c6,22,18
  //   ,65,1f,90,3,c6,20,18,b1,1f,91,21,c8,d0,f9,e6,20,e6,22,ca,d0,f2
  //   ,20,72,c5,20,42,c4,ad,0,2,f0,8b,18,a5,2a,85,57,65,5,85,55,a4,2b
  //   ,84,58,90,1,c8,84,56,20,d8,c2,a5,11,a4,12,8d,fe,1,8c,ff,1,a5,2e
  //   ,a4,2f,85,2a,84,2b,a4,5,88,b9,fc,1,91,5c,88,10,f8,20,72,c5,20
  //   ,42,c4,4c,92,c3,a5,28,a4,29,85,1f,84,20,18,a0,1,b1,1f,f0,1d,a0
  //   ,4,c8,b1,1f,d0,fb,c8,98,65,1f,aa,a0,0,91,1f,a5,20,69,0,c8,91,1f
  //   ,86,1f,85,20,90,dd,60,a2,0,20,81,c4,c9,d,f0,6,9d,0,2,e8,d0,f3
  //   ,4c,d5,c9,20,cf,ff,a4,e,d0,c,c9,f,d0,8,48,a5,d,49,ff,85,d,68,60
  //   ,a6,77,a0,4,84,9,bd,0,2,10,7,c9,ff,f0,3e,e8,d0,f4,c9,20,f0,37
  //   ,85,4,c9,22,f0,56,24,9,70,2d,c9,3f,d0,4,a9,99,d0,25,c9,30,90,4
  //   ,c9,3c,90,1d,84,6e,a0,0,84,5,88,86,77,ca,c8,e8,bd,0,2,38,f9,92
  //   ,c0,f0,f5,c9,80,d0,30,5,5,a4,6e,e8,c8,99,fb,1,b9,fb,1,f0,36,38
  //   ,e9,3a,f0,4,c9,49,d0,2,85,9,38,e9,55,d0,9f,85,4,bd,0,2,f0,df,c5
  //   ,4,f0,db,c8,99,fb,1,e8,d0,f0,a6,77,e6,5,c8,b9,91,c0,10,fa,b9,92
  //   ,c0,d0,b4,bd,0,2,10,be,99,fd,1,c6,78,a9,ff,85,77,60,a5,28,a6,29
  //   ,a0,1,85,5c,86,5d,b1,5c,f0,1f,c8,c8,a5,12,d1,5c,90,18,f0,3,88
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  //   8-BIT
  //   SHIFT
  //   REG
  //   contents of _9000 (hex, n*v repeats v):
  //   2048*ff,78,a2,80,9a,d8,a2,0,8a,9d,0,80,a9,20,9d,0,81,9d,0,82,9d
  //   ,0,83,e8,d0,ee,a2,12,bd,84,99,9d,8f,81,ca,d0,f7,ca,8a,5d,0,80
  //   ,f0,4c,a9,ff,9d,0,80,5d,0,80,d0,22,9d,0,80,5d,0,80,d0,1a,a0,a
  //   ,b9,bb,99,99,df,81,88,d0,f7,e8,8a,ce,e1,81,a,90,fa,fe,0,80,e8
  //   ,4c,50,98,a0,b8,29,f,d0,1,88,8c,e0,81,a0,86,8c,e1,81,a0,8,b9,aa
  //   ,99,99,e1,81,88,d0,f7,fe,0,80,4c,71,98,8a,d0,aa,a2,9,bd,a0,99
  //   ,9d,df,81,ca,d0,f7,a9,0,9d,0,1,e8,d0,fa,8a,95,0,e8,d0,fa,ca,8a
  //   ,55,0,f0,47,a9,ff,95,0,55,0,d0,1f,95,0,55,0,d0,19,a0,a,b9,bb,99,99
  //   ,2f,82,88,d0,f7,e8,8a,ce,31,82,a,90,fa,f6,0,e8,4c,ba,98,9a,a2
  //   ,b1,e8,a,90,fc,8e,30,82,a2,9,bd,a9,99,9d,30,82,ca,d0,f7,ba,95
  //   ,0,9d,0,1,91,2,4c,d6,98,8a,d0,b0,a2,9,bd,b2,99,9d,2f,82,ca,d0
  //   ,f7,a0,1,bd,0,1,f0,17,a0,a,b9,bb,99,99,7f,82,88,d0,f7,85,0,8d
  //   ,ff,1,85,aa,8d,55,1,f0,f4,98,9d,0,1,c8,e8,d0,dc,98,5d,0,1,d0,a6
  //   ,c8,e8,d0,f6,a0,8,b9,c5,99,99,7f,82,88,d0,f7,84,2,84,0,a9,1,85
  //   ,3,a9,99,85,1,a2,7,b1,0,91,2,c8,d0,f9,e6,1,e6,3,ca,d0,f2,a2,7
  //   ,c6,1,c6,3,b1,2,d1,0,f0,20,a9,ff,91,2,51,2,d0,bf,91,2,51,2,d0
  //   ,b9,a2,a,bd,96,99,9d,cf,82,ca,d0,f7,85,7f,8d,80,3f,f0,f9,c8,d0
  //   ,d7,ca,d0,d0,a2,a,bd,ce,99,9d,d0,82,ca,10,f7,4c,d9,1,4,9,1,7,e
  //   ,f,13,14,9,3,20,33,32,30,33,35,30,7,81,b8,ad,81,b1,b1,a0,82,81
  //   ,84,14,16,20,12,1,d,20,f,b,89,ad,92,81,8d,a0,82,81,84,1a,2d,10
  //   ,1,7,5,20,f,b,81,b8,ad,81,84,92,a0,82,81,84,13,14,1,3,b,20,f,b
  //   ,12,5,d,f,16,5,20,3,c,9,10,a9,6,85,7,20,63,5,a2,b,bd,cf,82,49
  //   ,80,9d,cf,82,ca,d0,f5,ad,fd,ff,c9,98,f0,e5,c6,7,10,e5,a2,b,a9
  //   ,20,9d,cf,82,ca,d0,fa,84,0,a9,10,85,1,98,91,0,c8,d0,fa,98,d1,0
  //   ,d0,8,c8,d0,f8,e8,6,1,10,ed,a5,1,85,b,c9,40,90,2,46,b,38,e9,8
  //   ,85,a,bd,6c,7,85,10,a9,f,8d,10,e8,a,8d,40,e8,8d,42,e8,a2,ff,8e
  //   ,22,e8,8e,45,e8,a9,3c,8d,13,e8,8d,21,e8,8d,23,e8,8d,11,e8,8e,22
  //   ,e8,a9,c,8d,4c,e8,84,11,84,12,20,9f,6,20,3b,6,f0,12,10,3,4c,86
  //   ,5,a2,9,20,5,6,20,9f,6,20,63,5,f0,f3,a2,9,20,2a,6,20,3b,6,f0,e9
  //   ,a2,9,20,18,6,a2,1a,20,2a,6,a8,85,e,2c,4f,e8,10,5,88,d0,f8,f0
  //   ,1b,a0,0,2c,4f,e8,30,5,88,d0,f8,f0,f,a0,a,2c,4f,e8,30,fb,88,d0
  //   ,fd,2c,4f,e8,30,6,20,5,6,4c,1d,7,ee,ff,ff,2c,4f,e8,30,f2,20,18
  //   ,6,a5,10,20,ff,6,a2,21,20,2a,6,a0,ff,84,6,c8,a6,a,84,0,a9,8,85
  //   ,1,98,18,65,1,45,6,91,0,a5,0,d0,24,c8,d0,f1,e6,1,ca,d0,ec,a6,a
  //   ,c6,1,98,18,65,1,45,6,51,0,f0,5c,a9,ff,91,0,51,0,d0,33,91,0,51
  //   ,0,d0,2d,a2,37,e6,1,a5,1,e8,4a,90,fc,a9,41,20,21,6,8a,c9,3a,90
  //   ,a,38,e9,a,48,a9,31,20,21,6,68,20,21,6,a2,26,20,5,6,85,7f,8d,80
  //   ,3f,30,f9,a2,31,e8,a,90,fc,a9,49,a4,1,c4,b,90,2,a9,4a,20,a8,6
  //   ,a2,22,20,5,6,a9,aa,91,0,4a,91,0,90,f7,c8,d0,97,ca,d0,92,e6,6
  //   ,d0,3,4c,d3,2,a5,10,20,ff,6,a2,21,20,18,6,a2,1e,20,2a,6,84,5,84
  //   ,4,a2,10,a5,5,c9,f0,d0,6,a9,e8,85,5,a2,8,a9,0,18,c6,5,71,4,c8
  //   ,d0,fb,ca,d0,f6,69,0,48,a2,1e,20,e,6,a9,20,20,b0,6,a5,5,4*4a,18
  //   ,69,ca,a2,3d,20,15,7,68,a2,d,20,15,7,a5,5,c9,a0,b0,be,e6,e,20
  //   ,c8,6,20,5a,5,a2,2a,20,2a,6,a9,fd,a0,9,8c,10,e8,cd,12,e8,f0,d
  //   ,20,5,6,a0,a,8c,10,e8,88,10,fa,30,f6,4a,90,2,9,80,88,10,e3,8c
  //   ,10,e8,cc,12,e8,d0,e3,20,18,6,ad,fe,ff,85,0,ad,ff,ff,85,1,a9,0
  //   ,85,9,a4,9,b1,0,c9,6c,d0,15,c8,b1,0,85,2,c8,b1,0,85,3,a0,0,a9
  //   ,68,91,2,c8,a9,6,91,2,e6,9,d0,df,a2,e,20,2a,6,20,3b,6,58,20,d7
  //   ,5,84,f,58,20,7d,5,a2,30,20,2a,6,20,d7,5,98,84,f,8d,44,e8,8d,45
  //   ,e8,20,6f,5,a2,43,20,2a,6,20,d7,5,98,84,f,8d,48,e8,8d,49,e8,20
  //   ,6f,5,a2,4d,20,c4,5,a2,52,20,c4,5,a2,57,20,2a,6,a0,0,98,8d,22
  //   ,e8,4d,20,e8,f0,18,48,20,a,6,68,a2,30,e8,4a,90,fc,8a,20,21,6,20
  //   ,8,6,ee,22,e8,4c,89,4,c8,d0,dc,20,18,6,a2,5f,20,2a,6,78,a2,68
  //   ,2c,20,e8,a0,4,20,fa,5,2c,21,e8,30,8,20,5,6,20,fa,5,d0,fb,a2,6e
  //   ,a0,2,2c,40,e8,50,ef,20,fd,5,2c,40,e8,70,e7,20,fd,5,a2,6b,a0,3c
  //   ,8c,23,e8,2c,40,e8,10,2c,a9,34,8d,23,e8,2c,40,e8,30,22,a2,76,8c
  //   ,11,e8,2c,10,e8,50,1b,8d,11,e8,2c,10,e8,70,13,8c,11,e8,a2,72,8c
  //   ,21,e8,4e,40,e8,b0,15,a0,21,2c,a0,23,2c,a0,11,20,5,6,a9,8,59,0
  //   ,e8,99,0,e8,d0,f6,8d,21,e8,4e,40,e8,b0,e3,a2,79,2c,22,e8,ee,43
  //   ,e8,ce,43,e8,2c,23,e8,30,c,20,5,6,ee,43,e8,ce,43,e8,4c,2b,5,a2
  //   ,5f,20,18,6,a2,5,fe,f3,7,bd,f3,7,c9,3a,90,a,a9,30,9d,f3,7,ca,10
  //   ,ee,30,ea,a2,7c,20,a,6,20,5a,5,4c,2f,2,a2,a,20,63,5,ca,d0,fa,60
  //   ,a9,0,a8,18,69,1,d0,fc,c8,d0,f9,60,86,7,a4,e,b9,4f,7,aa,bd,0,e8
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  //   4 TO 16
  //   DECODER
  //   S
  //   R
  //   QUAD
  //   2TO1
  //   MUX
  //   E for 8k PET
  //   F for 16k PET
  //   E
  //   F
  //   2 - IEEE-488 Interface
  //   5 - RAMS
  //   7 - DISPLAY LOGIC
  //   A
  //   C
  //   B
  //   Jumperd for 16k
  //   8-BIT
  //   LATCH
  //   L
  //   M
  //   H
  //   I
  //   J
  //   4-BIT
  //   COUNTER
  //   ~{200 LINES}
  //   ~{20 LINES}
  //   3 - Cassette & Keyboard
  //   8 - DISPLAY RAMS
  //   DEBUG
  //   Breakpoint
  //   1KX4
  //   RAM
  //   BCD TO
  //   DECIMAL
  //   DECODER
  //   USER PORT (J4)
endmodule
