// Digital circuit Mainboard-PET2001-4.dig as structural Verilog
module Mainboard_PET2001_4 (
  input  _8MHz,
  output [15:0] BA,
  output [7:0] D,
  output \BΦ2 ,
  output [31:0] cycle,
  output r_w
);

  wire _1_CASS_MOTOR, _1_CASS_READ, _1_CASS_SWITCH, _2_CASS_MOTOR, _2_CASS_READ, _2_CASS_SWITCH,
       _74ls93_1_qa, _74ls93_1_qc, _74ls93_1_qd, _74ls93_2_qa, _74ls93_2_qb, _74ls93_2_qc, _74ls93_2_qd,
       _74ls93_3_qb, _74ls93_3_qc, _74ls93_3_qd, _74ls107_1_q, _74ls107_2_nq, _74ls107_2_q, _74ls107_3_nq,
       _74ls107_3_q, _74ls107_4_q, _74ls107_6_nq, _74ls107_6_q, _74ls107_7_nq, _74ls107_7_q, _74ls107_8_nq,
       _74ls107_8_q, _74ls107_clr_top_1_q, _74ls107_clr_top_2_q, _74ls145_1__0, _74ls145_1__1, _74ls145_1__2,
       _74ls145_1__3, _74ls145_1__4, _74ls145_1__5, _74ls145_1__6, _74ls145_1__7, _74ls145_1__8,
       _74ls145_1__9, _74ls157_1_y2, _74ls165_layout_2_1_nqh, _74ls165_layout_2_1_qh, _74s74_1_q,
       _74s74_2_nq, _74s74_2_q, \_6502_layout_2_1_φ2 , _6520_layout_2_2_cb2, _6520_layout_2_2_pa0,
       _6520_layout_2_2_pa1, _6520_layout_2_2_pa2, _6520_layout_2_2_pa3, _6522_layout_2_1_pb4, _74100_1_q1,
       _74100_1_q2, _74100_1_q3, _74100_1_q4, _74100_1_q5, _74100_1_q6, _74100_1_q7, _74100_1_q8,
       _74154_layout_2_1_y8, _74177_layout_2_1_qa, _74177_layout_2_1_qb, _74177_layout_2_1_qc,
       _74177_layout_2_1_qd, _74177_layout_2_2_qa, _74177_layout_2_2_qb, _74177_layout_2_2_qc,
       _74177_layout_2_2_qd, and_1_out, and_3_out, and_4_out, and_6_out, and_7_out, and_8_out, and_10_out,
       and_11_out, and_12_out, and_13_out, and_14_out, and_15_out, and_16_out, and_17_out, BBD0, BBD1, BBD2,
       BBD3, BBD4, BBD5, BBD6, BBD7, BD0, BD1, BD2, BD3, BD4, BD5, BD6, BD7, BLANK_TV, CA1, CASS_WRITE,
       CHARROM_d0, CHARROM_d1, CHARROM_d2, CHARROM_d3, CHARROM_d4, CHARROM_d5, CHARROM_d6, CHARROM_d7,
       comparator_1_eq, DIAG, DIS_OFF, DIS_ON, fuse_1_b, GRAPHIC, HORZ_DRIVE, nand_1_out, nand_3_out,
       nand_4_out, nand_5_out, nand_7_out, nand_8_out, nand_9_out, nand_10_out, nand_11_out, nand_13_out,
       nand_14_out, nBA11, nEOI, nIRQ, nor_1_out, nor_2_out, nor_3_out, nor_4_out, nor_5_out, nor_6_out,
       nor_7_out, not_1_out, not_2_out, not_6_out, not_7_out, not_8_out, not_9_out, nRES, nSEL0, nSEL1,
       nSELC, nSELD, nSELE, nSELF, nSRQ_IN, or_1_out, or_2_out, or_3_out, PA0, PA1, PA2, PA3, PA4, PA5, PA6,
       PA7, pullup_2_out, reset_1_out, RESET_Delay_ovf, RW_nE, SD0, SD1, SD2, SD3, SD4, SD5, SD6, SD7, SEL8,
       SYNC, TV_VIDEO_DRIVE, VERT_DRIVE, \Φ0 ;
  wire [1:0] _74ls157_1_y3;
  wire [3:0] _74ls157_2_y1, _74ls157_3_y1;
  wire [7:0] _6520_layout_2_2_pb7;
  wire [10:0] d_ff_1_q, d_ff_2_q, d_ff_3_q, d_ff_4_q, d_ff_5_q, d_ff_6_q, d_ff_7_q;
  wire [11:0] _6502_layout_2_1_a0;

  not not_1 (not_1_out, _74ls93_1_qd);
  _74LS107 _74ls107_1 (.J(_74ls93_1_qd), .nCLK(and_1_out), .K(not_1_out), .Q(_74ls107_1_q), .nQ(\Φ0 ), .nCLR(1'b1));
  not not_2 (not_2_out, 1'b1);
  PullUp pullup_1 (.out(nIRQ));
  _74LS244 _74ls244_1 (
    ._1Y1(D[0]), ._2A1(D[0]), ._1Y2(D[1]), ._2A2(D[1]), ._1Y3(D[2]), ._2A3(D[2]), ._1Y4(D[3]), ._2A4(D[3]),
    ._1nG(not_6_out), ._1A1(BD0), ._2Y1(BD0), ._1A2(BD1), ._2Y2(BD1), ._1A3(BD2), ._2Y3(BD2), ._1A4(BD3),
    ._2Y4(BD3), ._2nG(and_6_out));
  _74LS244 _74ls244_2 (
    ._1Y1(D[4]), ._2A1(D[4]), ._1Y2(D[5]), ._2A2(D[5]), ._1Y3(D[6]), ._2A3(D[6]), ._1Y4(D[7]), ._2A4(D[7]),
    ._1nG(not_6_out), ._1A1(BD4), ._2Y1(BD4), ._1A2(BD5), ._2Y2(BD5), ._1A3(BD6), ._2Y3(BD6), ._1A4(BD7),
    ._2Y4(BD7), ._2nG(and_6_out));
  _74LS93 _74ls93_1 (
    .CKA(_74ls93_1_qd), .CKB(and_1_out), .R1(not_2_out), .R2(not_2_out), .QA(_74ls93_1_qa),
    .QC(_74ls93_1_qc), .QD(_74ls93_1_qd));  // open: QB
  _74LS93 _74ls93_2 (
    .CKA(_74ls93_1_qa), .CKB(_74ls93_2_qa), .R1(not_2_out), .R2(not_2_out), .QA(_74ls93_2_qa),
    .QB(_74ls93_2_qb), .QC(_74ls93_2_qc), .QD(_74ls93_2_qd));
  _74LS107 _74ls107_2 (.J(1'b1), .nCLK(_74ls93_2_qd), .K(1'b1), .Q(_74ls107_2_q), .nQ(_74ls107_2_nq), .nCLR(1'b1));
  and and_1 (and_1_out, 1'b1, _8MHz);
  _74154_layout_2 _74154_layout_2_1 (
    .D(BA[15]), .C(BA[14]), .B(BA[13]), .A(BA[12]), .nG1(1'b0), .nG2(1'b0), .Y0(nSEL0), .Y1(nSEL1),
    .Y8(_74154_layout_2_1_y8), .Y12(nSELC), .Y13(nSELD), .Y14(nSELE), .Y15(nSELF));  // open: Y2, Y3, Y4, Y5, Y6, Y7, Y9, Y10, Y11
  not not_3 (BA[11], nBA11);
  Delay delay_1 (.in(_6502_layout_2_1_a0[9]), .out(BA[9]));
  Delay delay_2 (.in(_6502_layout_2_1_a0[6]), .out(BA[6]));
  Delay delay_3 (.in(_6502_layout_2_1_a0[3]), .out(BA[3]));
  not not_4 (SEL8, _74154_layout_2_1_y8);
  not not_5 (nBA11, _6502_layout_2_1_a0[11]);
  Delay delay_4 (.in(_6502_layout_2_1_a0[10]), .out(BA[10]));
  Delay delay_5 (.in(_6502_layout_2_1_a0[8]), .out(BA[8]));
  Delay delay_6 (.in(_6502_layout_2_1_a0[7]), .out(BA[7]));
  Delay delay_7 (.in(_6502_layout_2_1_a0[5]), .out(BA[5]));
  Delay delay_8 (.in(_6502_layout_2_1_a0[4]), .out(BA[4]));
  Delay delay_9 (.in(_6502_layout_2_1_a0[2]), .out(BA[2]));
  Delay delay_10 (.in(_6502_layout_2_1_a0[1]), .out(BA[1]));
  and and_2 (BA[0], 1'b1, _6502_layout_2_1_a0[0]);
  not not_6 (not_6_out, and_6_out);
  and and_3 (and_3_out, _74ls93_2_qc, _74ls107_2_q);
  and and_4 (and_4_out, _74ls107_2_nq, _74ls93_2_qd);
  and and_5 (RW_nE, nSELE, pullup_2_out, pullup_2_out, r_w);
  Reset reset_1 (.out(reset_1_out));
  _74LS107 _74ls107_3 (
    .J(1'b1), .nCLK(_74ls93_1_qd), .K(1'b0), .Q(_74ls107_3_q), .nQ(_74ls107_3_nq), .nCLR(nand_1_out));
  nand nand_1 (nand_1_out, and_1_out, _74ls107_3_q);
  _74LS107 _74ls107_4 (.J(DIS_ON), .nCLK(_74ls93_2_qb), .K(DIS_OFF), .Q(_74ls107_4_q), .nQ(HORZ_DRIVE), .nCLR(1'b1));
  _74LS107 _74ls107_5 (.J(and_3_out), .nCLK(_74ls93_1_qa), .K(and_4_out), .Q(DIS_ON), .nQ(DIS_OFF), .nCLR(1'b1));
  and and_6 (and_6_out, nSELC, nSELD, nSELF, RW_nE);
  Counter #(.Bits(10)) RESET_Delay (.en(reset_1_out), .C(\Φ0 ), .clr(nRES), .ovf(RESET_Delay_ovf));  // open: out
  _6502_layout_2 _6502_layout_2_1 (
    .R_W(r_w), .\Φ0 (\Φ0 ), .\Φ2 (\_6502_layout_2_1_φ2 ), .nRESET(nRES), .nIRQ(nIRQ), .nNMI(1'b1),
    .RDY(1'b1), .D0(D[0]), .D1(D[1]), .D2(D[2]), .D3(D[3]), .D4(D[4]), .D5(D[5]), .D6(D[6]), .D7(D[7]),
    .A15(BA[15]), .A14(BA[14]), .A13(BA[13]), .A12(BA[12]), .A11(_6502_layout_2_1_a0[11]),
    .A10(_6502_layout_2_1_a0[10]), .A9(_6502_layout_2_1_a0[9]), .A8(_6502_layout_2_1_a0[8]),
    .A7(_6502_layout_2_1_a0[7]), .A6(_6502_layout_2_1_a0[6]), .A5(_6502_layout_2_1_a0[5]),
    .A4(_6502_layout_2_1_a0[4]), .A3(_6502_layout_2_1_a0[3]), .A2(_6502_layout_2_1_a0[2]),
    .A1(_6502_layout_2_1_a0[1]), .A0(_6502_layout_2_1_a0[0]));  // open: Φ1, SYNC
  nand nand_2 (\BΦ2 , nand_3_out, pullup_2_out);
  and and_7 (and_7_out, BA[6], BA[11]);
  nand nand_3 (nand_3_out, \_6502_layout_2_1_φ2 , pullup_2_out);
  RS_FF_AS rs_ff_as_1 (.S(RESET_Delay_ovf), .R(1'b0), .Q(nRES));  // open: nQ
  PullUp pullup_2 (.out(pullup_2_out));
  _74LS107 _74ls107_6 (.J(and_8_out), .nCLK(_74ls93_1_qc), .K(1'b1), .Q(_74ls107_6_q), .nQ(_74ls107_6_nq), .nCLR(1'b1));
  and and_8 (and_8_out, DIS_OFF, or_2_out);
  _74LS107 _74ls107_7 (
    .J(_74ls107_8_nq), .nCLK(_74ls107_6_q), .K(_74ls107_8_q), .Q(_74ls107_7_q), .nQ(_74ls107_7_nq),
    .nCLR(1'b1));
  or or_1 (or_1_out, ~_74ls107_6_nq, ~nand_9_out);  // Or
  _74100 _74100_1 (
    ._1(_74177_layout_2_1_qa), ._2(_74177_layout_2_1_qb), ._3(_74177_layout_2_1_qc),
    ._4(_74177_layout_2_1_qd), ._5(_74177_layout_2_2_qa), ._6(_74177_layout_2_2_qb),
    ._7(_74177_layout_2_2_qc), ._8(_74177_layout_2_2_qd), .Q1(_74100_1_q1), .Q2(_74100_1_q2),
    .Q3(_74100_1_q3), .Q4(_74100_1_q4), .Q5(_74100_1_q5), .Q6(_74100_1_q6), .Q7(_74100_1_q7),
    .Q8(_74100_1_q8), .C1(or_1_out), .C2(or_1_out));
  not not_7 (not_7_out, nand_5_out);
  nand nand_4 (nand_4_out, not_7_out, _74100_1_q2);
  _6520_layout_2 _6520_layout_2_1 (
    .nIRQB(nIRQ), .nIRQA(nIRQ), .nRESET(nRES), .\Φ2 (\_6502_layout_2_1_φ2 ), .nCS2(nSELE), .CS1(BA[5]),
    .CS0(BA[11]), .RS1(BA[1]), .RS0(BA[0]), .R_W(r_w), .D0(D[0]), .D1(D[1]), .D2(D[2]), .D3(D[3]), .D4(D[4]),
    .D5(D[5]), .D6(D[6]), .D7(D[7]), .CA1(1'b1), .CB1(nSRQ_IN));  // open: CA2, PA0, PA1, PA2, PA3, PA4, PA5, PA6, PA7, PB0, PB1, PB2, PB3, PB4, PB5, PB6, PB7, CB2
  _6522_layout_2 _6522_layout_2_1 (
    .R_W(r_w), .RS0(BA[0]), .RS1(BA[1]), .RS2(BA[2]), .RS3(BA[3]), .CS1(and_7_out), .nCS2(nSELE),
    .\Φ2 (\_6502_layout_2_1_φ2 ), .nRESET(nRES), .nIRQ(nIRQ), .D0(D[0]), .D1(D[1]), .D2(D[2]), .D3(D[3]),
    .D4(D[4]), .D5(D[5]), .D6(D[6]), .D7(D[7]), .CA1(CA1), .CA2(GRAPHIC), .PA0(PA0), .PA1(PA1), .PA2(PA2),
    .PA3(PA3), .PA4(PA4), .PA5(PA5), .PA6(PA6), .PA7(PA7), .PB3(CASS_WRITE), .PB4(_6522_layout_2_1_pb4),
    .PB5(SYNC), .CB1(_2_CASS_READ));  // open: PB0, PB1, PB2, PB6, PB7, CB2
  _6520_layout_2 _6520_layout_2_2 (
    .nIRQB(nIRQ), .nIRQA(nIRQ), .nRESET(nRES), .\Φ2 (\_6502_layout_2_1_φ2 ), .nCS2(nSELE), .CS1(BA[4]),
    .CS0(BA[11]), .RS1(BA[1]), .RS0(BA[0]), .R_W(r_w), .D0(D[0]), .D1(D[1]), .D2(D[2]), .D3(D[3]), .D4(D[4]),
    .D5(D[5]), .D6(D[6]), .D7(D[7]), .CA1(_1_CASS_READ), .CA2(BLANK_TV), .PA0(_6520_layout_2_2_pa0),
    .PA1(_6520_layout_2_2_pa1), .PA2(_6520_layout_2_2_pa2), .PA3(_6520_layout_2_2_pa3), .PA4(_1_CASS_SWITCH),
    .PA5(_2_CASS_SWITCH), .PA6(nEOI), .PA7(DIAG), .PB0(_6520_layout_2_2_pb7[0]),
    .PB1(_6520_layout_2_2_pb7[1]), .PB2(_6520_layout_2_2_pb7[2]), .PB3(_6520_layout_2_2_pb7[3]),
    .PB4(_6520_layout_2_2_pb7[4]), .PB5(_6520_layout_2_2_pb7[5]), .PB6(_6520_layout_2_2_pb7[6]),
    .PB7(_6520_layout_2_2_pb7[7]), .CB1(SYNC), .CB2(_6520_layout_2_2_cb2));
  _74LS107 _74ls107_8 (
    .J(_74ls107_7_q), .nCLK(_74ls107_6_q), .K(_74ls107_7_nq), .Q(_74ls107_8_q), .nQ(_74ls107_8_nq),
    .nCLR(1'b1));
  _74LS107_CLR_TOP _74ls107_clr_top_1 (
    .J(1'b1), .nCLK(_74ls107_3_q), .K(1'b1), .Q(_74ls107_clr_top_1_q), .nCLR(DIS_ON));  // open: nQ
  _74LS107_CLR_TOP _74ls107_clr_top_2 (
    .J(1'b1), .nCLK(_74ls107_clr_top_1_q), .K(1'b1), .Q(_74ls107_clr_top_2_q), .nCLR(DIS_ON));  // open: nQ
  _74177_layout_2 _74177_layout_2_1 (
    .CLK1(_74ls107_clr_top_2_q), .CLK2(_74177_layout_2_1_qa), .QA(_74177_layout_2_1_qa),
    .QB(_74177_layout_2_1_qb), .QC(_74177_layout_2_1_qc), .QD(_74177_layout_2_1_qd), .nLD(DIS_ON),
    .nCLR(_74ls107_6_nq), .A(_74100_1_q1), .B(_74100_1_q2), .C(_74100_1_q3), .D(_74100_1_q4));
  _74177_layout_2 _74177_layout_2_2 (
    .CLK1(_74177_layout_2_1_qd), .CLK2(_74177_layout_2_2_qa), .QA(_74177_layout_2_2_qa),
    .QB(_74177_layout_2_2_qb), .QC(_74177_layout_2_2_qc), .QD(_74177_layout_2_2_qd), .nLD(DIS_ON),
    .nCLR(_74ls107_6_nq), .A(_74100_1_q5), .B(_74100_1_q6), .C(_74100_1_q7), .D(_74100_1_q8));
  nand nand_5 (nand_5_out, _74100_1_q5, _74100_1_q6, _74100_1_q7, _74100_1_q8);
  assign nEOI = ~BLANK_TV ? 1'b0 : 1'bz;  // DriverInvSel driverinvsel_1
  nand nand_6 (VERT_DRIVE, _74ls107_7_nq, _74ls107_8_nq);
  and and_9 (SYNC, _74ls107_7_q, _74ls107_8_q);
  not not_8 (not_8_out, SYNC);
  nand nand_7 (nand_7_out, 1'b1, _74ls93_3_qd, not_8_out, _74177_layout_2_2_qa);
  or or_2 (or_2_out, ~nand_7_out, ~nand_4_out);  // Or
  _74LS93 _74ls93_3 (
    .CKA(1'b1), .CKB(DIS_ON), .R1(_74ls107_6_q), .R2(1'b1), .QB(_74ls93_3_qb), .QC(_74ls93_3_qc),
    .QD(_74ls93_3_qd));  // open: QA
  _74LS157 _74ls157_1 (
    ._1A(1'b1), ._1B(1'b1), ._2A(1'b1), ._2B(RW_nE), ._3A(_74ls107_clr_top_1_q), ._3B(BA[0]),
    ._4A(_74ls107_clr_top_2_q), ._4B(BA[1]), .S(SEL8), .G(1'b0), .Y2(_74ls157_1_y2), .Y3(_74ls157_1_y3[0]),
    .Y4(_74ls157_1_y3[1]));  // open: Y1
  _74LS157 _74ls157_2 (
    ._1A(_74177_layout_2_1_qa), ._1B(BA[2]), ._2A(_74177_layout_2_1_qb), ._2B(BA[3]),
    ._3A(_74177_layout_2_1_qc), ._3B(BA[4]), ._4A(_74177_layout_2_1_qd), ._4B(BA[5]), .S(SEL8), .G(1'b0),
    .Y1(_74ls157_2_y1[0]), .Y2(_74ls157_2_y1[1]), .Y3(_74ls157_2_y1[2]), .Y4(_74ls157_2_y1[3]));
  _74LS157 _74ls157_3 (
    ._1A(_74177_layout_2_2_qa), ._1B(BA[6]), ._2A(_74177_layout_2_2_qb), ._2B(BA[7]),
    ._3A(_74177_layout_2_2_qc), ._3B(BA[8]), ._4A(_74177_layout_2_2_qd), ._4B(BA[9]), .S(SEL8), .G(1'b0),
    .Y1(_74ls157_3_y1[0]), .Y2(_74ls157_3_y1[1]), .Y3(_74ls157_3_y1[2]), .Y4(_74ls157_3_y1[3]));
  not not_9 (not_9_out, _6520_layout_2_2_pa2);
  not not_10 (_2_CASS_MOTOR, _6522_layout_2_1_pb4);
  not not_11 (_1_CASS_MOTOR, _6520_layout_2_2_cb2);
  nand nand_8 (nand_8_out, _6520_layout_2_2_pa0, _6520_layout_2_2_pa1, _6520_layout_2_2_pa3, not_9_out);
  nand nand_9 (nand_9_out, _74ls93_3_qd, _74ls93_3_qc, _74ls93_3_qb, DIS_ON);
  _74LS145 _74ls145_1 (
    .A(_6520_layout_2_2_pa0), .B(_6520_layout_2_2_pa1), .C(_6520_layout_2_2_pa2), .D(_6520_layout_2_2_pa3),
    ._0(_74ls145_1__0), ._1(_74ls145_1__1), ._2(_74ls145_1__2), ._3(_74ls145_1__3), ._4(_74ls145_1__4),
    ._5(_74ls145_1__5), ._6(_74ls145_1__6), ._7(_74ls145_1__7), ._8(_74ls145_1__8), ._9(_74ls145_1__9));
  _74LS165_layout_2 _74ls165_layout_2_1 (
    .SH_nLD(_74ls107_3_nq), .CLKINH(1'b0), .SER(1'b0), .CLK(and_1_out), .QH(_74ls165_layout_2_1_qh),
    .nQH(_74ls165_layout_2_1_nqh), .A(CHARROM_d0), .B(CHARROM_d1), .C(CHARROM_d2), .D(CHARROM_d3),
    .E(CHARROM_d4), .F(CHARROM_d5), .G(CHARROM_d6), .H(CHARROM_d7));
  _6540_Character_ROM CHARROM (
    .A0(_74ls93_3_qb), .A1(_74ls93_3_qc), .A2(_74ls93_3_qd), .CS1(1'b1), .CS2(1'b1), .nCS3(1'b0),
    .nCS4(1'b0), .nCS5(1'b0), .\Φ2 (_74ls107_1_q), .D0(CHARROM_d0), .D1(CHARROM_d1), .D2(CHARROM_d2),
    .D3(CHARROM_d3), .D4(CHARROM_d4), .D5(CHARROM_d5), .D6(CHARROM_d6), .D7(CHARROM_d7), .A10(GRAPHIC),
    .A9(SD6), .A8(SD5), .A7(SD4), .A6(SD3), .A5(SD2), .A4(SD1), .A3(SD0));
  LED led_1 (.in(nand_8_out));
  PETKeyboard petkeyboard_1 (
    .R0(_74ls145_1__0), .R1(_74ls145_1__1), .R2(_74ls145_1__2), .R3(_74ls145_1__3), .R4(_74ls145_1__4),
    .R5(_74ls145_1__5), .R6(_74ls145_1__6), .R7(_74ls145_1__7), .R8(_74ls145_1__8), .R9(_74ls145_1__9),
    .B0(_6520_layout_2_2_pb7[0]), .B1(_6520_layout_2_2_pb7[1]), .B2(_6520_layout_2_2_pb7[2]),
    .B3(_6520_layout_2_2_pb7[3]), .B4(_6520_layout_2_2_pb7[4]), .B5(_6520_layout_2_2_pb7[5]),
    .B6(_6520_layout_2_2_pb7[6]), .B7(_6520_layout_2_2_pb7[7]), .CLK(SYNC));
  _6550_layout_1 _6550_layout_1_1 (
    .R_nW(_74ls157_1_y2), .A0(_74ls157_1_y3[0]), .A1(_74ls157_1_y3[1]), .A2(_74ls157_2_y1[0]),
    .A3(_74ls157_2_y1[1]), .A4(_74ls157_2_y1[2]), .A5(_74ls157_2_y1[3]), .A6(_74ls157_3_y1[0]),
    .A7(_74ls157_3_y1[1]), .A8(_74ls157_3_y1[2]), .A9(_74ls157_3_y1[3]), .D0(SD0), .D1(SD1), .D2(SD2),
    .D3(SD3), .CS1(1'b1), .CS2(1'b1), .nCS3(1'b0), .nCS4(1'b0), .\Φ2 (\BΦ2 ));
  _74S74 _74s74_1 (.Q(_74s74_1_q), .nP(1'b1), .D(SD7), .CK(_74ls107_1_q), .nCL(1'b1));  // open: nQ
  PullDown pulldown_1 (.out(GRAPHIC));
  _74S74 _74s74_2 (.Q(_74s74_2_q), .nQ(_74s74_2_nq), .nP(1'b1), .D(_74s74_1_q), .CK(_74ls107_3_q), .nCL(1'b1));
  _6550_layout_1 _6550_layout_1_2 (
    .R_nW(_74ls157_1_y2), .A0(_74ls157_1_y3[0]), .A1(_74ls157_1_y3[1]), .A2(_74ls157_2_y1[0]),
    .A3(_74ls157_2_y1[1]), .A4(_74ls157_2_y1[2]), .A5(_74ls157_2_y1[3]), .A6(_74ls157_3_y1[0]),
    .A7(_74ls157_3_y1[1]), .A8(_74ls157_3_y1[2]), .A9(_74ls157_3_y1[3]), .D0(SD4), .D1(SD5), .D2(SD6),
    .D3(SD7), .CS1(1'b1), .CS2(1'b1), .nCS3(1'b0), .nCS4(1'b0), .\Φ2 (\BΦ2 ));
  DipSwitch #(.dipDefault("true")) dipswitch_1 (.out(_2_CASS_SWITCH));
  DipSwitch #(.dipDefault("true")) dipswitch_2 (.out(_1_CASS_SWITCH));
  Comparator #(.Bits(16)) comparator_1 (.a(BA), .b(16'h8300), .eq(comparator_1_eq));  // open: gt, lt
  nand nand_10 (nand_10_out, _74ls165_layout_2_1_qh, _74s74_2_q);
  nand nand_11 (nand_11_out, _74ls165_layout_2_1_nqh, _74s74_2_nq);
  and and_10 (and_10_out, nand_10_out, nand_11_out);
  nand nand_12 (TV_VIDEO_DRIVE, DIS_ON, and_10_out, SYNC, BLANK_TV);
  _74LS244 _74ls244_3 (
    ._1Y1(BD0), ._2A1(BD0), ._1Y2(BD1), ._2A2(BD1), ._1Y3(BD2), ._2A3(BD2), ._1Y4(BD3), ._2A4(BD3),
    ._1nG(nand_13_out), ._1A1(SD0), ._2Y1(SD0), ._1A2(SD1), ._2Y2(SD1), ._1A3(SD2), ._2Y3(SD2), ._1A4(SD3),
    ._2Y4(SD3), ._2nG(_74ls157_1_y2));
  _74LS244 _74ls244_4 (
    ._1Y1(BD4), ._2A1(BD4), ._1Y2(BD5), ._2A2(BD5), ._1Y3(BD6), ._2A3(BD6), ._1Y4(BD7), ._2A4(BD7),
    ._1nG(nand_13_out), ._1A1(SD4), ._2Y1(SD4), ._1A2(SD5), ._2Y2(SD5), ._1A3(SD6), ._2Y3(SD6), ._1A4(SD7),
    ._2Y4(SD7), ._2nG(_74ls157_1_y2));
  Break break_1 (.brk(\BΦ2 ));
  Counter #(.Bits(32)) counter_1 (.en(1'b1), .C(\BΦ2 ), .clr(1'b0), .out(cycle));  // open: ovf
  nand nand_13 (nand_13_out, SEL8, RW_nE);
  Fuse #(.Blown("true")) fuse_1 (.A(nSEL1), .B(fuse_1_b));
  or or_3 (or_3_out, ~fuse_1_b, ~nSEL0);  // Or
  PullUp pullup_3 (.out(fuse_1_b));
  nand nand_14 (nand_14_out, RW_nE, or_3_out);
  CRT_white crt_white_1 (.VIDEO(TV_VIDEO_DRIVE), .CLK8(_8MHz), .HOR_DRIVE_IN(HORZ_DRIVE), .VER_DRIVE_IN(VERT_DRIVE));
  _74LS244 _74ls244_5 (
    ._1Y1(BBD7), ._2A1(BBD7), ._1Y2(BBD6), ._2A2(BBD6), ._1Y3(BBD5), ._2A3(BBD5), ._1Y4(BBD4), ._2A4(BBD4),
    ._1nG(RW_nE), ._1A1(BD7), ._2Y1(BD7), ._1A2(BD6), ._2Y2(BD6), ._1A3(BD5), ._2Y3(BD5), ._1A4(BD4),
    ._2Y4(BD4), ._2nG(nand_14_out));
  _74LS244 _74ls244_6 (
    ._1Y1(BBD3), ._2A1(BBD3), ._1Y2(BBD2), ._2A2(BBD2), ._1Y3(BBD1), ._2A3(BBD1), ._1Y4(BBD0), ._2A4(BBD0),
    ._1nG(RW_nE), ._1A1(BD3), ._2Y1(BD3), ._1A2(BD2), ._2Y2(BD2), ._1A3(BD1), ._2Y3(BD1), ._1A4(BD0),
    ._2Y4(BD0), ._2nG(nand_14_out));
  nor nor_1 (nor_1_out, 1'b0, nSELF, 1'b0);
  D_FF #(.Bits(11)) d_ff_1 (.D(BA[10:0]), .C(\BΦ2 ), .Q(d_ff_1_q));  // open: nQ
  and and_11 (and_11_out, BA[11], 1'b1, nor_1_out, \BΦ2 );
  ROM #(.AddrBits(11), .Bits(8)) F800 (.A(d_ff_1_q), .sel(and_11_out), .D(D));
  nor nor_2 (nor_2_out, 1'b0, nSELF, BA[11]);
  D_FF #(.Bits(11)) d_ff_2 (.D(BA[10:0]), .C(\BΦ2 ), .Q(d_ff_2_q));  // open: nQ
  and and_12 (and_12_out, 1'b1, 1'b1, nor_2_out, \BΦ2 );
  ROM #(.AddrBits(11), .Bits(8)) F000 (.A(d_ff_2_q), .sel(and_12_out), .D(D));
  nor nor_3 (nor_3_out, 1'b0, nSELE, BA[11]);
  D_FF #(.Bits(11)) d_ff_3 (.D(BA[10:0]), .C(\BΦ2 ), .Q(d_ff_3_q));  // open: nQ
  and and_13 (and_13_out, 1'b1, 1'b1, nor_3_out, \BΦ2 );
  ROM #(.AddrBits(11), .Bits(8)) E000 (.A(d_ff_3_q), .sel(and_13_out), .D(D));
  nor nor_4 (nor_4_out, 1'b0, nSELD, 1'b0);
  D_FF #(.Bits(11)) d_ff_4 (.D(BA[10:0]), .C(\BΦ2 ), .Q(d_ff_4_q));  // open: nQ
  and and_14 (and_14_out, BA[11], 1'b1, nor_4_out, \BΦ2 );
  ROM #(.AddrBits(11), .Bits(8)) D800 (.A(d_ff_4_q), .sel(and_14_out), .D(D));
  _6550_layout_3 _0C00_0FFF (
    .A0_A9(BA[9:0]), .\Φ2 (\BΦ2 ), .R_nW(RW_nE), .D3(BBD7), .D2(BBD6), .D1(BBD5), .D0(BBD4), .CS1(BA[10]),
    .CS2(BA[11]), .nCS3(nSEL0), .nCS4(1'b0));
  _6550_layout_3 _0C00_0FFF_2 (
    .A0_A9(BA[9:0]), .\Φ2 (\BΦ2 ), .R_nW(RW_nE), .D3(BBD3), .D2(BBD2), .D1(BBD1), .D0(BBD0), .CS1(BA[10]),
    .CS2(BA[11]), .nCS3(nSEL0), .nCS4(1'b0));
  nor nor_5 (nor_5_out, 1'b0, nSELD, BA[11]);
  D_FF #(.Bits(11)) d_ff_5 (.D(BA[10:0]), .C(\BΦ2 ), .Q(d_ff_5_q));  // open: nQ
  and and_15 (and_15_out, 1'b1, 1'b1, nor_5_out, \BΦ2 );
  ROM #(.AddrBits(11), .Bits(8)) D000 (.A(d_ff_5_q), .sel(and_15_out), .D(D));
  _6550_layout_3 _0800_0BFF (
    .A0_A9(BA[9:0]), .\Φ2 (\BΦ2 ), .R_nW(RW_nE), .D3(BBD7), .D2(BBD6), .D1(BBD5), .D0(BBD4), .CS1(1'b1),
    .CS2(BA[11]), .nCS3(nSEL0), .nCS4(BA[10]));
  _6550_layout_3 _0800_0BFF_2 (
    .A0_A9(BA[9:0]), .\Φ2 (\BΦ2 ), .R_nW(RW_nE), .D3(BBD3), .D2(BBD2), .D1(BBD1), .D0(BBD0), .CS1(1'b1),
    .CS2(BA[11]), .nCS3(nSEL0), .nCS4(BA[10]));
  nor nor_6 (nor_6_out, 1'b0, nSELC, 1'b0);
  D_FF #(.Bits(11)) d_ff_6 (.D(BA[10:0]), .C(\BΦ2 ), .Q(d_ff_6_q));  // open: nQ
  and and_16 (and_16_out, BA[11], 1'b1, nor_6_out, \BΦ2 );
  ROM #(.AddrBits(11), .Bits(8)) C800 (.A(d_ff_6_q), .sel(and_16_out), .D(D));
  _6550_layout_3 _0400_07FF (
    .A0_A9(BA[9:0]), .\Φ2 (\BΦ2 ), .R_nW(RW_nE), .D3(BBD7), .D2(BBD6), .D1(BBD5), .D0(BBD4), .CS1(1'b1),
    .CS2(BA[10]), .nCS3(nSEL0), .nCS4(BA[11]));
  _6550_layout_3 _0400_07FF_2 (
    .A0_A9(BA[9:0]), .\Φ2 (\BΦ2 ), .R_nW(RW_nE), .D3(BBD3), .D2(BBD2), .D1(BBD1), .D0(BBD0), .CS1(1'b1),
    .CS2(BA[10]), .nCS3(nSEL0), .nCS4(BA[11]));
  _6550_layout_3 _0000_03FF (
    .A0_A9(BA[9:0]), .\Φ2 (\BΦ2 ), .R_nW(RW_nE), .D3(BBD7), .D2(BBD6), .D1(BBD5), .D0(BBD4), .CS1(1'b1),
    .CS2(nBA11), .nCS3(nSEL0), .nCS4(BA[10]));
  _6550_layout_3 _0000_03FF_2 (
    .A0_A9(BA[9:0]), .\Φ2 (\BΦ2 ), .R_nW(RW_nE), .D3(BBD3), .D2(BBD2), .D1(BBD1), .D0(BBD0), .CS1(1'b1),
    .CS2(nBA11), .nCS3(nSEL0), .nCS4(BA[10]));
  nor nor_7 (nor_7_out, 1'b0, nSELC, BA[11]);
  D_FF #(.Bits(11)) d_ff_7 (.D(BA[10:0]), .C(\BΦ2 ), .Q(d_ff_7_q));  // open: nQ
  and and_17 (and_17_out, 1'b1, 1'b1, nor_7_out, \BΦ2 );
  ROM #(.AddrBits(11), .Bits(8)) C000 (.A(d_ff_7_q), .sel(and_17_out), .D(D));

  // Other names for the same wires on the sheet: A12 = BA[12]; A13 = BA[13]; A14 = BA[14]; A15 = BA[15];
  //   VIDEO_ON = SYNC

  // Notes on the sheet:
  //   _8MHz: Hz: 2147483647
  //   1 - Computer Main Logic
  //   3 - Main Logic / Video Logic
  //   DEBUG
  //   Breakpoint
  //   2 - Memory Section
  //   Jumper for
  //   8k only
  //   6540
  //   contents of F800 (hex, n*v repeats v):
  //   d0,4,a0,94,d0,97,8d,64,2,4c,77,f2,48,20,ba,f0,a5,f0,10,6,20,32
  //   ,f1,4c,21,f8,29,1f,9,60,20,2c,f1,ad,c,2,10,3,4c,7d,f4,68,4c,6
  //   ,f8,20,67,f6,a6,f1,fe,70,2,bc,70,2,c0,c0,60,20,5e,f8,f0,30,a0
  //   ,41,20,de,e7,a0,56,20,de,e7,a5,f1,9,30,20,ea,e3,20,39,f3,20,5e
  //   ,f8,d0,f8,a0,aa,4c,de,e7,a9,10,a6,f1,e0,1,f0,2,a9,20,2c,10,e8
  //   ,d0,3,2c,10,e8,60,20,5e,f8,f0,fa,a0,41,20,de,e7,a0,4d,d0,c3,a9
  //   ,0,8d,c,2,8d,b,2,20,7d,f6,20,13,f9,20,3b,f8,78,a9,0,8d,78,2,85
  //   ,eb,85,e7,8d,76,2,8d,77,2,8d,66,2,a2,e,20,1b,fd,a6,f1,ca,f0,7
  //   ,a9,90,8d,4e,e8,d0,1e,ee,11,e8,d0,19,20,7d,f6,20,13,f9,a9,14,8d
  //   ,79,2,20,71,f8,78,a9,a0,8d,4e,e8,a2,8,20,1b,fd,a9,2,85,fd,20,ec
  //   ,fb,ce,13,e8,a6,f1,ca,d0,a,a9,34,8d,13,e8,8d,7,2,d0,b,ad,40,e8
  //   ,8e,8,2,29,ef,8d,40,e8,8d,49,e8,58,a9,e6,cd,1a,2,f0,11,20,1e,f9
  //   ,2c,13,e8,10,f1,2c,12,e8,20,36,f7,4c,fa,f8,60,20,1e,f9,a9,e6,cd
  //   ,1a,2,d0,f6,60,20,2a,f3,d0,8,8,20,fb,fc,20,99,f2,28,4c,1c,c7,86
  //   ,e8,a5,e7,a,a,18,65,e7,18,65,e8,85,e8,a9,0,24,e7,30,1,2a,6,e8
  //   ,2a,6,e8,2a,aa,ad,48,e8,c9,15,90,f9,65,e8,8d,44,e8,8a,6d,49,e8
  //   ,8d,45,e8,58,60,ae,49,e8,a0,ff,98,ed,48,e8,ec,49,e8,d0,f2,86,e8
  //   ,aa,8c,48,e8,8c,49,e8,98,e5,e8,86,e8,4a,66,e8,4a,66,e8,a5,e7,18
  //   ,69,3c,2c,40,e8,2c,10,e8,c5,e8,b0,55,ae,66,2,f0,3,4c,a3,fa,ae
  //   ,6c,2,30,1b,a2,0,69,30,65,e7,c5,e8,b0,1e,e8,69,26,65,e7,c5,e8
  //   ,b0,1b,69,2c,65,e7,c5,e8,90,3,4c,4a,fa,ea,a5,eb,f0,25,8d,74,2
  //   ,d0,20,ee,75,2,b0,4,ea,ce,75,2,38,e9,13,e5,e8,6d,a,2,8d,a,2,ad
  //   ,6f,2,49,1,8d,6f,2,f0,24,86,f6,a5,eb,f0,1b,2c,4d,e8,50,16,a9,0
  //   ,8d,6f,2,ad,6c,2,10,36,30,be,a2,a6,20,2e,f9,ad,65,2,d0,b8,4c,7e
  //   ,e6,ad,a,2,f0,8,30,4,c6,e7,c6,e7,e6,e7,a9,0,8d,a,2,e4,f6,d0,11
  //   ,8a,d0,9c,ad,75,2,30,c0,c9,10,90,bc,8d,28,2,b0,b7,8a,4d,65,2,8d
  //   ,65,2,a5,eb,f0,cb,ce,6c,2,30,bc,46,f6,66,fe,a2,da,20,2e,f9,4c
  //   ,7e,e6,ad,28,2,f0,4,a5,eb,f0,8,ad,6c,2,30,3,4c,ca,f9,46,e8,a9
  //   ,93,38,e5,e8,65,e7,a,aa,20,2e,f9,ee,66,2,a5,eb,d0,14,ad,28,2,f0
  //   ,2b,8d,74,2,a9,0,8d,28,2,a9,c0,8d,4e,e8,85,eb,ad,28,2,85,ec,f0
  //   ,9,a9,0,85,eb,a9,40,8d,4e,e8,a5,fe,85,fc,ad,74,2,d,75,2,85,ed
  //   ,4c,7e,e6,20,ec,fb,8d,66,2,a2,da,20,2e,f9,a5,fd,f0,3,8d,73,2,a9
  //   ,f,2c,78,2,10,18,a5,ec,d0,c,a6,fd,ca,d0,c,a9,8,20,e5,fb,d0,5,a9
  //   ,0,8d,78,2,4c,7e,e6,70,37,d0,1a,a5,ec,d0,f5,a5,ed,d0,f1,ad,73
  //   ,2,4a,a5,fc,30,3,90,1c,18,b0,19,29,f,8d,78,2,ce,78,2,d0,da,a9
  //   ,40,8d,78,2,20,dc,fb,a9,0,8d,79,2,f0,cb,a9,80,8d,78,2,d0,c4,a5
  //   ,ec,f0,a,a9,4,20,e5,fb,a9,0,4c,a7,fb,20,90,fd,d0,3,4c,a5,fb,ae
  //   ,73,2,ca,f0,31,ad,b,2,f0,c,a0,0,a5,fc,d1,e3,f0,4,a9,1,85,ed,a5
  //   ,ed,f0,54,a2,3d,ec,76,2,90,46,ae,76,2,a5,e4,9d,1,1,a5,e3,9d,0
  //   ,1,e8,e8,8e,76,2,4c,92,fb,ae,77,2,ec,76,2,f0,3b,a5,e3,dd,0,1,d0
  //   ,34,a5,e4,dd,1,1,d0,2d,ee,77,2,ee,77,2,ad,b,2,f0,c,a5,fc,a0,0
  //   ,d1,e3,f0,1a,a9,1,85,ed,a5,ed,f0,7,a9,10,20,e5,fb,d0,b,ad,b,2
  //   ,d0,6,a5,fc,a0,0,91,e3,e6,e3,d0,38,e6,e4,d0,34,a9,80,8d,78,2,a6
  //   ,fd,ca,30,2,86,fd,ce,73,2,f0,9,ad,76,2,d0,1e,85,fd,f0,1a,20,fb
  //   ,fc,20,dc,fb,a0,0,8c,79,2,20,7c,fd,ad,79,2,45,fc,f0,5,a9,20,20
  //   ,e5,fb,4c,7e,e6,a5,f8,85,e4,a5,f7,85,e3,60,d,c,2,8d,c,2,60,a9
  //   ,8,8d,6c,2,a9,0,8d,6f,2,8d,74,2,8d,65,2,8d,75,2,60,a5,fc,4a,a9
  //   ,60,90,2,a9,b0,a2,0,8d,48,e8,8e,49,e8,ad,40,e8,49,8,8d,40,e8,29
  //   ,8,60,38,66,e4,30,44,ad,74,2,d0,13,a9,10,a2,1,20,b,fc,d0,36,ee
  //   ,74,2,a5,e4,10,2f,4c,bb,fc,ad,75,2,d0,a,20,7,fc,d0,22,ee,75,2
  //   ,d0,1d,20,0,fc,d0,18,ad,6f,2,49,1,8d,6f,2,f0,11,a5,fc,49,1,85
  //   ,fc,29,1,4d,65,2,8d,65,2,4c,7e,e6,46,fc,ce,6c,2,ad,6c,2,f0,3f
  //   ,10,f1,20,ec,fb,58,ad,70,2,f0,13,a2,0,86,f6,ce,70,2,a6,fd,e0,2
  //   ,d0,2,9,80,85,fc,d0,d5,20,90,fd,90,a,d0,85,e6,e4,a5,f6,85,fc,b0
  //   ,c6,a0,0,b1,e3,85,fc,45,f6,85,f6,e6,e3,d0,b8,e6,e4,d0,b4,ad,65
  //   ,2,49,1,85,fc,4c,7e,e6,c6,fd,d0,3,20,ed,ff,a9,50,8d,73,2,a2,8
  //   ,78,20,1b,fd,d0,e9,a9,78,20,9,fc,d0,e2,ce,73,2,d0,dd,20,ec,fb
  //   ,ce,79,2,10,d5,a2,a,20,1b,fd,58,ee,79,2,a5,fd,f0,26,20,dc,fb,a2
  //   ,9,8e,70,2,4c,74,fc,8,78,20,ed,ff,a9,7f,8d,4e,e8,a9,3c,8d,11,e8
  //   ,a9,3d,8d,13,e8,a2,c,20,1b,fd,28,60,20,fb,fc,f0,9d,bd,28,fd,8d
  //   ,19,2,bd,29,fd,8d,1a,2,60,c2,fd,80,fe,0,0,9e,fe,cf,fc,21,fc,85
  //   ,e6,5f,f9,a2,ff,9a,d8,20,e1,e1,ad,10,e8,10,57,58,4c,d2,e0,84,0
  //   ,84,1,a0,3,98,18,65,1,45,2,91,0,c8,d0,f5,e6,1,e4,1,d0,ef,84,0
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  //   contents of F000 (hex, n*v repeats v):
  //   54,4f,4f,20,4d,41,4e,59,20,46,49,4c,45,d3,46,49,4c,45,20,4f,50
  //   ,45,ce,46,49,4c,45,20,4e,4f,54,20,4f,50,45,ce,46,49,4c,45,20,4e
  //   ,4f,54,20,46,4f,55,4e,c4,d,53,45,41,52,43,48,49,4e,47,a0,46,4f
  //   ,52,a0,d,50,52,45,53,53,20,50,4c,41,59,a0,26,20,52,45,43,4f,52
  //   ,44,a0,4f,4e,20,54,41,50,45,20,a3,d,4c,4f,41,c4,d,57,52,49,54
  //   ,49,4e,47,a0,d,56,45,52,49,46,d9,44,45,56,49,43,45,20,4e,4f,54
  //   ,20,50,52,45,53,45,4e,d4,4e,4f,54,20,49,4e,50,55,54,20,46,49,4c
  //   ,c5,4e,4f,54,20,4f,55,54,50,55,54,20,46,49,4c,c5,d,46,4f,55,4e
  //   ,44,a0,d,4f,4b,8d,d,52,45,41,44,59,2e,8d,a9,40,d0,2,a9,20,48,ad
  //   ,40,e8,9,2,8d,40,e8,a9,3c,8d,21,e8,2c,1d,2,f0,12,a9,34,8d,11,e8
  //   ,20,f1,f0,a9,0,8d,1d,2,a9,3c,8d,11,e8,68,5,f1,8d,22,2,ad,40,e8
  //   ,10,fb,29,fb,8d,40,e8,a9,3c,8d,23,e8,ad,40,e8,29,41,c9,41,f0,43
  //   ,ad,22,2,49,ff,8d,22,e8,2c,40,e8,50,fb,a9,34,8d,23,e8,a9,ff,8d
  //   ,45,e8,ad,40,e8,2c,4d,e8,70,1d,4a,90,f5,a9,3c,8d,23,e8,a9,ff,8d
  //   ,22,e8,60,8d,22,2,20,f1,f0,ad,40,e8,9,4,8d,40,e8,60,a9,1,20,e5
  //   ,fb,d0,df,a9,80,30,f7,a9,2,20,e5,fb,ad,40,e8,29,fd,8d,40,e8,a9
  //   ,34,8d,21,e8,a9,d,60,8d,22,2,20,f1,f0,20,4b,f1,4c,32,f1,2c,1d
  //   ,2,30,5,ce,1d,2,d0,5,48,20,f1,f0,68,8d,22,2,60,a9,5f,d0,2,a9,3f
  //   ,85,f1,20,bc,f0,d0,ab,a9,34,8d,21,e8,ad,40,e8,9,2,8d,40,e8,a9
  //   ,ff,8d,45,e8,2c,4d,e8,70,a8,2c,40,e8,30,f6,ad,40,e8,29,fd,8d,40
  //   ,e8,2c,10,e8,70,5,a9,40,20,e5,fb,ad,20,e8,49,ff,48,a9,3c,8d,21
  //   ,e8,2c,40,e8,10,fb,a9,34,8d,21,e8,68,60,a9,0,8d,c,2,ad,63,2,d0
  //   ,1b,ad,d,2,f0,51,78,4c,7d,e2,ad,63,2,d0,d,a5,e2,8d,21,2,a5,f5
  //   ,8d,20,2,4c,fa,e2,c9,3,d0,b,8d,60,2,a5,f2,8d,1e,2,4c,fa,e2,b0
  //   ,25,8e,61,2,20,2d,f8,d0,e,20,7f,f8,a0,0,98,a6,f1,9d,70,2,4c,5
  //   ,f2,b1,f3,d0,7,a9,40,20,e5,fb,d0,e2,ae,61,2,60,ad,c,2,f0,1,60
  //   ,4c,87,f1,48,ad,64,2,d0,3,4c,79,c3,c9,3,d0,4,68,4c,ea,e3,30,4
  //   ,68,4c,67,f1,68,85,e9,c9,1d,d0,5,ee,6a,2,f0,d9,c9,a,f0,d5,48,8a
  //   ,48,98,48,20,2d,f8,d0,12,20,b9,f8,a6,f1,a9,1,9d,70,2,20,e3,f5
  //   ,a9,2,91,f3,c8,a5,e9,91,f3,68,a8,68,aa,68,60,ad,64,2,f0,9,c9,3
  //   ,f0,5,30,3,20,7e,f1,ad,63,2,f0,9,c9,3,f0,5,30,3,20,7a,f1,a9,0
  //   ,8d,63,2,a9,3,8d,64,2,60,a9,0,8d,62,2,f0,d2,ae,62,2,ca,30,16,dd
  //   ,42,2,f0,11,d0,f6,bd,42,2,85,ef,bd,4c,2,85,f1,bd,56,2,85,f0,60
  //   ,20,d4,f4,a5,ef,20,ab,f2,d0,57,20,b8,f2,8a,48,a5,f1,f0,2f,c9,3
  //   ,f0,2b,b0,26,a5,f0,f0,25,20,67,f6,a2,2,bd,4,f3,20,48,f2,ca,10
  //   ,f7,20,b9,f8,a5,f0,c9,2,d0,e,a9,5,20,ed,f5,4c,a,f3,d,31,0,20,e6
  //   ,f6,68,aa,ce,62,2,ec,62,2,f0,15,ac,62,2,b9,42,2,9d,42,2,b9,4c
  //   ,2,9d,4c,2,b9,56,2,9d,56,2,60,ad,9,2,c9,ef,d0,7,8,a9,0,8d,d,2
  //   ,28,60,20,2a,f3,4c,1c,c7,a5,ca,d0,f5,4c,de,e7,a9,0,8d,b,2,20,33
  //   ,f4,a9,ff,cd,9,2,d0,fb,cd,9,2,d0,f6,a9,4,85,f8,a9,0,85,f7,a5,f1
  //   ,d0,3,4c,1c,ce,c9,3,f0,f9,90,36,20,1c,f7,20,ff,f3,20,62,f4,20
  //   ,b6,f0,20,22,f4,20,39,f3,20,87,f1,ae,c,2,30,43,ac,b,2,f0,c,88
  //   ,d1,f7,f0,9,a2,2,8e,c,2,d0,2,91,f7,e6,f7,d0,de,e6,f8,4c,7e,f3
  //   ,20,67,f6,20,3b,f8,20,ff,f3,a5,ee,f0,8,20,95,f4,d0,8,4c,79,f5
  //   ,20,ae,f5,f0,f8,e0,1,d0,eb,20,4d,f6,20,22,f4,20,8a,f8,ad,b,2,d0
  //   ,50,20,13,f9,ad,c,2,29,10,f0,a,a0,0,8c,d,2,a0,60,4c,7b,f5,a0,ae
  //   ,20,3f,f3,a5,ca,d0,b,a5,e6,85,7d,a5,e5,85,7c,4c,30,c4,20,9a,c5
  //   ,4c,81,c5,a5,ca,d0,1e,a0,32,20,de,e7,a5,ee,f0,15,a0,3d,20,de,e7
  //   ,a4,ee,f0,c,a0,0,b1,f9,20,ea,e3,c8,c4,ee,d0,f6,60,a0,5f,ad,b,2
  //   ,f0,2,a0,6d,20,3f,f3,a0,39,4c,3f,f3,a2,0,8e,c,2,86,e5,86,ee,86
  //   ,f0,e8,86,f1,a9,4,86,e6,20,15,f5,20,4,f5,20,15,f5,20,5c,f4,86
  //   ,f1,20,15,f5,20,5c,f4,86,f0,60,20,1d,f5,4c,76,d6,a5,f0,30,f5,a4
  //   ,ee,f0,f1,20,ba,f0,a5,f0,9,40,85,f0,9,f0,20,2c,f1,ad,c,2,10,5
  //   ,a0,74,4c,7b,f5,a5,ee,f0,c,a0,0,b1,f9,20,67,f1,c8,c4,ee,d0,f6
  //   ,4c,7e,f1,20,ae,f5,f0,20,a0,5,8c,68,2,a0,0,84,e9,c4,ee,f0,12,b1
  //   ,f9,ac,68,2,d1,f3,d0,e5,e6,e9,ee,68,2,a4,e9,d0,ea,98,60,a9,1,8d
  //   ,b,2,20,4b,f3,ad,c,2,29,10,f0,5,a0,6e,4c,7b,f5,a0,aa,4c,de,e7
  //   ,a2,0,86,f0,8e,c,2,86,ee,e8,86,f1,20,22,f5,20,76,d6,86,ef,20,15
  //   ,f5,20,5c,f4,86,f1,e0,3,90,2,c6,f0,20,15,f5,20,5c,f4,86,f0,20
  //   ,15,f5,20,1d,f5,20,b8,cc,20,7b,d5,85,ee,a5,71,85,f9,a5,72,85,fa
  //   ,60,20,c8,0,d0,2,68,68,60,a9,2c,20,13,ce,20,c8,0,d0,f5,4c,1c,ce
  //   ,20,d4,f4,a5,ef,d0,3,4c,1c,ce,20,ab,f2,d0,4,a0,e,d0,3e,ae,62,2
  //   ,a0,0,8c,c,2,e0,a,f0,f2,ee,62,2,a5,ef,9d,42,2,a5,f0,9d,56,2,a5
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  //   contents of E000 (hex, n*v repeats v):
  //   a6,a0,0,20,74,da,a9,0,85,b5,a5,63,20,16,e0,a9,9d,a0,0,4c,e1,d9
  //   ,48,4c,d7,df,81,49,f,da,a2,83,49,f,da,a2,7f,4*0,5,84,e6,1a,2d
  //   ,1b,86,28,7,fb,f8,87,99,68,89,1,87,23,35,df,e1,86,a5,5d,e7,28
  //   ,83,49,f,da,a2,a5,b5,48,10,3,20,67,de,a5,b0,48,c9,81,90,7,a9,91
  //   ,a0,d8,20,e1,d9,a9,78,a0,e0,20,f3,de,68,c9,81,90,7,a9,1a,a0,e0
  //   ,20,25,d7,68,10,3,4c,67,de,60,b,76,b3,83,bd,d3,79,1e,f4,a6,f5
  //   ,7b,83,fc,b0,10,7c,c,1f,67,ca,7c,de,53,cb,c1,7d,14,64,70,4c,7d
  //   ,b7,ea,51,7a,7d,63,30,88,7e,7e,92,44,99,3a,7e,4c,cc,91,c7,7f,aa,aa,aa
  //   ,13,81,4*0,e6,c9,d0,2,e6,ca,ad,60,ea,c9,3a,b0,a,c9,20,f0,ef,38
  //   ,e9,30,38,e9,d0,60,80,4f,c7,52,59,a2,ff,86,89,9a,a9,4c,85,a3,85
  //   ,0,a9,30,a0,d1,85,1,84,2,a2,1c,bd,b4,e0,95,c1,ca,d0,f8,8a,85,b7
  //   ,85,3,85,67,85,4,85,5,48,85,64,a9,3,85,a2,a9,2c,85,9,20,d2,c9
  //   ,a2,68,86,65,a9,0,a0,4,85,8,84,9,a0,0,e6,8,d0,8,e6,9,a5,9,c9,80
  //   ,f0,f,a9,92,91,8,d1,8,d0,7,a,91,8,d1,8,f0,e5,a5,8,a4,9,85,86,84
  //   ,87,85,82,84,83,a2,0,a0,4,86,7a,84,7b,a0,0,98,91,7a,e6,7a,d0,2
  //   ,e6,7b,a5,7a,a4,7b,20,2a,c3,20,d2,c9,a5,86,38,e5,7a,aa,a5,87,e5
  //   ,7b,20,9f,dc,a9,74,a0,e1,20,27,ca,20,53,c5,4c,8b,c3,20,42,59,54
  //   ,45,53,20,46,52,45,45,13,2a,2a,2a,20,43,4f,4d,4d,4f,44,4f,52,45
  //   ,20,42,41,53,49,43,20,2a,2a,2a,11,11,11,0,18,4c,2b,c7,24,b4,10
  //   ,7,c9,54,d0,3,4c,3b,ce,60,24,b4,30,3,4c,90,ce,c9,54,f0,3,4c,82
  //   ,ce,4c,69,ce,85,5a,e8,4c,d9,e1,10,5,a5,8e,a4,8f,60,a0,ff,60,d0
  //   ,a,e6,5,d0,6,a5,e2,85,5,d0,f6,60,86,c9,68,68,98,4c,88,cb,a9,7f
  //   ,8d,4e,e8,85,6,85,7,a2,0,8a,9d,0,2,ca,d0,fa,ca,a9,85,8d,19,2,a9
  //   ,e6,8d,1a,2,a9,3,8d,64,2,a9,f,8d,10,e8,a,8d,40,e8,8d,42,e8,8e
  //   ,22,e8,8e,45,e8,a9,3d,8d,13,e8,2c,12,e8,a9,3c,8d,21,e8,8d,23,e8
  //   ,8d,11,e8,8e,22,e8,a9,c,8d,4c,e8,8d,25,2,8d,24,2,a0,0,8c,e,2,84
  //   ,e0,a9,84,85,e1,a9,20,c6,e1,91,e0,88,d0,fb,a5,e1,c9,80,d0,f1,a9
  //   ,80,a2,19,9d,28,2,ca,d0,fa,a0,12,20,73,e2,a0,c,20,73,e2,a0,5,20
  //   ,73,e2,a0,0,84,e2,84,f5,20,db,e5,60,a2,18,fe,29,2,ca,88,d0,f9
  //   ,60,ac,f,2,a2,0,bd,10,2,9d,f,2,e8,ec,d,2,d0,f4,ce,d,2,98,58,60
  //   ,20,ea,e3,ad,d,2,8d,24,2,f0,f8,78,ad,27,2,f0,b,ad,26,2,a0,0,8c
  //   ,27,2,20,ac,e7,20,7d,e2,c9,83,d0,11,78,a2,9,8e,d,2,bd,d4,e7,9d
  //   ,e,2,ca,d0,f7,f0,cf,c9,d,d0,c8,a4,f2,8c,60,2,b1,e0,c9,20,d0,3
  //   ,88,d0,f7,c8,8c,1e,2,a0,0,84,e2,84,ea,ad,20,2,30,1a,c5,f5,d0,16
  //   ,ad,21,2,85,e2,cd,1e,2,90,c,4c,27,e3,98,48,8a,48,ad,60,2,f0,94
  //   ,a4,e2,b1,e0,85,f6,29,3f,6,f6,24,f6,10,2,9,80,90,4,a6,ea,d0,4
  //   ,70,2,9,40,e6,e2,20,49,e3,cc,1e,2,d0,13,a9,0,8d,60,2,a9,d,ae,64
  //   ,2,e0,3,f0,3,20,ea,e3,a9,d,85,f6,68,aa,68,a8,a5,f6,c9,de,d0,2
  //   ,a9,ff,60,c9,22,d0,8,a5,ea,49,1,85,ea,a9,22,60,9,40,ae,e,2,f0
  //   ,2,9,80,a6,fb,f0,2,c6,fb,20,ac,e7,e6,e2,a4,f2,c4,e2,b0,1a,a6,f5
  //   ,c0,4f,d0,d,20,97,e3,20,30,e5,a9,0,85,e2,4c,8a,e3,e0,18,d0,1d
  //   ,20,aa,e3,68,a8,a5,fb,f0,2,46,ea,68,aa,68,58,60,e0,17,b0,8,bd
  //   ,2b,2,9,80,9d,2b,2,60,20,b1,e3,4c,8a,e3,20,59,e5,c6,f5,a6,f5,1e
  //   ,2a,2,5e,2a,2,20,97,e3,a5,e2,48,20,db,e5,68,85,e2,60,a0,27,a6
  //   ,f5,d0,6,86,e2,68,68,d0,ba,bd,28,2,30,6,ca,bd,28,2,a0,4f,ca,86
  //   ,f5,85,e1,bd,bc,e7,85,e0,84,e2,84,f2,60,48,85,f6,8a,48,98,48,a9
  //   ,0,8d,60,2,a4,e2,a5,f6,10,3,4c,8f,e4,c9,d,d0,3,4c,48,e5,c9,20
  //   ,90,8,29,3f,20,49,e3,4c,58,e3,a6,fb,f0,3,4c,5d,e3,c9,14,d0,1c
  //   ,88,84,e2,10,6,20,c4,e3,4c,33,e4,c8,b1,e0,88,91,e0,c8,c4,f2,d0
  //   ,f5,a9,20,91,e0,d0,3d,a6,ea,f0,3,4c,5d,e3,c9,12,d0,3,8d,e,2,c9
  //   ,13,d0,3,20,69,e2,c9,1d,d0,12,c8,84,e2,88,c4,f2,90,7,20,30,e5
  //   ,a0,0,84,e2,4c,8a,e3,c9,11,d0,e,18,98,69,28,a8,c5,f2,90,ee,f0
  //   ,ec,20,30,e5,4c,8a,e3,e8,85,f5,98,e9,28,85,e2,e6,f5,ad,bc,e7,85
  //   ,e0,ad,29,2,85,e1,d0,e7,29,7f,c9,7f,d0,2,a9,5e,c9,20,90,3,4c,56
  //   ,e3,c9,d,d0,3,4c,48,e5,a6,ea,d0,30,c9,14,d0,28,a4,f2,b1,e0,c9
  //   ,20,d0,4,c4,e2,d0,7,c0,4f,f0,b9,20,5,e6,a4,f2,88,b1,e0,c8,91,e0
  //   ,88,c4,e2,d0,f5,a9,20,91,e0,e6,fb,d0,58,a6,fb,f0,5,9,40,4c,5d
  //   ,e3,c9,11,d0,2c,a5,e2,c9,28,90,6,e9,28,85,e2,b0,3f,a6,f5,f0,3b
  //   ,bd,28,2,10,7,c6,f5,20,db,e5,90,2f,ca,ca,86,f5,20,db,e5,a5,e2
  //   ,18,69,28,85,e2,d0,1f,c9,12,d0,5,a9,0,8d,e,2,c9,1d,d0,b,88,84
  //   ,e2,10,d,20,c4,e3,4c,8a,e3,c9,13,d0,3,20,36,e2,4c,8a,e3,38,4e
  //   ,20,2,a6,f5,e8,e0,19,d0,3,20,59,e5,bd,29,2,10,f3,86,f5,4c,db,e5
  //   ,a9,0,85,fb,8d,e,2,85,ea,85,e2,20,30,e5,4c,8a,e3,78,a0,0,84,e0
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  //   contents of D800 (hex, n*v repeats v):
  //   38,e5,b0,b0,c7,49,ff,69,1,85,b0,90,e,e6,b0,f0,42,66,b1,66,b2,66
  //   ,b3,66,b4,66,bf,60,a5,b5,49,ff,85,b5,a5,b1,49,ff,85,b1,a5,b2,49
  //   ,ff,85,b2,a5,b3,49,ff,85,b3,a5,b4,49,ff,85,b4,a5,bf,49,ff,85,bf
  //   ,e6,bf,d0,e,e6,b4,d0,a,e6,b3,d0,6,e6,b2,d0,2,e6,b1,60,a2,4a,4c
  //   ,59,c3,a2,74,b4,4,84,bf,b4,3,94,4,b4,2,94,3,b4,1,94,2,a4,b7,94
  //   ,1,69,8,30,e8,f0,e6,e9,8,a8,a5,bf,b0,14,16,1,90,2,f6,1,76,1,76
  //   ,1,76,2,76,3,76,4,6a,c8,d0,ec,18,60,81,4*0,3,7f,5e,56,cb,79,80
  //   ,13,9b,b,64,80,76,38,93,16,82,38,aa,3b,20,80,35,4,f3,34,81,35
  //   ,4,f3,34,80,80,0,0,0,80,31,72,17,f8,20,fd,da,f0,2,10,3,4c,30,d1
  //   ,a5,b0,e9,7f,48,a9,80,85,b0,a9,ab,a0,d8,20,3c,d7,a9,b0,a0,d8,20
  //   ,e1,d9,a9,91,a0,d8,20,25,d7,a9,96,a0,d8,20,f3,de,a9,b5,a0,d8,20
  //   ,3c,d7,68,20,50,dc,a9,ba,a0,d8,20,5e,d9,f0,5b,20,89,d9,a9,0,85
  //   ,75,85,76,85,77,85,78,a5,bf,20,2b,d9,a5,b4,20,2b,d9,a5,b3,20,2b
  //   ,d9,a5,b2,20,2b,d9,a5,b1,20,30,d9,4c,61,da,d0,3,4c,58,d8,4a,9
  //   ,80,a8,90,19,18,a5,78,65,bc,85,78,a5,77,65,bb,85,77,a5,76,65,ba
  //   ,85,76,a5,75,65,b9,85,75,66,75,66,76,66,77,66,78,66,bf,98,4a,d0
  //   ,d6,60,85,71,84,72,a0,4,b1,71,85,bc,88,b1,71,85,bb,88,b1,71,85
  //   ,ba,88,b1,71,85,bd,45,b5,85,be,a5,bd,9,80,85,b9,88,b1,71,85,b8
  //   ,a5,b0,60,a5,b8,f0,1f,18,65,b0,90,4,30,1d,18,2c,10,14,69,80,85
  //   ,b0,d0,3,4c,d0,d7,a5,be,85,b5,60,a5,b5,49,ff,30,5,68,68,4c,cc
  //   ,d7,4c,53,d8,20,de,da,aa,f0,10,18,69,2,b0,f2,a2,0,86,be,20,4c
  //   ,d7,e6,b0,f0,e7,60,84,20,0,0,0,20,de,da,a9,cb,a0,d9,a2,0,86,be
  //   ,20,74,da,4c,e4,d9,20,5e,d9,f0,76,20,ed,da,a9,0,38,e5,b0,85,b0
  //   ,20,89,d9,e6,b0,f0,ba,a2,fc,a9,1,a4,b9,c4,b1,d0,10,a4,ba,c4,b2
  //   ,d0,a,a4,bb,c4,b3,d0,4,a4,bc,c4,b4,8,2a,90,9,e8,95,78,f0,32,10
  //   ,34,a9,1,28,b0,e,6,bc,26,bb,26,ba,26,b9,b0,e6,30,ce,10,e2,a8,a5
  //   ,bc,e5,b4,85,bc,a5,bb,e5,b3,85,bb,a5,ba,e5,b2,85,ba,a5,b9,e5,b1
  //   ,85,b9,98,4c,21,da,a9,40,d0,ce,6*a,85,bf,28,4c,61,da,a2,8a,4c
  //   ,59,c3,a5,75,85,b1,a5,76,85,b2,a5,77,85,b3,a5,78,85,b4,4c,ac,d7
  //   ,85,71,84,72,a0,4,b1,71,85,b4,88,b1,71,85,b3,88,b1,71,85,b2,88
  //   ,b1,71,85,b5,9,80,85,b1,88,b1,71,85,b0,84,bf,60,a2,ab,2c,a2,a6
  //   ,a0,0,f0,4,a6,98,a4,99,20,ed,da,86,71,84,72,a0,4,a5,b4,91,71,88
  //   ,a5,b3,91,71,88,a5,b2,91,71,88,a5,b5,9,7f,25,b1,91,71,88,a5,b0
  //   ,91,71,84,bf,60,a5,bd,85,b5,a2,5,b5,b7,95,af,ca,d0,f9,86,bf,60
  //   ,20,ed,da,a2,6,b5,af,95,b7,ca,d0,f9,86,bf,60,a5,b0,f0,fb,6,bf
  //   ,90,f7,20,44,d8,d0,f2,4c,d,d8,a5,b0,f0,9,a5,b5,2a,a9,ff,b0,2,a9
  //   ,1,60,20,fd,da,85,b1,a9,0,85,b2,a2,88,a5,b1,49,ff,2a,a9,0,85,b4
  //   ,85,b3,86,b0,85,bf,85,b5,4c,a7,d7,46,b5,60,85,73,84,74,a0,0,b1
  //   ,73,c8,aa,f0,c4,b1,73,45,b5,30,c2,e4,b0,d0,21,b1,73,9,80,c5,b1
  //   ,d0,19,c8,b1,73,c5,b2,d0,12,c8,b1,73,c5,b3,d0,b,c8,a9,7f,c5,bf
  //   ,b1,73,e5,b4,f0,28,a5,b5,90,2,49,ff,4c,3,db,a5,b0,f0,4a,38,e9
  //   ,a0,24,b5,10,9,aa,a9,ff,85,b7,20,22,d8,8a,a2,b0,c9,f9,10,6,20
  //   ,6e,d8,84,b7,60,a8,a5,b5,29,80,46,b1,5,b1,85,b1,20,85,d8,84,b7
  //   ,60,a5,b0,c9,a0,b0,20,20,6d,db,84,bf,a5,b5,84,b5,49,80,2a,a9,a0
  //   ,85,b0,a5,b4,85,5a,4c,a7,d7,85,b1,85,b2,85,b3,85,b4,a8,60,a0,0
  //   ,a2,a,94,ac,ca,10,fb,90,f,c9,2d,d0,4,86,b6,f0,4,c9,2b,d0,5,20
  //   ,c2,0,90,5b,c9,2e,f0,2e,c9,45,d0,30,20,c2,0,90,17,c9,ab,f0,e,c9
  //   ,2d,f0,a,c9,aa,f0,8,c9,2b,f0,4,d0,7,66,af,20,c2,0,90,5c,24,af
  //   ,10,e,a9,0,38,e5,ad,4c,1b,dc,66,ae,24,ae,50,c3,a5,ad,38,e5,ac
  //   ,85,ad,f0,12,10,9,20,d0,d9,e6,ad,d0,f9,f0,7,20,b4,d9,c6,ad,d0
  //   ,f9,a5,b6,30,1,60,4c,67,de,48,24,ae,10,2,e6,ac,20,b4,d9,68,38
  //   ,e9,30,20,50,dc,4c,dc,db,48,20,de,da,68,20,e,db,a5,bd,45,b5,85
  //   ,be,a6,b0,4c,3f,d7,a5,ad,c9,c,90,9,24,af,30,3,4c,53,d8,a9,b,a,a
  //   ,18,65,ad,a,18,a0,0,71,c9,38,e9,30,85,ad,4c,2,dc,9b,3e,bc,1f,fd
  //   ,9e,6e,6b,27,fe,9e,6e,6b,28,0,a9,94,a0,c2,20,ac,dc,a5,89,a6,88
  //   ,85,b1,86,b2,a2,90,38,20,1b,db,20,af,dc,4c,27,ca,a0,1,a9,20,24
  //   ,b5,10,2,a9,2d,99,ff,0,85,b5,84,c0,c8,a9,30,a6,b0,d0,3,4c,d6,dd
  //   ,a9,0,e0,80,f0,2,b0,9,a9,8f,a0,dc,20,fd,d8,a9,f7,85,ac,a9,8a,a0
  //   ,dc,20,2d,db,f0,1e,10,12,a9,85,a0,dc,20,2d,db,f0,2,10,e,20,b4
  //   ,d9,c6,ac,d0,ee,20,d0,d9,e6,ac,d0,dc,20,1e,d7,20,6d,db,a2,1,a5
  //   ,ac,18,69,a,30,9,c9,b,b0,6,69,ff,aa,a9,2,38,e9,2,85,ad,86,ac,8a
  //   ,f0,2,10,13,a4,c0,a9,2e,c8,99,ff,0,8a,f0,6,a9,30,c8,99,ff,0,84
  //   ,c0,a0,0,a2,80,a5,b4,18,79,eb,dd,85,b4,a5,b3,79,ea,dd,85,b3,a5
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  //   contents of D000 (hex, n*v repeats v):
  //   90,e1,e8,d0,dc,c9,41,90,5,e9,5b,38,e9,a5,60,68,48,c9,2a,d0,7,a9
  //   ,1a,a0,d0,60,0,0,a5,94,a4,95,c9,54,d0,b,c0,c9,f0,ed,c0,49,d0,3
  //   ,4c,1c,ce,c9,53,d0,4,c0,54,f0,f5,a5,7e,a4,7f,85,ae,84,af,a5,80
  //   ,a4,81,85,a9,84,aa,18,69,7,90,1,c8,85,a7,84,a8,20,da,c2,a5,a7
  //   ,a4,a8,c8,85,7e,84,7f,a0,0,a5,94,91,ae,c8,a5,95,91,ae,a9,0,c8
  //   ,91,ae,c8,91,ae,c8,91,ae,c8,91,ae,c8,91,ae,a5,ae,18,69,2,a4,af
  //   ,90,1,c8,85,96,84,97,60,a5,5c,a,69,5,65,ae,a4,af,90,1,c8,85,a7
  //   ,84,a8,60,90,80,0,0,20,c2,0,20,a4,cc,a5,b5,30,d,a5,b0,c9,90,90
  //   ,9,a9,99,a0,d0,20,2d,db,d0,7a,4c,6d,db,a5,5d,5,5f,48,a5,5e,48
  //   ,a0,0,98,48,a5,95,48,a5,94,48,20,9d,d0,68,85,94,68,85,95,68,a8
  //   ,ba,bd,2,1,48,bd,1,1,48,a5,b3,9d,2,1,a5,b4,9d,1,1,c8,20,c8,0,c9
  //   ,2c,f0,d2,84,5c,20,b,ce,68,85,5e,68,85,5f,29,7f,85,5d,a6,7e,a5
  //   ,7f,86,ae,85,af,c5,81,d0,4,e4,80,f0,39,a0,0,b1,ae,c8,c5,94,d0
  //   ,6,a5,95,d1,ae,f0,16,c8,b1,ae,18,65,ae,aa,c8,b1,ae,65,af,90,d7
  //   ,a2,70,2c,a2,35,4c,59,c3,a2,7d,a5,5d,d0,f7,20,88,d0,a5,5c,a0,4
  //   ,d1,ae,d0,e7,4c,d3,d1,20,88,d0,20,2a,c3,a9,0,a8,85,c1,a2,5,a5
  //   ,94,91,ae,10,1,ca,c8,a5,95,91,ae,10,2,ca,ca,86,c0,a5,5c,c8,c8,c8
  //   ,91,ae,a2,b,a9,0,24,5d,50,8,68,18,69,1,aa,68,69,0,c8,91,ae,c8
  //   ,8a,91,ae,20,33,d2,86,c0,85,c1,a4,71,c6,5c,d0,dc,65,a8,b0,5d,85
  //   ,a8,a8,8a,65,a7,90,3,c8,f0,52,20,2a,c3,85,80,84,81,a9,0,e6,c1
  //   ,a4,c0,f0,5,88,91,a7,d0,fb,c6,a8,c6,c1,d0,f5,e6,a8,38,a5,80,e5
  //   ,ae,a0,2,91,ae,a5,81,c8,e5,af,91,ae,a5,5d,d0,60,c8,b1,ae,85,5c
  //   ,a9,0,85,c0,85,c1,c8,68,aa,85,b3,68,85,b4,d1,ae,90,e,d0,6,c8,8a
  //   ,d1,ae,90,7,4c,2d,d1,4c,57,c3,c8,a5,c1,5,c0,18,f0,a,20,33,d2,8a
  //   ,65,b3,aa,98,a4,71,65,b4,86,c0,c6,5c,d0,ca,a2,5,a5,94,10,1,ca
  //   ,a5,95,10,2,ca,ca,86,77,a9,0,20,3c,d2,8a,65,a7,85,96,98,65,a8
  //   ,85,97,a8,a5,96,60,84,71,b1,ae,85,77,88,b1,ae,85,78,a9,10,85,ac
  //   ,a2,0,a0,0,8a,a,aa,98,2a,a8,b0,a6,6,c0,26,c1,90,b,18,8a,65,77
  //   ,aa,98,65,78,a8,b0,95,c6,ac,d0,e3,60,a5,5e,f0,3,20,7e,d5,20,4
  //   ,d4,38,a5,82,e5,80,a8,a5,83,e5,81,a2,0,86,5e,85,b1,84,b2,a2,90
  //   ,4c,16,db,a4,5,a9,0,f0,ed,a6,89,e8,d0,a2,a2,9a,4c,59,c3,20,c3
  //   ,d2,20,8b,d2,20,e,ce,a9,80,85,61,20,7b,cf,20,a7,cc,20,b,ce,a9
  //   ,b2,20,13,ce,48,a5,97,48,a5,96,48,a5,ca,48,a5,c9,48,20,f0,c7,4c
  //   ,33,d3,a9,a5,20,13,ce,9,80,85,61,20,82,cf,85,9d,84,9e,4c,a7,cc
  //   ,20,c3,d2,a5,9e,48,a5,9d,48,20,5,ce,20,a7,cc,68,85,9d,68,85,9e
  //   ,a0,2,a2,ed,b1,9d,f0,9f,85,96,aa,c8,b1,9d,85,97,c8,b1,96,48,88
  //   ,10,fa,a4,97,20,a6,da,a5,ca,48,a5,c9,48,b1,9d,85,c9,c8,b1,9d,85
  //   ,ca,a5,97,48,a5,96,48,20,a4,cc,68,85,9d,68,85,9e,20,c8,0,f0,3
  //   ,4c,1c,ce,68,85,c9,68,85,ca,a0,0,68,91,9d,68,c8,91,9d,68,c8,91
  //   ,9d,68,c8,91,9d,68,c8,91,9d,60,20,a7,cc,a0,0,20,b1,dc,68,68,a9
  //   ,ff,a0,0,f0,12,a6,b3,a4,b4,86,9f,84,a0,20,d2,d3,86,b1,84,b2,85
  //   ,b0,60,a2,22,86,5a,86,5b,85,be,84,bf,85,b1,84,b2,a0,ff,c8,b1,be
  //   ,f0,c,c5,5a,f0,4,c5,5b,d0,f3,c9,22,f0,1,18,84,b0,98,65,be,85,c0
  //   ,a6,bf,90,1,e8,86,c1,a5,bf,d0,b,98,20,59,d3,a6,be,a4,bf,20,60
  //   ,d5,a6,65,e0,71,d0,5,a2,cc,4c,59,c3,a5,b0,95,0,a5,b1,95,1,a5,b2
  //   ,95,2,a0,0,86,b3,84,b4,88,84,5e,86,66,e8,e8,e8,86,65,60,46,60
  //   ,48,49,ff,38,65,82,a4,83,b0,1,88,c4,81,90,11,d0,4,c5,80,90,b,85
  //   ,82,84,83,85,84,84,85,aa,68,60,a2,52,a5,60,30,b8,20,4,d4,a9,80
  //   ,85,60,68,d0,d0,a6,86,a5,87,86,82,85,83,a0,0,84,9e,a5,80,a6,81
  //   ,85,ae,86,af,a9,68,a2,0,85,71,86,72,c5,65,f0,5,20,a1,d4,f0,f7
  //   ,a9,7,85,a2,a5,7c,a6,7d,85,71,86,72,e4,7f,d0,4,c5,7e,f0,5,20,97
  //   ,d4,f0,f3,85,a7,86,a8,a9,3,85,a2,a5,a7,a6,a8,e4,81,d0,7,c5,80
  //   ,d0,3,4c,e0,d4,85,71,86,72,a0,0,b1,71,aa,c8,b1,71,8,c8,b1,71,65
  //   ,a7,85,a7,c8,b1,71,65,a8,85,a8,28,10,d3,8a,30,d0,c8,b1,71,20,f3
  //   ,e7,65,71,85,71,90,2,e6,72,a6,72,e4,a8,d0,4,c5,a7,f0,bc,20,a1
  //   ,d4,f0,f3,b1,71,30,35,c8,b1,71,10,30,c8,b1,71,f0,2b,c8,b1,71,aa
  //   ,c8,b1,71,c5,83,90,6,d0,1e,e4,82,b0,1a,c5,af,90,16,d0,4,e4,ae
  //   ,90,10,86,ae,85,af,a5,71,a6,72,85,9d,86,9e,a5,a2,85,a4,a5,a2,18
  //   ,65,71,85,71,90,2,e6,72,a6,72,a0,0,60,a6,9e,f0,f7,a5,a4,e9,3,4a
  //   ,a8,85,a4,b1,9d,65,ae,85,a9,a5,af,69,0,85,aa,a5,82,a6,83,85,a7
  //   ,86,a8,20,e1,c2,a4,a4,c8,a5,a7,91,9d,aa,e6,a8,a5,a8,c8,91,9d,4c
  //   ,8,d4,a5,b4,48,a5,b3,48,20,9d,cd,20,a9,cc,68,85,be,68,85,bf,a0
  //   ,0,b1,be,18,71,b3,90,5,a2,b5,4c,59,c3,20,59,d3,20,52,d5,a5,9f
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  //   contents of C800 (hex, n*v repeats v):
  //   2c,a2,0,86,5a,a0,0,84,5b,a5,5b,a6,5a,85,5a,86,5b,b1,c9,f0,e8,c5
  //   ,5b,f0,e4,c8,c9,22,f0,eb,d0,f1,20,b8,cc,20,c8,0,c9,89,f0,5,a9
  //   ,a7,20,13,ce,a5,b0,d0,5,20,1,c8,f0,bb,20,c8,0,b0,3,4c,9d,c7,4c
  //   ,f2,c6,20,76,d6,48,c9,8d,f0,4,c9,89,d0,91,c6,b4,d0,4,68,4c,f5
  //   ,c6,20,c2,0,20,63,c8,c9,2c,f0,ee,68,60,a2,0,86,8,86,9,b0,f7,e9
  //   ,2f,85,5a,a5,9,85,71,c9,19,b0,d4,a5,8,a,26,71,a,26,71,65,8,85
  //   ,8,a5,71,65,9,85,9,6,8,26,9,a5,8,65,5a,85,8,90,2,e6,9,20,c2,0
  //   ,4c,69,c8,20,7b,cf,85,98,84,99,a9,b2,20,13,ce,a5,5f,48,a5,5e,48
  //   ,20,b8,cc,68,2a,20,aa,cc,d0,18,68,10,12,20,ed,da,20,a7,d0,a0,0
  //   ,a5,b3,91,98,c8,a5,b4,91,98,60,4c,a2,da,68,a4,99,c0,d0,d0,53,20
  //   ,7e,d5,c9,6,f0,3,4c,30,d1,a0,0,84,b0,84,b5,84,c0,20,1c,c9,20,b4
  //   ,d9,e6,c0,a4,c0,20,1c,c9,20,de,da,aa,f0,5,e8,8a,20,bf,d9,a4,c0
  //   ,c8,c0,6,d0,df,20,b4,d9,20,6d,db,a2,2,78,b5,b2,9d,0,2,ca,10,f8
  //   ,58,60,b1,71,20,cf,0,90,3,4c,30,d1,e9,2f,4c,50,dc,a0,2,b1,b3,c5
  //   ,83,90,17,d0,7,88,b1,b3,c5,82,90,e,a4,b4,c4,7d,90,8,d0,d,a5,b3
  //   ,c5,7c,b0,7,a5,b3,a4,b4,4c,67,c9,a0,0,b1,b3,20,59,d3,a5,9f,a4
  //   ,a0,85,be,84,bf,20,52,d5,a9,b0,a0,0,85,9f,84,a0,20,b3,d5,a0,0
  //   ,b1,9f,91,98,c8,b1,9f,91,98,c8,b1,9f,91,98,60,20,85,c9,4c,d6,ca
  //   ,20,76,d6,f0,5,a9,2c,20,13,ce,8,20,c9,ff,86,3,28,4c,9f,c9,20,2a
  //   ,ca,20,c8,0,f0,31,f0,55,c9,a3,f0,5f,c9,a6,f0,5b,c9,2c,f0,4a,c9
  //   ,3b,f0,6e,20,b8,cc,24,5e,30,df,20,af,dc,20,6b,d3,20,2a,ca,20,44
  //   ,ca,d0,d4,a0,0,94,a,a2,9,a5,3,d0,26,a5,3,d0,2,85,5,a9,d,20,49
  //   ,ca,a9,a,20,49,ca,a5,3,d0,12,8a,48,a6,4,f0,8,a9,0,20,49,ca,ca
  //   ,d0,fa,86,5,68,aa,60,a5,5,38,e9,a,b0,fc,49,ff,69,1,d0,14,48,20
  //   ,73,d6,c9,29,d0,75,68,c9,a3,d0,8,8a,e5,5,90,9,f0,7,aa,20,44,ca,ca
  //   ,d0,fa,20,c2,0,4c,a1,c9,20,6b,d3,20,7e,d5,aa,a0,0,e8,ca,f0,c4
  //   ,b1,71,20,49,ca,c8,c9,d,d0,f3,20,e2,c9,4c,31,ca,a9,1d,2c,a9,3f
  //   ,24,64,30,27,48,c9,1d,f0,18,c9,9d,f0,4,c9,14,d0,a,a5,5,f0,12,a5
  //   ,3,d0,e,c6,5,29,7f,c9,20,90,6,a5,3,20,cc,e1,ea,68,20,d2,ff,29
  //   ,ff,60,a5,62,f0,b,20,c2,e1,ea,85,88,84,89,4c,1c,ce,a5,3,f0,5,a2
  //   ,c4,4c,59,c3,a9,23,a0,cc,20,27,ca,a5,8c,a4,8d,85,c9,84,ca,60,20
  //   ,8b,d2,c9,23,d0,10,20,c2,0,20,76,d6,a9,2c,20,13,ce,20,c6,ff,86
  //   ,3,a2,b,a0,0,84,b,a9,40,20,2a,cb,a6,3,d0,13,60,20,76,d6,a9,2c
  //   ,20,13,ce,20,c6,ff,86,3,20,f1,ca,a5,3,20,cc,ff,a2,0,86,3,60,46
  //   ,64,c9,22,d0,b,20,d1,cd,a9,3b,20,13,ce,20,2a,ca,20,8b,d2,a9,2c
  //   ,85,9,20,17,cb,a5,3,f0,d,ad,c,2,29,2,f0,6,20,d6,ca,4c,f0,c7,a5
  //   ,a,d0,19,a5,3,d0,e4,4c,9b,e1,a5,3,d0,6,20,47,ca,20,44,ca,4c,68
  //   ,c4,a6,90,a4,91,a9,98,85,62,86,92,84,93,20,7b,cf,85,98,84,99,a5
  //   ,c9,a4,ca,85,8,84,9,a6,92,a4,93,86,c9,84,ca,20,c8,0,d0,1f,24,62
  //   ,50,b,20,e4,ff,85,a,a0,0,a2,9,d0,c,30,72,a5,3,d0,3,20,47,ca,20
  //   ,17,cb,86,c9,84,ca,20,c2,0,24,5e,10,2e,24,62,50,6,a9,0,20,bc,e1
  //   ,ea,85,5a,c9,22,f0,7,a9,3a,85,5a,a9,2c,18,85,5b,a5,c9,a4,ca,69
  //   ,0,90,1,c8,20,71,d3,20,bb,d6,20,d2,c8,4c,a8,cb,20,c5,db,a5,5f
  //   ,20,ba,c8,20,c8,0,f0,7,c9,2c,f0,3,4c,77,ca,a5,c9,a4,ca,85,92,84
  //   ,93,a5,8,a4,9,85,c9,84,ca,20,c8,0,f0,2c,20,11,ce,4c,30,cb,20,fe
  //   ,c7,c8,aa,d0,12,a2,2a,c8,b1,c9,f0,6d,c8,b1,c9,85,8e,c8,b1,c9,c8
  //   ,85,8f,b1,c9,aa,20,f3,c7,e0,83,d0,dd,4c,6b,cb,a5,92,a4,93,a6,62
  //   ,10,3,4c,17,c7,a0,0,b1,92,f0,b,a5,3,d0,7,a9,12,a0,cc,4c,27,ca
  //   ,60,3f,45,58,54,52,41,20,49,47,4e,4f,52,45,44,d,a,0,3f,52,45,44
  //   ,4f,20,46,52,4f,4d,20,53,54,41,52,54,d,a,0,d0,4,a0,0,f0,3,20,7b
  //   ,cf,85,98,84,99,20,ac,c2,f0,4,a2,0,f0,69,9a,4*e8,8a,6*e8,86,73
  //   ,a0,1,20,74,da,ba,bd,9,1,85,b5,a5,98,a4,99,20,3c,d7,20,a2,da,a0
  //   ,1,20,2f,db,ba,38,fd,9,1,f0,17,bd,f,1,85,88,bd,10,1,85,89,bd,12
  //   ,1,85,c9,bd,11,1,85,ca,4c,b5,c6,8a,69,11,aa,9a,20,c8,0,c9,2c,d0
  //   ,f1,20,c2,0,20,3c,cc,20,b8,cc,18,24,38,24,5e,30,3,b0,3,60,b0,fd
  //   ,a2,a8,4c,59,c3,a6,c9,d0,2,c6,ca,c6,c9,a2,0,24,48,8a,48,a9,1,20
  //   ,1d,c3,20,9d,cd,a9,0,85,9c,20,c8,0,38,e9,b1,90,17,c9,3,b0,13,c9
  //   ,1,2a,49,1,45,9c,c5,9c,90,61,85,9c,20,c2,0,4c,d5,cc,a6,9c,d0,2c
  //   ,b0,7b,69,7,90,77,65,5e,d0,3,4c,15,d5,69,ff,85,71,a,65,71,a8,68
  //   ,d9,74,c0,b0,67,20,a7,cc,48,20,3a,cd,68,a4,9a,10,17,aa,f0,56,d0
  //   ,5f,46,5e,8a,2a,a6,c9,d0,2,c6,ca,c6,c9,a0,1b,85,9c,d0,d7,d9,74
  //   ,c0,b0,48,90,d9,b9,76,c0,48,b9,75,c0,48,20,4d,cd,a5,9c,4c,c3,cc
  //   ,4c,1c,ce,a5,b5,be,74,c0,a8,68,85,71,e6,71,68,85,72,98,48,20,ed
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  //   contents of C000 (hex, n*v repeats v):
  //   1d,c7,48,c6,35,cc,ef,c7,c5,ca,df,ca,70,cf,23,cb,9c,c8,9c,c7,74
  //   ,c7,1f,c8,c,c7,7f,c7,c9,c7,32,c8,1b,c7,42,c8,1,d7,d4,ff,d7,ff
  //   ,da,ff,94,d2,f8,d6,7e,c9,9e,c9,44,c7,a7,c5,6f,c7,84,c9,dd,ff,bf
  //   ,ff,c2,ff,9e,ca,50,c5,b,db,9e,db,2a,db,0,0,64,d2,85,d2,24,de,45
  //   ,df,bf,d8,a0,de,9e,df,a5,df,ee,df,48,e0,e6,d6,54,d6,49,d3,85,d6
  //   ,63,d6,c4,d5,d8,d5,4,d6,f,d6,79,3e,d7,79,27,d7,7b,ff,d8,7b,e3
  //   ,d9,7f,2d,de,50,d8,ce,46,d5,ce,7d,66,de,5a,e7,cd,64,5,cf,45,4e
  //   ,c4,46,4f,d2,4e,45,58,d4,44,41,54,c1,49,4e,50,55,54,a3,49,4e,50
  //   ,55,d4,44,49,cd,52,45,41,c4,4c,45,d4,47,4f,54,cf,52,55,ce,49,c6
  //   ,52,45,53,54,4f,52,c5,47,4f,53,55,c2,52,45,54,55,52,ce,52,45,cd
  //   ,53,54,4f,d0,4f,ce,57,41,49,d4,4c,4f,41,c4,53,41,56,c5,56,45,52
  //   ,49,46,d9,44,45,c6,50,4f,4b,c5,50,52,49,4e,54,a3,50,52,49,4e,d4
  //   ,43,4f,4e,d4,4c,49,53,d4,43,4c,d2,43,4d,c4,53,59,d3,4f,50,45,ce
  //   ,43,4c,4f,53,c5,47,45,d4,4e,45,d7,54,41,42,a8,54,cf,46,ce,53,50
  //   ,43,a8,54,48,45,ce,4e,4f,d4,53,54,45,d0,ab,ad,aa,af,de,41,4e,c4
  //   ,4f,d2,be,bd,bc,53,47,ce,49,4e,d4,41,42,d3,55,53,d2,46,52,c5,50
  //   ,4f,d3,53,51,d2,52,4e,c4,4c,4f,c7,45,58,d0,43,4f,d3,53,49,ce,54
  //   ,41,ce,41,54,ce,50,45,45,cb,4c,45,ce,53,54,52,a4,56,41,cc,41,53
  //   ,c3,43,48,52,a4,4c,45,46,54,a4,52,49,47,48,54,a4,4d,49,44,a4,0
  //   ,4e,45,58,54,20,57,49,54,48,4f,55,54,20,46,4f,d2,53,59,4e,54,41
  //   ,d8,52,45,54,55,52,4e,20,57,49,54,48,4f,55,54,20,47,4f,53,55,c2
  //   ,4f,55,54,20,4f,46,20,44,41,54,c1,49,4c,4c,45,47,41,4c,20,51,55
  //   ,41,4e,54,49,54,d9,5*0,4f,56,45,52,46,4c,4f,d7,4f,55,54,20,4f
  //   ,46,20,4d,45,4d,4f,52,d9,55,4e,44,45,46,27,44,20,53,54,41,54,45
  //   ,4d,45,4e,d4,42,41,44,20,53,55,42,53,43,52,49,50,d4,52,45,44,49
  //   ,4d,27,44,20,41,52,52,41,d9,44,49,56,49,53,49,4f,4e,20,42,59,20
  //   ,5a,45,52,cf,49,4c,4c,45,47,41,4c,20,44,49,52,45,43,d4,54,59,50
  //   ,45,20,4d,49,53,4d,41,54,43,c8,53,54,52,49,4e,47,20,54,4f,4f,20
  //   ,4c,4f,4e,c7,42,41,44,20,44,41,54,c1,46,4f,52,4d,55,4c,41,20,54
  //   ,4f,4f,20,43,4f,4d,50,4c,45,d8,43,41,4e,27,54,20,43,4f,4e,54,49
  //   ,4e,55,c5,55,4e,44,45,46,27,44,20,46,55,4e,43,54,49,4f,ce,20,45
  //   ,52,52,4f,52,0,20,49,4e,20,0,d,a,52,45,41,44,59,2e,d,a,0,d,a,42
  //   ,52,45,41,4b,0,ba,4*e8,bd,1,1,c9,81,d0,21,a5,99,d0,a,bd,2,1,85
  //   ,98,bd,3,1,85,99,dd,3,1,d0,7,a5,98,dd,2,1,f0,7,8a,18,69,12,aa
  //   ,d0,d8,60,20,2a,c3,85,80,84,81,38,a5,a9,e5,ae,85,71,a8,a5,aa,e5
  //   ,af,aa,e8,98,f0,23,a5,a9,38,e5,71,85,a9,b0,3,c6,aa,38,a5,a7,e5
  //   ,71,85,a7,b0,8,c6,a8,90,4,b1,a9,91,a7,88,d0,f9,b1,a9,91,a7,c6
  //   ,aa,c6,a8,ca,d0,f2,60,a,69,36,b0,35,85,71,ba,e4,71,90,2e,60,c4
  //   ,83,90,28,d0,4,c5,82,90,22,48,a2,9,98,48,b5,a6,ca,10,fa,20,4,d4
  //   ,a2,f7,68,95,b0,e8,30,fa,68,a8,68,c4,83,90,6,d0,5,c5,82,b0,1,60
  //   ,a2,52,46,64,a5,3,f0,7,20,cc,ff,a9,0,85,3,20,d2,c9,20,47,ca,bd
  //   ,90,c1,48,29,7f,20,49,ca,e8,68,10,f3,20,84,c5,a9,8d,a0,c2,20,27
  //   ,ca,a4,89,c8,f0,3,20,94,dc,46,64,a9,99,a0,c2,20,27,ca,20,68,c4
  //   ,86,c9,84,ca,20,c2,0,f0,f4,a2,ff,86,89,90,6,20,8d,c4,4c,e9,c6
  //   ,20,63,c8,20,8d,c4,84,5c,20,22,c5,90,44,a0,1,b1,ae,85,72,a5,7c
  //   ,85,71,a5,af,85,74,a5,ae,88,f1,ae,18,65,7c,85,7c,85,73,a5,7d,69
  //   ,ff,85,7d,e5,af,aa,38,a5,ae,e5,7c,a8,b0,3,e8,c6,74,18,65,71,90
  //   ,3,c6,72,18,b1,71,91,73,c8,d0,f9,e6,72,e6,74,ca,d0,f2,a5,a,f0
  //   ,2f,a5,86,a4,87,85,82,84,83,a5,7c,85,a9,65,5c,85,a7,a4,7d,84,aa
  //   ,90,1,c8,84,a8,20,da,c2,a5,80,a4,81,85,7c,84,7d,a4,5c,88,b9,6
  //   ,0,91,ae,88,10,f8,20,67,c5,a5,7a,a4,7b,85,71,84,72,18,a0,1,b1
  //   ,71,d0,3,4c,94,c3,a0,4,c8,b1,71,d0,fb,c8,98,65,71,aa,a0,0,91,71
  //   ,a5,72,69,0,c8,91,71,86,71,85,72,90,da,ca,10,5,20,d2,c9,a2,0,20
  //   ,79,c4,c9,d,f0,5,95,a,e8,d0,f4,4c,c8,c9,20,cf,ff,a4,3,d0,c,c9
  //   ,f,d0,8,48,a5,64,49,ff,85,64,68,60,a6,c9,a0,4,84,60,b5,0,10,7
  //   ,c9,ff,f0,41,e8,d0,f5,c9,20,f0,3a,85,5b,c9,22,f0,58,24,60,70,30
  //   ,c9,3f,d0,4,a9,99,d0,28,c9,30,90,4,c9,3c,90,20,84,c0,a0,0,84,5c
  //   ,88,86,c9,ca,c8,e8,b5,0,c9,20,f0,f9,38,f9,92,c0,f0,f2,c9,80,d0
  //   ,2f,5,5c,a4,c0,e8,c8,99,5,0,b9,5,0,f0,34,38,e9,3a,f0,4,c9,49,d0
  //   ,2,85,60,38,e9,55,d0,9d,85,5b,b5,0,f0,e0,c5,5b,f0,dc,c8,99,5,0
  //   ,e8,d0,f1,a6,c9,e6,5c,c8,b9,91,c0,10,fa,b9,92,c0,d0,b2,b5,0,10
  //   ,c0,99,7,0,a9,9,85,c9,60,a5,7a,a6,7b,a0,1,85,ae,86,af,b1,ae,f0
  //   ,1f,c8,c8,a5,9,d1,ae,90,18,f0,3,88,d0,9,a5,8,88,d1,ae,90,c,f0
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  //   contents of ROM (hex, n*v repeats v):
  //   C:\Users\thoma\Documents\Projects\PET-Digital-Simulation\rom_files\Basic v2\characters-2.901447-10.bin false
endmodule
