// Digital circuit Mainboard-PET2001-8.dig as structural Verilog
module Mainboard_PET2001_8 (
  input  _8MHz,
  output [11:0] BA,
  output [7:0] D,
  output \BΦ2 ,
  output [31:0] cycle,
  output r_w
);

  wire _1_CASS_MOTOR, _1_CASS_READ, _1_CASS_SWITCH, _2_CASS_MOTOR, _2_CASS_SWITCH, _74ls93_1_qa,
       _74ls93_1_qc, _74ls93_1_qd, _74ls93_2_qa, _74ls93_2_qb, _74ls93_2_qc, _74ls93_2_qd, _74ls93_3_qb,
       _74ls93_3_qc, _74ls93_3_qd, _74ls107_1_q, _74ls107_2_nq, _74ls107_2_q, _74ls107_3_nq, _74ls107_3_q,
       _74ls107_4_q, _74ls107_6_nq, _74ls107_6_q, _74ls107_7_nq, _74ls107_7_q, _74ls107_8_nq, _74ls107_8_q,
       _74ls107_clr_top_1_q, _74ls107_clr_top_2_q, _74ls145_1__0, _74ls145_1__1, _74ls145_1__2,
       _74ls145_1__3, _74ls145_1__4, _74ls145_1__5, _74ls145_1__6, _74ls145_1__7, _74ls145_1__8,
       _74ls145_1__9, _74ls157_1_y2, _74ls165_layout_2_1_nqh, _74ls165_layout_2_1_qh, _74s74_1_q,
       _74s74_2_nq, _74s74_2_q, _6502_layout_2_1_a12, _6502_layout_2_1_a13, _6502_layout_2_1_a14,
       _6502_layout_2_1_a15, _6502_layout_2_1_r_w, \_6502_layout_2_1_φ2 , _6520_layout_2_1_nirqb,
       _6520_layout_2_2_cb2, _6520_layout_2_2_pa0, _6520_layout_2_2_pa1, _6520_layout_2_2_pa2,
       _6520_layout_2_2_pa3, _6520_layout_2_2_pa6, _6522_layout_2_1_pb4, _6540_character_rom_1_d0,
       _6540_character_rom_1_d1, _6540_character_rom_1_d2, _6540_character_rom_1_d3,
       _6540_character_rom_1_d4, _6540_character_rom_1_d5, _6540_character_rom_1_d6,
       _6540_character_rom_1_d7, _74100_1_q1, _74100_1_q2, _74100_1_q3, _74100_1_q4, _74100_1_q5,
       _74100_1_q6, _74100_1_q7, _74100_1_q8, _74154_layout_2_1_y8, _74177_layout_2_1_qa,
       _74177_layout_2_1_qb, _74177_layout_2_1_qc, _74177_layout_2_1_qd, _74177_layout_2_2_qa,
       _74177_layout_2_2_qb, _74177_layout_2_2_qc, _74177_layout_2_2_qd, and_1_out, and_3_out, and_4_out,
       and_6_out, and_7_out, and_8_out, BD0, BD1, BD2, BD3, BD4, BD5, BD6, BD7, BLANK_TV, CASS_WRITE,
       comparator_1_eq, DIAG, DIS_OFF, DIS_ON, GRAPHIC, HORZ_DRIVE, nand_1_out, nand_3_out, nand_4_out,
       nand_5_out, nand_7_out, nand_8_out, nand_9_out, nand_10_out, nand_11_out, nand_13_out, nBA11,
       not_1_out, not_2_out, not_4_out, not_7_out, not_8_out, not_9_out, nSEL0, nSEL1, nSELC, nSELD, nSELE,
       nSELF, or_1_out, or_2_out, or_3_out, pullup_1_out, RDY, reset_1_out, RESET_Delay_ovf, rs_ff_as_1_q,
       SD0, SD1, SD2, SD3, SD4, SD5, SD6, SD7, SEL8, SYNC, TV_VIDEO_DRIVE, VERT_DRIVE, \Φ0 ;
  wire [1:0] _74ls157_1_y3;
  wire [3:0] _74ls157_2_y1, _74ls157_3_y1;
  wire [7:0] _6520_layout_2_2_pb7;
  wire [11:0] _6502_layout_2_1_a0;

  not not_1 (not_1_out, _74ls93_1_qd);
  _74LS107 _74ls107_1 (.J(_74ls93_1_qd), .nCLK(and_1_out), .K(not_1_out), .Q(_74ls107_1_q), .nQ(\Φ0 ), .nCLR(1'b1));
  not not_2 (not_2_out, 1'b1);
  _74LS244 _74ls244_1 (
    ._1Y1(D[0]), ._2A1(D[0]), ._1Y2(D[1]), ._2A2(D[1]), ._1Y3(D[2]), ._2A3(D[2]), ._1Y4(D[3]), ._2A4(D[3]),
    ._1nG(and_6_out), ._1A1(BD0), ._2Y1(BD0), ._1A2(BD1), ._2Y2(BD1), ._1A3(BD2), ._2Y3(BD2), ._1A4(BD3),
    ._2Y4(BD3), ._2nG(not_4_out));
  _74LS244 _74ls244_2 (
    ._1Y1(D[4]), ._2A1(D[4]), ._1Y2(D[5]), ._2A2(D[5]), ._1Y3(D[6]), ._2A3(D[6]), ._1Y4(D[7]), ._2A4(D[7]),
    ._1nG(and_6_out), ._1A1(BD4), ._2Y1(BD4), ._1A2(BD5), ._2Y2(BD5), ._1A3(BD6), ._2Y3(BD6), ._1A4(BD7),
    ._2Y4(BD7), ._2nG(not_4_out));
  _74LS93 _74ls93_1 (
    .CKA(_74ls93_1_qd), .CKB(and_1_out), .R1(not_2_out), .R2(not_2_out), .QA(_74ls93_1_qa),
    .QC(_74ls93_1_qc), .QD(_74ls93_1_qd));  // open: QB
  _74LS93 _74ls93_2 (
    .CKA(_74ls93_1_qa), .CKB(_74ls93_2_qa), .R1(not_2_out), .R2(not_2_out), .QA(_74ls93_2_qa),
    .QB(_74ls93_2_qb), .QC(_74ls93_2_qc), .QD(_74ls93_2_qd));
  _74LS107 _74ls107_2 (.J(1'b1), .nCLK(_74ls93_2_qd), .K(1'b1), .Q(_74ls107_2_q), .nQ(_74ls107_2_nq), .nCLR(1'b1));
  and and_1 (and_1_out, 1'b1, _8MHz);
  _74154_layout_2 _74154_layout_2_1 (
    .D(_6502_layout_2_1_a15), .C(_6502_layout_2_1_a14), .B(_6502_layout_2_1_a13), .A(_6502_layout_2_1_a12),
    .nG1(1'b0), .nG2(1'b0), .Y0(nSEL0), .Y1(nSEL1), .Y8(_74154_layout_2_1_y8), .Y12(nSELC), .Y13(nSELD),
    .Y14(nSELE), .Y15(nSELF));  // open: Y2, Y3, Y4, Y5, Y6, Y7, Y9, Y10, Y11
  not not_3 (BA[11], nBA11);
  Delay delay_1 (.in(_6502_layout_2_1_a0[9]), .out(BA[9]));
  Delay delay_2 (.in(_6502_layout_2_1_a0[6]), .out(BA[6]));
  Delay delay_3 (.in(_6502_layout_2_1_a0[3]), .out(BA[3]));
  not not_4 (not_4_out, and_6_out);
  not not_5 (SEL8, _74154_layout_2_1_y8);
  not not_6 (nBA11, _6502_layout_2_1_a0[11]);
  Delay delay_4 (.in(_6502_layout_2_1_a0[10]), .out(BA[10]));
  Delay delay_5 (.in(_6502_layout_2_1_a0[8]), .out(BA[8]));
  Delay delay_6 (.in(_6502_layout_2_1_a0[7]), .out(BA[7]));
  Delay delay_7 (.in(_6502_layout_2_1_a0[5]), .out(BA[5]));
  Delay delay_8 (.in(_6502_layout_2_1_a0[4]), .out(BA[4]));
  Delay delay_9 (.in(_6502_layout_2_1_a0[2]), .out(BA[2]));
  Delay delay_10 (.in(_6502_layout_2_1_a0[1]), .out(BA[1]));
  and and_2 (BA[0], 1'b1, _6502_layout_2_1_a0[0]);
  and and_3 (and_3_out, _74ls93_2_qc, _74ls107_2_q);
  and and_4 (and_4_out, _74ls107_2_nq, _74ls93_2_qd);
  Button #(.activeLow("true")) button_1 (.out(RDY));
  and and_5 (r_w, nSELE, pullup_1_out, pullup_1_out, _6502_layout_2_1_r_w);
  Reset reset_1 (.out(reset_1_out));
  Comparator #(.Bits(12)) comparator_1 (.a(BA), .b(12'hd17), .eq(comparator_1_eq));  // open: gt, lt
  _74LS107 _74ls107_3 (
    .J(1'b1), .nCLK(_74ls93_1_qd), .K(1'b0), .Q(_74ls107_3_q), .nQ(_74ls107_3_nq), .nCLR(nand_1_out));
  nand nand_1 (nand_1_out, and_1_out, _74ls107_3_q);
  _74LS107 _74ls107_4 (.J(DIS_ON), .nCLK(_74ls93_2_qb), .K(DIS_OFF), .Q(_74ls107_4_q), .nQ(HORZ_DRIVE), .nCLR(1'b1));
  _74LS107 _74ls107_5 (.J(and_3_out), .nCLK(_74ls93_1_qa), .K(and_4_out), .Q(DIS_ON), .nQ(DIS_OFF), .nCLR(1'b1));
  and and_6 (and_6_out, nSELC, nSELD, nSELF, r_w);
  Counter #(.Bits(2)) RESET_Delay (.en(reset_1_out), .C(\Φ0 ), .clr(rs_ff_as_1_q), .ovf(RESET_Delay_ovf));  // open: out
  _6502_layout_2 _6502_layout_2_1 (
    .R_W(_6502_layout_2_1_r_w), .\Φ0 (\Φ0 ), .\Φ2 (\_6502_layout_2_1_φ2 ), .nRESET(rs_ff_as_1_q),
    .nIRQ(_6520_layout_2_1_nirqb), .nNMI(1'b1), .RDY(1'b1), .D0(D[0]), .D1(D[1]), .D2(D[2]), .D3(D[3]),
    .D4(D[4]), .D5(D[5]), .D6(D[6]), .D7(D[7]), .A15(_6502_layout_2_1_a15), .A14(_6502_layout_2_1_a14),
    .A13(_6502_layout_2_1_a13), .A12(_6502_layout_2_1_a12), .A11(_6502_layout_2_1_a0[0]),
    .A10(_6502_layout_2_1_a0[1]), .A9(_6502_layout_2_1_a0[2]), .A8(_6502_layout_2_1_a0[3]),
    .A7(_6502_layout_2_1_a0[4]), .A6(_6502_layout_2_1_a0[5]), .A5(_6502_layout_2_1_a0[6]),
    .A4(_6502_layout_2_1_a0[7]), .A3(_6502_layout_2_1_a0[8]), .A2(_6502_layout_2_1_a0[9]),
    .A1(_6502_layout_2_1_a0[10]), .A0(_6502_layout_2_1_a0[11]));  // open: Φ1, SYNC
  nand nand_2 (\BΦ2 , nand_3_out, pullup_1_out);
  Break #(.Cycles(10000000)) break_1 (.brk(comparator_1_eq));
  and and_7 (and_7_out, BA[6], BA[11]);
  nand nand_3 (nand_3_out, \_6502_layout_2_1_φ2 , pullup_1_out);
  RS_FF_AS rs_ff_as_1 (.S(RESET_Delay_ovf), .R(1'b0), .Q(rs_ff_as_1_q));  // open: nQ
  PullUp pullup_1 (.out(pullup_1_out));
  _74LS107 _74ls107_6 (.J(and_8_out), .nCLK(_74ls93_1_qc), .K(1'b1), .Q(_74ls107_6_q), .nQ(_74ls107_6_nq), .nCLR(1'b1));
  Counter #(.Bits(32)) counter_1 (.en(1'b1), .C(\BΦ2 ), .clr(1'b0), .out(cycle));  // open: ovf
  and and_8 (and_8_out, DIS_OFF, or_2_out);
  _74LS107 _74ls107_7 (
    .J(_74ls107_8_nq), .nCLK(_74ls107_6_q), .K(_74ls107_8_q), .Q(_74ls107_7_q), .nQ(_74ls107_7_nq),
    .nCLR(1'b1));
  or or_1 (or_1_out, ~_74ls107_6_nq, ~nand_9_out);  // Or
  _74100 _74100_1 (
    ._1(_74177_layout_2_1_qa), ._2(_74177_layout_2_1_qb), ._3(_74177_layout_2_1_qc),
    ._4(_74177_layout_2_1_qd), ._5(_74177_layout_2_2_qa), ._6(_74177_layout_2_2_qb),
    ._7(_74177_layout_2_2_qc), ._8(_74177_layout_2_2_qd), .Q1(_74100_1_q1), .Q2(_74100_1_q2),
    .Q3(_74100_1_q3), .Q4(_74100_1_q4), .Q5(_74100_1_q5), .Q6(_74100_1_q6), .Q7(_74100_1_q7),
    .Q8(_74100_1_q8), .C1(or_1_out), .C2(or_1_out));
  not not_7 (not_7_out, nand_5_out);
  nand nand_4 (nand_4_out, not_7_out, _74100_1_q2);
  _6520_layout_2 _6520_layout_2_1 (
    .nIRQB(_6520_layout_2_1_nirqb), .nIRQA(_6520_layout_2_1_nirqb), .nRESET(rs_ff_as_1_q),
    .\Φ2 (\_6502_layout_2_1_φ2 ), .nCS2(nSELE), .CS1(BA[5]), .CS0(BA[11]), .RS1(BA[1]), .RS0(BA[0]),
    .R_W(_6502_layout_2_1_r_w), .D0(D[0]), .D1(D[1]), .D2(D[2]), .D3(D[3]), .D4(D[4]), .D5(D[5]), .D6(D[6]),
    .D7(D[7]), .CA1(1'b1), .CA2(GRAPHIC), .CB1(1'b1));  // open: PA0, PA1, PA2, PA3, PA4, PA5, PA6, PA7, PB0, PB1, PB2, PB3, PB4, PB5, PB6, PB7, CB2
  _6522_layout_2 _6522_layout_2_1 (
    .R_W(_6502_layout_2_1_r_w), .RS0(BA[0]), .RS1(BA[1]), .RS2(BA[2]), .RS3(BA[3]), .CS1(and_7_out),
    .nCS2(nSELE), .\Φ2 (\_6502_layout_2_1_φ2 ), .nRESET(rs_ff_as_1_q), .nIRQ(_6520_layout_2_1_nirqb),
    .D0(D[0]), .D1(D[1]), .D2(D[2]), .D3(D[3]), .D4(D[4]), .D5(D[5]), .D6(D[6]), .D7(D[7]), .CA1(1'b1),
    .PB3(CASS_WRITE), .PB4(_6522_layout_2_1_pb4), .PB5(SYNC), .CB1(_1_CASS_READ));  // open: CA2, PA0, PA1, PA2, PA3, PA4, PA5, PA6, PA7, PB0, PB1, PB2, PB6, PB7, CB2
  _6520_layout_2 _6520_layout_2_2 (
    .nIRQB(_6520_layout_2_1_nirqb), .nIRQA(_6520_layout_2_1_nirqb), .nRESET(rs_ff_as_1_q),
    .\Φ2 (\_6502_layout_2_1_φ2 ), .nCS2(nSELE), .CS1(BA[4]), .CS0(BA[11]), .RS1(BA[1]), .RS0(BA[0]),
    .R_W(_6502_layout_2_1_r_w), .D0(D[0]), .D1(D[1]), .D2(D[2]), .D3(D[3]), .D4(D[4]), .D5(D[5]), .D6(D[6]),
    .D7(D[7]), .CA1(_1_CASS_READ), .CA2(BLANK_TV), .PA0(_6520_layout_2_2_pa0), .PA1(_6520_layout_2_2_pa1),
    .PA2(_6520_layout_2_2_pa2), .PA3(_6520_layout_2_2_pa3), .PA4(_1_CASS_SWITCH), .PA5(_2_CASS_SWITCH),
    .PA6(_6520_layout_2_2_pa6), .PA7(DIAG), .PB0(_6520_layout_2_2_pb7[0]), .PB1(_6520_layout_2_2_pb7[1]),
    .PB2(_6520_layout_2_2_pb7[2]), .PB3(_6520_layout_2_2_pb7[3]), .PB4(_6520_layout_2_2_pb7[4]),
    .PB5(_6520_layout_2_2_pb7[5]), .PB6(_6520_layout_2_2_pb7[6]), .PB7(_6520_layout_2_2_pb7[7]), .CB1(SYNC),
    .CB2(_6520_layout_2_2_cb2));
  _74LS107 _74ls107_8 (
    .J(_74ls107_7_q), .nCLK(_74ls107_6_q), .K(_74ls107_7_nq), .Q(_74ls107_8_q), .nQ(_74ls107_8_nq),
    .nCLR(1'b1));
  _74LS107_CLR_TOP _74ls107_clr_top_1 (
    .J(1'b1), .nCLK(_74ls107_3_q), .K(1'b1), .Q(_74ls107_clr_top_1_q), .nCLR(DIS_ON));  // open: nQ
  _74LS107_CLR_TOP _74ls107_clr_top_2 (
    .J(1'b1), .nCLK(_74ls107_clr_top_1_q), .K(1'b1), .Q(_74ls107_clr_top_2_q), .nCLR(DIS_ON));  // open: nQ
  _74177_layout_2 _74177_layout_2_1 (
    .CLK1(_74ls107_clr_top_2_q), .CLK2(_74177_layout_2_1_qa), .QA(_74177_layout_2_1_qa),
    .QB(_74177_layout_2_1_qb), .QC(_74177_layout_2_1_qc), .QD(_74177_layout_2_1_qd), .nLD(DIS_ON),
    .nCLR(_74ls107_6_nq), .A(_74100_1_q1), .B(_74100_1_q2), .C(_74100_1_q3), .D(_74100_1_q4));
  _74177_layout_2 _74177_layout_2_2 (
    .CLK1(_74177_layout_2_1_qd), .CLK2(_74177_layout_2_2_qa), .QA(_74177_layout_2_2_qa),
    .QB(_74177_layout_2_2_qb), .QC(_74177_layout_2_2_qc), .QD(_74177_layout_2_2_qd), .nLD(DIS_ON),
    .nCLR(_74ls107_6_nq), .A(_74100_1_q5), .B(_74100_1_q6), .C(_74100_1_q7), .D(_74100_1_q8));
  nand nand_5 (nand_5_out, _74100_1_q5, _74100_1_q6, _74100_1_q7, _74100_1_q8);
  nand nand_6 (VERT_DRIVE, _74ls107_7_nq, _74ls107_8_nq);
  and and_9 (SYNC, _74ls107_7_q, _74ls107_8_q);
  not not_8 (not_8_out, SYNC);
  nand nand_7 (nand_7_out, 1'b1, _74ls93_3_qd, not_8_out, _74177_layout_2_2_qa);
  or or_2 (or_2_out, ~nand_7_out, ~nand_4_out);  // Or
  _74LS93 _74ls93_3 (
    .CKA(1'b1), .CKB(DIS_ON), .R1(_74ls107_6_q), .R2(1'b1), .QB(_74ls93_3_qb), .QC(_74ls93_3_qc),
    .QD(_74ls93_3_qd));  // open: QA
  _74LS157 _74ls157_1 (
    ._1A(1'b1), ._1B(1'b1), ._2A(1'b1), ._2B(r_w), ._3A(_74ls107_clr_top_1_q), ._3B(BA[0]),
    ._4A(_74ls107_clr_top_2_q), ._4B(BA[1]), .S(SEL8), .G(1'b0), .Y2(_74ls157_1_y2), .Y3(_74ls157_1_y3[0]),
    .Y4(_74ls157_1_y3[1]));  // open: Y1
  _74LS157 _74ls157_2 (
    ._1A(_74177_layout_2_1_qa), ._1B(BA[2]), ._2A(_74177_layout_2_1_qb), ._2B(BA[3]),
    ._3A(_74177_layout_2_1_qc), ._3B(BA[4]), ._4A(_74177_layout_2_1_qd), ._4B(BA[5]), .S(SEL8), .G(1'b0),
    .Y1(_74ls157_2_y1[0]), .Y2(_74ls157_2_y1[1]), .Y3(_74ls157_2_y1[2]), .Y4(_74ls157_2_y1[3]));
  _74LS157 _74ls157_3 (
    ._1A(_74177_layout_2_2_qa), ._1B(BA[6]), ._2A(_74177_layout_2_2_qb), ._2B(BA[7]),
    ._3A(_74177_layout_2_2_qc), ._3B(BA[8]), ._4A(_74177_layout_2_2_qd), ._4B(BA[9]), .S(SEL8), .G(1'b0),
    .Y1(_74ls157_3_y1[0]), .Y2(_74ls157_3_y1[1]), .Y3(_74ls157_3_y1[2]), .Y4(_74ls157_3_y1[3]));
  not not_9 (not_9_out, _6520_layout_2_2_pa2);
  not not_10 (_2_CASS_MOTOR, _6522_layout_2_1_pb4);
  not not_11 (_1_CASS_MOTOR, _6520_layout_2_2_cb2);
  nand nand_8 (nand_8_out, _6520_layout_2_2_pa0, _6520_layout_2_2_pa1, _6520_layout_2_2_pa3, not_9_out);
  nand nand_9 (nand_9_out, _74ls93_3_qd, _74ls93_3_qc, _74ls93_3_qb, DIS_ON);
  _74LS145 _74ls145_1 (
    .A(_6520_layout_2_2_pa0), .B(_6520_layout_2_2_pa1), .C(_6520_layout_2_2_pa2), .D(_6520_layout_2_2_pa3),
    ._0(_74ls145_1__0), ._1(_74ls145_1__1), ._2(_74ls145_1__2), ._3(_74ls145_1__3), ._4(_74ls145_1__4),
    ._5(_74ls145_1__5), ._6(_74ls145_1__6), ._7(_74ls145_1__7), ._8(_74ls145_1__8), ._9(_74ls145_1__9));
  _74LS165_layout_2 _74ls165_layout_2_1 (
    .SH_nLD(_74ls107_3_nq), .CLKINH(1'b0), .SER(1'b0), .CLK(and_1_out), .QH(_74ls165_layout_2_1_qh),
    .nQH(_74ls165_layout_2_1_nqh), .A(_6540_character_rom_1_d0), .B(_6540_character_rom_1_d1),
    .C(_6540_character_rom_1_d2), .D(_6540_character_rom_1_d3), .E(_6540_character_rom_1_d4),
    .F(_6540_character_rom_1_d5), .G(_6540_character_rom_1_d6), .H(_6540_character_rom_1_d7));
  _6540_Character_ROM _6540_character_rom_1 (
    .A0(_74ls93_3_qb), .A1(_74ls93_3_qc), .A2(_74ls93_3_qd), .CS1(1'b1), .CS2(1'b1), .nCS3(1'b0),
    .nCS4(1'b0), .nCS5(1'b0), .\Φ2 (_74ls107_1_q), .D0(_6540_character_rom_1_d0),
    .D1(_6540_character_rom_1_d1), .D2(_6540_character_rom_1_d2), .D3(_6540_character_rom_1_d3),
    .D4(_6540_character_rom_1_d4), .D5(_6540_character_rom_1_d5), .D6(_6540_character_rom_1_d6),
    .D7(_6540_character_rom_1_d7), .A10(GRAPHIC), .A9(SD6), .A8(SD5), .A7(SD4), .A6(SD3), .A5(SD2), .A4(SD1),
    .A3(SD0));
  LED led_1 (.in(nand_8_out));
  PETKeyboard petkeyboard_1 (
    .R0(_74ls145_1__0), .R1(_74ls145_1__1), .R2(_74ls145_1__2), .R3(_74ls145_1__3), .R4(_74ls145_1__4),
    .R5(_74ls145_1__5), .R6(_74ls145_1__6), .R7(_74ls145_1__7), .R8(_74ls145_1__8), .R9(_74ls145_1__9),
    .B0(_6520_layout_2_2_pb7[0]), .B1(_6520_layout_2_2_pb7[1]), .B2(_6520_layout_2_2_pb7[2]),
    .B3(_6520_layout_2_2_pb7[3]), .B4(_6520_layout_2_2_pb7[4]), .B5(_6520_layout_2_2_pb7[5]),
    .B6(_6520_layout_2_2_pb7[6]), .B7(_6520_layout_2_2_pb7[7]), .CLK(SYNC));
  _6550_layout_1 _6550_layout_1_1 (
    .R_nW(_74ls157_1_y2), .A0(_74ls157_1_y3[0]), .A1(_74ls157_1_y3[1]), .A2(_74ls157_2_y1[0]),
    .A3(_74ls157_2_y1[1]), .A4(_74ls157_2_y1[2]), .A5(_74ls157_2_y1[3]), .A6(_74ls157_3_y1[0]),
    .A7(_74ls157_3_y1[1]), .A8(_74ls157_3_y1[2]), .A9(_74ls157_3_y1[3]), .D0(SD0), .D1(SD1), .D2(SD2),
    .D3(SD3), .CS1(1'b1), .CS2(1'b1), .nCS3(1'b0), .nCS4(1'b0), .\Φ2 (\BΦ2 ));
  _74S74 _74s74_1 (.Q(_74s74_1_q), .nP(1'b1), .D(SD7), .CK(_74ls107_1_q), .nCL(1'b1));  // open: nQ
  _74S74 _74s74_2 (.Q(_74s74_2_q), .nQ(_74s74_2_nq), .nP(1'b1), .D(_74s74_1_q), .CK(_74ls107_3_q), .nCL(1'b1));
  _6550_layout_1 _6550_layout_1_2 (
    .R_nW(_74ls157_1_y2), .A0(_74ls157_1_y3[0]), .A1(_74ls157_1_y3[1]), .A2(_74ls157_2_y1[0]),
    .A3(_74ls157_2_y1[1]), .A4(_74ls157_2_y1[2]), .A5(_74ls157_2_y1[3]), .A6(_74ls157_3_y1[0]),
    .A7(_74ls157_3_y1[1]), .A8(_74ls157_3_y1[2]), .A9(_74ls157_3_y1[3]), .D0(SD4), .D1(SD5), .D2(SD6),
    .D3(SD7), .CS1(1'b1), .CS2(1'b1), .nCS3(1'b0), .nCS4(1'b0), .\Φ2 (\BΦ2 ));
  DipSwitch #(.dipDefault("true")) dipswitch_1 (.out(_2_CASS_SWITCH));
  DipSwitch #(.dipDefault("true")) dipswitch_2 (.out(_1_CASS_SWITCH));
  nand nand_10 (nand_10_out, _74ls165_layout_2_1_qh, _74s74_2_q);
  nand nand_11 (nand_11_out, _74ls165_layout_2_1_nqh, _74s74_2_nq);
  PullDown pulldown_1 (.out(_1_CASS_READ));
  or or_3 (or_3_out, ~nand_10_out, ~nand_11_out);  // Or
  nand nand_12 (TV_VIDEO_DRIVE, DIS_ON, or_3_out, SYNC, BLANK_TV);
  nand nand_13 (nand_13_out, SEL8, r_w);
  _74LS244 _74ls244_3 (
    ._1Y1(BD0), ._2A1(BD0), ._1Y2(BD1), ._2A2(BD1), ._1Y3(BD2), ._2A3(BD2), ._1Y4(BD3), ._2A4(BD3),
    ._1nG(_74ls157_1_y2), ._1A1(SD0), ._2Y1(SD0), ._1A2(SD1), ._2Y2(SD1), ._1A3(SD2), ._2Y3(SD2), ._1A4(SD3),
    ._2Y4(SD3), ._2nG(nand_13_out));
  _74LS244 _74ls244_4 (
    ._1Y1(BD4), ._2A1(BD4), ._1Y2(BD5), ._2A2(BD5), ._1Y3(BD6), ._2A3(BD6), ._1Y4(BD7), ._2A4(BD7),
    ._1nG(_74ls157_1_y2), ._1A1(SD4), ._2Y1(SD4), ._1A2(SD5), ._2Y2(SD5), ._1A3(SD6), ._2Y3(SD6), ._1A4(SD7),
    ._2Y4(SD7), ._2nG(nand_13_out));
  CRT_white crt_white_1 (.VIDEO(TV_VIDEO_DRIVE), .CLK8(_8MHz), .HOR_DRIVE_IN(HORZ_DRIVE), .VER_DRIVE_IN(VERT_DRIVE));
  // also tied to VCC on the sheet: DIAG

  // Other names for the same wires on the sheet: _2_CASS_READ = _1_CASS_READ; RW_nE = r_w; VIDEO_ON = SYNC

  // Notes on the sheet:
  //   _8MHz: Hz: 2147483647
  //   1 - Computer Main Logic
  //   3 - Main Logic / Video Logic
  //   DEBUG
  //   Breakpoint
  //   Set to 0 to start in DIAG mode
  //   2 - Memory Section
endmodule
