// Digital circuit PETKeyboard.dig as structural Verilog
module PETKeyboard (
  input  R1,
  input  R2,
  input  R3,
  input  R4,
  input  R5,
  input  R6,
  input  R7,
  input  R8,
  input  R9,
  input  R0,
  input  CLK,
  output B0,
  output B1,
  output B2,
  output B3,
  output B4,
  output B5,
  output B6,
  output B7
);

  wire keyboard_1_av, keyboard_1_d;

  Keyboard keyboard_1 (.C(CLK), .en(1'b1), .D(keyboard_1_d), .av(keyboard_1_av));
  // PETKeyboard petkeyboard_1: pin names not known; wires that end beside it: keyboard_1_d, keyboard_1_av, {R9, R8, R7, R6, R5, R4, R3, R2, R1, R0}, CLK, {B7, B6, B5, B4, B3, B2, B1, B0}
endmodule
