// Digital circuit 6502_test.dig as structural Verilog
module _6502_test (
  input  _1MHz,
  output SYNC,
  output CLK,
  output PHI2,
  output PHI1,
  output [7:0] DATA,
  output [15:0] ADDR,
  output R_nW
);

  wire counter_1_ovf, not_1_out, not_2_out, rs_ff_as_1_q;

  Counter #(.Bits(2)) counter_1 (.en(1'b1), .C(_1MHz), .clr(rs_ff_as_1_q), .ovf(counter_1_ovf));  // open: out
  RS_FF_AS rs_ff_as_1 (.S(counter_1_ovf), .R(1'b0), .Q(rs_ff_as_1_q));  // open: nQ
  // MOS6502 mos6502_1: pin names not known; wires that end beside it: 1'b1, rs_ff_as_1_q, 1'b1, 1'b1, _1MHz, DATA, ADDR, R_nW, SYNC, PHI1, PHI2
  not not_1 (not_1_out, ADDR[15]);
  not not_2 (not_2_out, R_nW);
  ROM #(.AddrBits(12), .Bits(8)) rom_1 (.A(ADDR[11:0]), .sel(ADDR[15]), .D(DATA));
  RAMSinglePortSel #(.AddrBits(12), .Bits(8)) ramsingleportsel_1 (
    .A(ADDR[11:0]), .CS(not_1_out), .WE(not_2_out), .OE(R_nW), .D(DATA));

  assign CLK = _1MHz;

  // Notes on the sheet:
  //   _1MHz: Hz: 10
  //   contents of rom_1 (hex, n*v repeats v):
  //   54,4f,4f,20,4d,41,4e,59,20,46,49,4c,45,d3,46,49,4c,45,20,4f,50
  //   ,45,ce,46,49,4c,45,20,4e,4f,54,20,4f,50,45,ce,46,49,4c,45,20,4e
  //   ,4f,54,20,46,4f,55,4e,c4,d,53,45,41,52,43,48,49,4e,47,a0,46,4f
  //   ,52,a0,d,50,52,45,53,53,20,50,4c,41,59,a0,26,20,52,45,43,4f,52
  //   ,44,a0,4f,4e,20,54,41,50,45,20,a3,d,4c,4f,41,c4,d,57,52,49,54
  //   ,49,4e,47,a0,d,56,45,52,49,46,d9,44,45,56,49,43,45,20,4e,4f,54
  //   ,20,50,52,45,53,45,4e,d4,4e,4f,54,20,49,4e,50,55,54,20,46,49,4c
  //   ,c5,4e,4f,54,20,4f,55,54,50,55,54,20,46,49,4c,c5,d,46,4f,55,4e
  //   ,44,a0,d,4f,4b,8d,d,52,45,41,44,59,2e,8d,d,41,52,45,20,59,4f,55
  //   ,20,53,55,52,45,20,bf,d,3f,20,42,41,44,20,44,49,53,4b,20,8d,a9
  //   ,40,2c,a9,20,48,ad,40,e8,9,2,8d,40,e8,a9,3c,8d,21,e8,24,a0,f0
  //   ,11,a9,34,8d,11,e8,20,9,f1,a9,0,85,a0,a9,3c,8d,11,e8,68,5,d4,85
  //   ,a5,ad,40,e8,10,fb,29,fb,8d,40,e8,a9,3c,8d,23,e8,ad,40,e8,29,41
  //   ,c9,41,f0,55,a5,a5,49,ff,8d,22,e8,2c,40,e8,50,fb,a9,34,8d,23,e8
  //   ,a9,ff,8d,45,e8,ad,40,e8,2c,4d,e8,70,1c,4a,90,f5,a9,3c,8d,23,e8
  //   ,a9,ff,8d,22,e8,60,85,a5,20,9,f1,ad,40,e8,9,4,8d,40,e8,60,ad,fc
  //   ,3,10,f,20,43,f3,d0,cd,ad,fc,3,10,10,20,43,f3,d0,68,a9,1,20,c4
  //   ,fb,d0,cc,a9,80,30,f7,a9,2,20,c4,fb,ad,40,e8,29,fd,8d,40,e8,a9
  //   ,34,8d,21,e8,a9,d,60,b9,0,f0,8,29,7f,20,2,e2,c8,28,10,f3,60,85
  //   ,a5,20,9,f1,20,75,f1,4c,48,f1,24,a0,30,4,c6,a0,d0,5,48,20,9,f1
  //   ,68,85,a5,60,ad,40,e8,29,fb,8d,40,e8,a9,5f,2c,a9,3f,20,d7,f0,d0
  //   ,88,a9,34,8d,21,e8,ad,40,e8,9,2,8d,40,e8,a9,ff,8d,45,e8,2c,4d
  //   ,e8,70,84,2c,40,e8,30,f6,ad,40,e8,29,fd,8d,40,e8,2c,10,e8,70,5
  //   ,a9,40,20,c4,fb,ad,20,e8,49,ff,48,a9,3c,8d,21,e8,2c,40,e8,10,fb
  //   ,a9,34,8d,21,e8,68,60,a9,0,85,96,a5,af,d0,17,a5,9e,f0,51,78,4c
  //   ,a7,e0,a5,af,d0,b,a5,c6,85,a4,a5,d8,85,a3,4c,16,e1,c9,3,d0,9,85
  //   ,ac,a5,d5,85,a1,4c,16,e1,b0,29,86,ad,20,49,f2,48,20,49,f2,d0,5
  //   ,a9,40,20,c4,fb,d6,ba,a6,ad,68,60,20,4b,f8,d0,b,20,9a,f8,a6,d4
  //   ,a9,0,95,ba,f0,f0,b1,d6,60,a5,96,f0,3,a9,d,60,4c,c0,f1,48,a5,b0
  //   ,c9,3,d0,4,68,4c,2,e2,30,4,68,4c,9e,f1,68,85,b4,c9,a,f0,e4,48
  //   ,8a,48,98,48,20,4b,f8,d0,10,20,cb,f8,a6,d4,a9,1,95,ba,a0,0,a9
  //   ,2,91,d6,c8,a5,b4,91,d6,68,a8,68,aa,68,60,a9,0,85,ae,a5,b0,c9
  //   ,4,90,3,20,b9,f1,a5,af,c9,4,90,3,20,ae,f1,a9,3,85,b0,a9,0,85,af
  //   ,60,a6,ae,ca,30,16,dd,51,2,f0,11,d0,f6,bd,51,2,85,d2,bd,5b,2,85
  //   ,d4,bd,65,2,85,d3,60,20,d,f5,a5,d2,20,c1,f2,d0,4d,20,cd,f2,8a
  //   ,48,a5,d4,f0,28,c9,3,f0,24,b0,1f,a5,d3,29,f,f0,1c,20,95,f6,a9
  //   ,0,20,78,f2,20,cb,f8,a5,d3,c9,62,d0,b,a9,5,20,19,f6,4c,18,f3,20
  //   ,2f,f7,68,aa,c6,ae,e4,ae,f0,14,a4,ae,b9,51,2,9d,51,2,b9,5b,2,9d
  //   ,5b,2,b9,65,2,9d,65,2,60,a5,9b,c9,ef,d0,7,8,20,a6,f2,85,9e,28
  //   ,60,20,35,f3,4c,c6,b7,20,51,f3,d0,f4,4c,85,f1,a5,78,c9,2,60,a5
  //   ,d4,d0,3,4c,0,bf,c9,3,f0,f9,90,71,a9,60,85,d3,a4,d1,d0,3,4c,0
  //   ,bf,20,49,f4,20,a5,f4,20,d2,f0,a5,d3,20,93,f1,20,c0,f1,85,fb,a5
  //   ,96,4a,4a,b0,3a,20,c0,f1,85,fc,20,6d,f4,a9,fd,25,96,85,96,20,43
  //   ,f3,20,c0,f1,aa,a5,96,4a,4a,b0,ed,8a,a4,9d,f0,c,88,d1,fb,f0,9
  //   ,a9,10,5,96,85,96,2c,91,fb,e6,fb,d0,2,e6,fc,24,96,70,7,50,ce,a0
  //   ,24,4c,af,f5,a5,fb,85,c9,a5,fc,85,ca,20,ae,f1,4c,2f,f7,20,95,f6
  //   ,20,57,f8,20,49,f4,a5,d1,f0,8,20,d3,f4,d0,8,4c,ad,f5,20,e5,f5
  //   ,f0,f8,e0,1,d0,eb,a5,96,29,10,d0,74,20,7b,f6,20,6d,f4,4c,a3,f8
  //   ,a9,0,85,9d,20,7d,f4,20,cc,f6,a9,ff,c5,9b,d0,fc,c5,9b,d0,f8,20
  //   ,56,f3,a5,9d,d0,50,20,2b,f9,a5,96,29,10,f0,9,a0,0,84,9e,a0,60
  //   ,4c,af,f5,a0,ae,20,49,f3,20,51,f3,d0,b,a5,ca,85,2b,a5,c9,85,2a
  //   ,4c,ad,b4,20,22,b6,4c,b,b6,20,51,f3,d0,1e,a0,32,20,85,f1,a5,d1
  //   ,f0,15,a0,3d,20,85,f1,a4,d1,f0,c,a0,0,b1,da,20,66,f2,c8,c4,d1
  //   ,d0,f6,60,a0,5f,a5,9d,f0,2,a0,6d,20,49,f3,a0,39,4c,49,f3,a2,0
  //   ,86,96,86,d1,86,d3,e8,86,d4,20,4d,f5,20,3c,f5,20,4d,f5,20,9f,f4
  //   ,86,d4,20,4d,f5,20,9f,f4,86,d3,60,20,55,f5,4c,d4,c8,a5,d3,30,f5
  //   ,a4,d1,f0,f1,20,d5,f0,a5,d3,9,f0,20,43,f1,a5,96,10,5,a0,74,4c
  //   ,af,f5,a5,d1,f0,c,a0,0,b1,da,20,9e,f1,c8,c4,d1,d0,f6,4c,b9,f1
  //   ,20,e5,f5,f0,1d,a0,5,84,b5,a0,0,84,b4,c4,d1,f0,10,b1,da,a4,b5
  //   ,d1,d6,d0,e7,e6,b4,e6,b5,a4,b4,d0,ec,98,60,a9,1,85,9d,20,5,f4
  //   ,a5,96,29,10,f0,5,a0,6e,4c,af,f5,a0,aa,4c,85,f1,a2,0,86,d3,86
  //   ,96,86,d1,e8,86,d4,20,58,f5,20,d4,c8,86,d2,20,4d,f5,20,9f,f4,86
  //   ,d4,e0,3,90,2,c6,d3,20,4d,f5,20,9f,f4,86,d3,20,4d,f5,20,55,f5
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endmodule
