// Digital circuit Clock1_strobe.dig as structural Verilog
module Clock1_strobe (
  input  CLK1,
  input  CLK8,
  output rising
);

  wire d_ff_1_q, xor_1_out;

  D_FF d_ff_1 (.D(CLK1), .C(CLK8), .Q(d_ff_1_q));  // open: nQ
  xor xor_1 (xor_1_out, CLK1, d_ff_1_q);
  and and_1 (rising, CLK1, xor_1_out);

  // Notes on the sheet:
  //   CLK8: Hz: 8
endmodule
