// Digital circuit keyboard_test.dig as structural Verilog
module keyboard_test (
  input  clk
);

  wire keyboard_1_av, keyboard_1_d;

  Keyboard keyboard_1 (.C(clk), .en(1'b1), .D(keyboard_1_d), .av(keyboard_1_av));
  // Probe on keyboard_1_d
endmodule
